// Logisim project cpu24.circ as structural Verilog: 21 circuits, main circuit ◇单周期MIPS
module \单周期MIPS  (
  input  IR1,
  input  IR2,
  input  IR3,
  output RegWrite,
  output MemWrite,
  output [31:0] PC,
  output [31:0] IR,
  output [31:0] RDin,
  output [31:0] MDin,
  output [31:0] LedData,
  output [5:0] out_11,
  output [5:0] out_12,
  output [4:0] out_13,
  output [4:0] out_14,
  output [4:0] out_15,
  output [15:0] out_16,
  output [25:0] out_17,
  output [4:0] out_18
);

  wire AluSrc, and_1_out, and_2_out, and_3_out, and_4_out, and_5_out, and_6_out, BEQ, BGTZ, BNE, CLK,
       clock_2_out, comparator_1_eq, comparator_1_lt, comparator_2_gt, comparator_3_eq, d_ff_1_q, DIVU,
       Equal, Go, Halt, IR1_t, IR2_t, IR3_t, IRA, IRB, IRC, JAL, JMP, JMP_IF, JR, LBU, MemToReg, MFLO,
       nand_1_out, not_1_out, not_2_out, not_3_out, not_4_out, or_4_out, RegDst, SignedExt, SysCall, W1, W2,
       W3, \单周期硬布线控制器_1_p6 ;
  wire [3:0] AluOp;
  wire [4:0] multiplexer_3_out, multiplexer_4_out, multiplexer_5_out, multiplexer_6_out;
  wire [7:0] multiplexer_11_out, ram_1_data_2, ram_1_data_3;
  wire [12:0] CNT_num;
  wire [15:0] ram_1_data, \总周期数 ;
  wire [27:0] PC_4;
  wire [31:0] bit_extender_1_out, bit_extender_2_out, bit_extender_3_out, HI, IMME32, LO, multiplexer_1_out,
       multiplexer_8_out, multiplexer_10_out, multiplexer_12_out, multiplexer_13_out, PC_4_IMME, PC_JR,
       PC_Next, Res1, Res2, shifter_1_out;
  wire [31:28] JmpPc;

  Clock #(.highDuration(1), .lowDuration(1)) clock_1 ();  // open: out
  Button _1 (.out(IRA));
  Button _2 (.out(IRB));
  Button _3 (.out(IRC));
  Button \u_继续运行  (.out(Go));
  LED #(.active("true")) led_1 (.in(W1));
  LED #(.active("true")) led_2 (.in(W2));
  LED #(.active("true")) led_3 (.in(W3));
  Hex_Digit_Display hex_digit_display_1 (.value(LedData[31:28]));  // open: dp
  not not_1 (not_1_out, Halt);
  Hex_Digit_Display hex_digit_display_2 (.value(LedData[27:24]));  // open: dp
  Hex_Digit_Display hex_digit_display_3 (.value(LedData[23:20]));  // open: dp
  and and_1 (and_1_out, BEQ, Equal);
  and and_2 (and_2_out, BNE, not_2_out);
  not not_2 (not_2_out, Equal);
  Register #(.width(32), .trigger("rising"), .Select("low")) u_PC (
    .D(PC_Next), .en(not_1_out), .Q(PC), .clk(CLK));  // open: clr
  D_Flip_Flop #(.trigger("high"), .Pre_Clr_Positions("LEGACY"), .NegatePresetClear("false"), .enable("true"), .NewFFLayout("false")) d_ff_1 (.Q(d_ff_1_q));  // open: clk, D, Qn, preset, en, reset
  // Probe on 13'ha0
  Hex_Digit_Display hex_digit_display_4 (.value(LedData[15:12]));  // open: dp
  Hex_Digit_Display hex_digit_display_5 (.value(LedData[19:16]));  // open: dp
  Comparator #(.width(13), .mode("twosComplement")) comparator_1 (
    .a(CNT_num), .b(13'ha0), .eq(comparator_1_eq), .lt(comparator_1_lt));  // open: gt
  Clock #(.highDuration(1), .lowDuration(1)) clock_2 (.out(clock_2_out));
  Hex_Digit_Display hex_digit_display_6 (.value(LedData[11:8]));  // open: dp
  Hex_Digit_Display hex_digit_display_7 (.value(LedData[7:4]));  // open: dp
  // Probe on \总周期数 
  or or_1 (JMP_IF, and_1_out, and_2_out);
  Multiplexer #(.select(3), .width(32), .disabled("Z"), .enable("false")) multiplexer_1 (
    .in0({JmpPc, PC_4}), .in1(PC_4_IMME), .in2({JmpPc, IR[25:0], 2'b00}), .in6(PC_JR),
    .out(multiplexer_1_out), .sel({JR, JMP, JMP_IF}));  // open: in3, in4, in5, in7
  nand nand_1 (nand_1_out, d_ff_1_q, comparator_1_eq);
  Counter #(.width(13), .max('h1fff), .ongoal("stay"), .trigger("rising"), .behavior("old")) counter_1 (
    .count(comparator_1_lt), .Q(CNT_num), .clk(clock_2_out));  // open: load, D, carry, clr, preset
  Hex_Digit_Display hex_digit_display_8 (.value(LedData[3:0]));  // open: dp
  Comparator #(.width(32), .mode("twosComplement")) comparator_2 (
    .a(PC_JR), .b({32{1'b0}}), .gt(comparator_2_gt));  // open: eq, lt
  // Mips_Probe mips_probe_1: pin names not known; wires that end beside it: IR, IR
  ROM #(.addrWidth(10), .dataWidth(32), .Select("high")) rom_1 (.addr(PC[11:2]), .data(IR));
  assign CLK = nand_1_out ? clock_2_out : 1'bz;  // Controlled_Buffer controlled_buffer_1
  and and_3 (and_3_out, comparator_2_gt, BGTZ);
  Multiplexer #(.select(1), .width(32), .disabled("Z"), .enable("false")) multiplexer_2 (
    .in0(multiplexer_1_out), .in1(PC_4_IMME), .out(PC_Next), .sel(and_3_out));
  Pull_Resistor #(.pull(1)) pull_resistor_1 (.node(CLK));
  or or_2 (IR1_t, IR1, IRA);
  or or_3 (IR2_t, IR2, IRB);
  Adder #(.width(32)) adder_1 (.a(PC), .b(32'h4), .out({JmpPc, PC_4}));  // open: cin, cout
  Adder #(.width(32)) adder_2 (.a({JmpPc, PC_4}), .b(shifter_1_out), .out(PC_4_IMME));  // open: cin, cout
  Shifter #(.width(32), .shift("ll")) shifter_1 (.in(IMME32), .\dist (5'b00010), .out(shifter_1_out));
  Multiplexer #(.select(1), .width(5), .disabled("Z"), .enable("false")) multiplexer_3 (
    .in0(IR[20:16]), .in1(IR[15:11]), .out(multiplexer_3_out), .sel(or_4_out));
  or or_4 (or_4_out, RegDst, MFLO);
  Multiplexer #(.select(1), .width(5), .disabled("Z"), .enable("false")) multiplexer_4 (
    .in0(IR[25:21]), .in1(5'b00010), .out(multiplexer_4_out), .sel(SysCall));
  Multiplexer #(.select(1), .width(5), .disabled("Z"), .enable("false")) multiplexer_5 (
    .in0(IR[20:16]), .in1(5'b00100), .out(multiplexer_5_out), .sel(SysCall));
  Multiplexer #(.select(1), .width(5), .disabled("Z"), .enable("false")) multiplexer_6 (
    .in0(multiplexer_3_out), .in1({5{1'b1}}), .out(multiplexer_6_out), .sel(JAL));
  or or_5 (IR3_t, IR3, IRC);
  // Probe on multiplexer_4_out
  // Probe on multiplexer_5_out
  // Probe on multiplexer_6_out
  Multiplexer #(.select(1), .width(32), .disabled("Z"), .enable("false")) multiplexer_7 (
    .in0(multiplexer_8_out), .in1(LO), .out(RDin), .sel(MFLO));
  Multiplexer #(.select(1), .width(32), .disabled("Z"), .enable("false")) multiplexer_8 (
    .in0(multiplexer_13_out), .in1({JmpPc, PC_4}), .out(multiplexer_8_out), .sel(JAL));
  MIPS_Regifile mips_regifile_1 (
    .Din(RDin), .Clk(CLK), .R1(PC_JR), .R2(MDin), .WE(RegWrite), .W_num(multiplexer_6_out),
    .R1_num(multiplexer_4_out), .R2_num(multiplexer_5_out));
  assign bit_extender_1_out = {{16{1'b0}}, IR[15:0]};  // Bit_Extender bit_extender_1
  assign bit_extender_2_out = {{16{IR[15]}}, IR[15:0]};  // Bit_Extender bit_extender_2
  // Probe on PC_JR
  // Probe on MDin
  Multiplexer #(.select(1), .width(32), .disabled("Z"), .enable("false")) multiplexer_9 (
    .in0(bit_extender_1_out), .in1(bit_extender_2_out), .out(IMME32), .sel(SignedExt));
  Multiplexer #(.select(1), .width(32), .disabled("Z"), .enable("false")) multiplexer_10 (
    .in0(MDin), .in1(IMME32), .out(multiplexer_10_out), .sel(AluSrc));
  // Probe on multiplexer_10_out
  // 单周期硬布线控制器 单周期硬布线控制器_1: pin names not known; wires that end beside it: JMP, JR, SignedExt, IR[31:26], IR[5:0], \单周期硬布线控制器_1_p6 , \单周期硬布线控制器_1_p6 , SysCall, BEQ, BNE, MemToReg, MemWrite, AluOp, AluSrc, RegWrite, JAL, RegDst, DIVU, MFLO, LBU, BGTZ
  MIPS_ALU mips_alu_1 (
    .X(PC_JR), .Y(multiplexer_10_out), .AluOP(AluOp), .Equal(Equal), .Result(Res1), .Result_2(Res2),
    .shamt(IR[10:6]));
  // Probe on Res1
  // Probe on LO
  Register #(.width(32), .trigger("rising"), .Select("low")) register_1 (
    .D(Res1), .en(DIVU), .Q(LO), .clk(CLK));  // open: clr
  // Probe on HI
  Register #(.width(32), .trigger("rising"), .Select("low")) register_2 (
    .D(Res2), .en(DIVU), .Q(HI), .clk(CLK));  // open: clr
  Comparator #(.width(32), .mode("twosComplement")) comparator_3 (
    .a(PC_JR), .b(32'ha), .eq(comparator_3_eq));  // open: gt, lt
  and and_4 (and_4_out, SysCall, comparator_3_eq);
  not not_3 (not_3_out, comparator_3_eq);
  and and_5 (and_5_out, not_3_out, SysCall);
  // Probe on MDin
  Counter #(.width(1), .max('h1), .ongoal("wrap"), .trigger("rising"), .behavior("old")) counter_2 (
    .load(and_4_out), .D(and_4_out), .count(1'b0), .Q(Halt), .clk(CLK), .clr(Go));  // open: carry, preset
  Counter #(.width(32), .max('hffffffff), .ongoal("wrap"), .trigger("rising"), .behavior("old")) counter_3 (
    .load(and_5_out), .D(MDin), .count(1'b0), .Q(LedData), .clk(CLK));  // open: carry, clr, preset
  RAM #(.addrWidth(10), .dataWidth(32), .bus("separate"), .Select("high")) ram_1 (
    .addr(Res1[11:2]), .din(MDin), .data({ram_1_data_3, ram_1_data_2, ram_1_data}), .str(MemWrite), .clk(CLK));  // open: sel, ld, clr
  Multiplexer #(.select(2), .width(8), .disabled("Z"), .enable("false")) multiplexer_11 (
    .in0(ram_1_data[7:0]), .in1(ram_1_data[15:8]), .in2(ram_1_data_2), .in3(ram_1_data_3),
    .out(multiplexer_11_out), .sel(Res1[1:0]));
  Counter #(.width(16), .max('hffff), .ongoal("wrap"), .trigger("rising"), .behavior("new")) counter_4 (
    .Q(\总周期数 ), .clk(and_6_out));  // open: load, D, count, carry, clr, preset, down
  and and_6 (and_6_out, CLK, not_4_out);
  not not_4 (not_4_out, Halt);
  assign bit_extender_3_out = {{24{1'b0}}, multiplexer_11_out};  // Bit_Extender bit_extender_3
  Multiplexer #(.select(1), .width(32), .disabled("Z"), .enable("false")) multiplexer_12 (
    .in0(Res1), .in1({ram_1_data_3, ram_1_data_2, ram_1_data}), .out(multiplexer_12_out), .sel(MemToReg));
  Multiplexer #(.select(1), .width(32), .disabled("Z"), .enable("false")) multiplexer_13 (
    .in0(multiplexer_12_out), .in1(bit_extender_3_out), .out(multiplexer_13_out), .sel(LBU));

  assign out_11 = IR[31:26];
  assign out_12 = IR[5:0];
  assign out_13 = IR[25:21];
  assign out_14 = IR[20:16];
  assign out_15 = IR[15:11];
  assign out_16 = IR[15:0];
  assign out_17 = IR[25:0];
  assign out_18 = IR[10:6];

  // Other names for the same wires on the sheet: OP[5:0] = IR[31:26]; ADDR[25:0] = IR[25:0]; FUNC[5:0] = IR[5:0];
  //   IMME[15:0] = IR[15:0]; JmpPc[27:2] = IR[25:0]; SHAMT[4:0] = IR[10:6]; RD[4:0] = IR[15:11]; RT[4:0] = IR[20:16];
  //   RS[4:0] = IR[25:21]; PC_4[31:28] = JmpPc; PCSrc[2:0] = {JR, JMP, JMP_IF}; R1[31:0] = PC_JR; R2[31:0] = MDin

  // Notes on the sheet:
  //   中断源
  //   中断等待指示
  //   总复位信号应将除ROM以外所有存储组件全部清零
  //   控制位
  //   暂停节拍，不能为0
  //   用这个时钟源需要去掉电路中的其他时钟源
  //   数码管输出
  //   戳工具置1进入计数暂停模式，ctrl+k时钟自动运行到对应节拍暂停
  //   ctrl+k关闭时钟连续运行，将控制位置零，进入单步调试模式调试
  //   数码管输出应该用寄存器锁存，否则显示数据只能一闪而过
  //   指令存储器
  //   指令字
  //   contents of rom_1 (hex, n*v repeats v):
  //   20090000 200b0020 34118483 20120401 118c00 129400 36318281 22520401 ad310000 2328820 21290004
  //   216bffff 1560fffb 20020022 200b0020 20090000 91310000 112020 20020022 c 21290004 216bffff 1560fff9
  //   2002000a c
  //   可计数暂停的时钟源
  //   为方便自动评测，需要输出PC，IR，寄存器堆写如数据RDin
  //   RAM写使能MemWrite、RAM写入数据MDin等信号
  //   JMP
  //   JR
endmodule

// 单周期硬布线控制器
module \单周期硬布线控制器  (
  input  [5:0] OP,
  input  [5:0] Func,
  output [3:0] ALU_OP,
  output MemToReg,
  output MemWrite,
  output ALU_SRC,
  output RegWrite,
  output SysCALL,
  output SignedExt,
  output RegDst,
  output Beq,
  output Bne,
  output JR,
  output JMP,
  output JAL,
  output DIVU,
  output MFLO,
  output LBU,
  output BGTZ,
  output R1_Used,
  output R2_Used
);

  \运算控制器自动生成  \u_运算控制器自动生成_1  (
    .OP0(OP[0]), .OP1(OP[1]), .OP2(OP[2]), .OP3(OP[3]), .OP4(OP[4]), .OP5(OP[5]), .F0(Func[0]), .F1(Func[1]),
    .F2(Func[2]), .F3(Func[3]), .F4(Func[4]), .F5(Func[5]), .S0(ALU_OP[0]), .S1(ALU_OP[1]), .S2(ALU_OP[2]),
    .S3(ALU_OP[3]));
  \控制信号自动生成  \u_控制信号自动生成_1  (
    .OP0(OP[0]), .OP1(OP[1]), .OP2(OP[2]), .MemToReg(MemToReg), .OP3(OP[3]), .OP4(OP[4]), .OP5(OP[5]),
    .MemWrite(MemWrite), .F0(Func[0]), .F1(Func[1]), .F2(Func[2]), .F3(Func[3]), .F4(Func[4]), .F5(Func[5]),
    .ALU_SRC(ALU_SRC), .RegWrite(RegWrite), .SysCALL(SysCALL), .SignedExt(SignedExt), .RegDst(RegDst),
    .BEQ(Beq), .BNE(Bne), .JR(JR), .JUMP(JMP), .JAL(JAL), .DIVU(DIVU), .MFLO(MFLO), .LBU(LBU), .BGTZ(BGTZ),
    .R1_Used(R1_Used), .R2_Used(R2_Used));

  // Other names for the same wires on the sheet: OP_CODE[5:0] = OP

  // Notes on the sheet:
  //   控制信号生成，产生数据通路需要的其他控制信号
  //   运算器控制器，根据指令生成运算器功能选择信号
endmodule

// 运算器控制器
module \运算控制器自动生成  (
  input  OP0,
  input  OP1,
  input  OP2,
  input  OP3,
  input  OP4,
  input  OP5,
  input  F0,
  input  F1,
  input  F2,
  input  F3,
  input  F4,
  input  F5,
  output S0,
  output S1,
  output S2,
  output S3
);

  wire and_1_out, and_2_out, and_3_out, and_4_out, and_5_out, and_6_out, and_7_out, and_8_out, and_9_out,
       and_10_out, and_11_out, and_12_out, and_13_out, and_14_out, and_15_out, and_16_out, and_17_out,
       and_18_out, and_19_out, and_20_out, and_21_out, and_22_out, and_23_out, and_24_out, and_25_out,
       and_26_out, and_27_out, and_28_out, and_29_out, and_30_out, and_31_out, and_32_out, and_33_out,
       and_34_out, and_35_out, and_36_out, and_37_out, not_1_out, not_2_out, not_3_out, not_4_out, not_5_out,
       not_6_out, not_7_out, not_8_out, not_9_out, not_10_out, not_11_out, not_12_out, not_13_out,
       not_14_out, not_15_out, not_16_out, not_17_out, not_18_out, not_19_out, not_20_out, not_21_out,
       not_22_out, not_23_out, not_24_out, not_25_out, not_26_out, not_27_out, not_28_out, not_29_out,
       not_30_out, not_31_out, not_32_out, not_33_out, not_34_out, not_35_out, not_36_out, not_37_out,
       not_38_out, not_39_out, not_40_out, not_41_out, not_42_out, not_43_out, not_44_out, not_45_out,
       not_46_out, not_47_out, not_48_out, not_49_out, not_50_out, not_51_out, not_52_out, not_53_out,
       not_54_out, not_55_out, not_56_out, not_57_out, not_58_out, not_59_out, not_60_out, not_61_out,
       not_62_out, not_63_out, not_64_out, not_65_out, not_66_out, not_67_out, not_68_out, not_69_out,
       not_70_out, not_71_out, not_72_out, not_73_out, not_74_out, not_75_out, not_76_out, not_77_out,
       not_78_out, not_79_out, not_80_out, not_81_out, not_82_out, not_83_out, not_84_out, not_85_out,
       not_86_out, not_87_out, not_88_out, not_89_out, not_90_out, not_91_out, not_92_out, not_93_out,
       not_94_out, not_95_out, not_96_out, not_97_out, not_98_out, not_99_out, not_100_out, not_101_out,
       not_102_out, not_103_out, not_104_out, not_105_out, not_106_out, not_107_out, not_108_out,
       not_109_out, not_110_out, not_111_out, not_112_out, not_113_out, not_114_out, not_115_out,
       not_116_out, not_117_out, not_118_out, not_119_out, not_120_out, not_121_out, not_122_out,
       not_123_out, not_124_out, not_125_out, not_126_out, not_127_out, not_128_out, not_129_out,
       not_130_out, not_131_out, not_132_out, not_133_out, not_134_out, not_135_out, not_136_out,
       not_137_out, not_138_out, not_139_out, not_140_out, not_141_out, not_142_out, not_143_out,
       not_144_out, not_145_out, not_146_out, not_147_out, not_148_out, not_149_out, not_150_out,
       not_151_out, not_152_out, not_153_out, not_154_out, not_155_out, not_156_out, not_157_out,
       not_158_out, not_159_out, not_160_out, not_161_out, not_162_out, not_163_out, not_164_out,
       not_165_out, not_166_out, not_167_out, not_168_out, not_169_out, not_170_out, not_171_out,
       not_172_out, not_173_out, not_174_out, not_175_out, not_176_out, not_177_out, not_178_out,
       not_179_out, not_180_out, not_181_out, not_182_out, not_183_out, not_184_out, not_185_out,
       not_186_out, not_187_out, not_188_out, not_189_out, not_190_out, not_191_out, not_192_out,
       not_193_out, not_194_out, not_195_out, not_196_out, not_197_out, not_198_out, not_199_out,
       not_200_out, not_201_out, not_202_out, not_203_out, not_204_out, not_205_out, not_206_out,
       not_207_out, not_208_out, not_209_out, not_210_out, not_211_out, not_212_out, not_213_out,
       not_214_out, not_215_out, not_216_out, not_217_out, not_218_out, not_219_out, not_220_out,
       not_221_out, not_222_out, not_223_out, not_224_out, not_225_out, not_226_out, not_227_out,
       not_228_out, not_229_out, not_230_out, not_231_out, not_232_out, not_233_out, not_234_out,
       not_235_out, not_236_out, not_237_out, not_238_out, not_239_out, not_240_out, not_241_out,
       not_242_out, not_243_out, not_244_out, not_245_out, not_246_out, not_247_out, not_248_out,
       not_249_out, not_250_out, not_251_out, not_252_out;

  not not_1 (not_1_out, OP5);
  not not_2 (not_2_out, OP4);
  not not_3 (not_3_out, OP3);
  not not_4 (not_4_out, OP2);
  not not_5 (not_5_out, OP1);
  not not_6 (not_6_out, OP0);
  not not_7 (not_7_out, F5);
  not not_8 (not_8_out, F4);
  not not_9 (not_9_out, F3);
  not not_10 (not_10_out, F2);
  not not_11 (not_11_out, OP5);
  not not_12 (not_12_out, OP4);
  not not_13 (not_13_out, OP3);
  not not_14 (not_14_out, OP2);
  not not_15 (not_15_out, OP1);
  not not_16 (not_16_out, OP0);
  not not_17 (not_17_out, F4);
  not not_18 (not_18_out, F3);
  not not_19 (not_19_out, F2);
  not not_20 (not_20_out, F1);
  not not_21 (not_21_out, F0);
  not not_22 (not_22_out, OP5);
  not not_23 (not_23_out, OP4);
  not not_24 (not_24_out, OP3);
  not not_25 (not_25_out, OP2);
  not not_26 (not_26_out, OP1);
  not not_27 (not_27_out, OP0);
  not not_28 (not_28_out, F4);
  not not_29 (not_29_out, F3);
  not not_30 (not_30_out, F2);
  not not_31 (not_31_out, F1);
  not not_32 (not_32_out, OP5);
  not not_33 (not_33_out, OP4);
  not not_34 (not_34_out, OP3);
  not not_35 (not_35_out, OP2);
  not not_36 (not_36_out, OP1);
  not not_37 (not_37_out, OP0);
  not not_38 (not_38_out, F4);
  not not_39 (not_39_out, F3);
  not not_40 (not_40_out, F1);
  not not_41 (not_41_out, F0);
  not not_42 (not_42_out, OP5);
  not not_43 (not_43_out, OP4);
  not not_44 (not_44_out, OP3);
  not not_45 (not_45_out, OP2);
  not not_46 (not_46_out, OP1);
  not not_47 (not_47_out, OP0);
  not not_48 (not_48_out, F4);
  not not_49 (not_49_out, F2);
  not not_50 (not_50_out, F0);
  not not_51 (not_51_out, OP5);
  not not_52 (not_52_out, OP4);
  not not_53 (not_53_out, OP2);
  not not_54 (not_54_out, OP1);
  not not_55 (not_55_out, OP0);
  not not_56 (not_56_out, OP5);
  not not_57 (not_57_out, OP4);
  not not_58 (not_58_out, OP1);
  not not_59 (not_59_out, OP0);
  not not_60 (not_60_out, OP5);
  not not_61 (not_61_out, OP4);
  not not_62 (not_62_out, OP2);
  not not_63 (not_63_out, OP1);
  not not_64 (not_64_out, OP5);
  not not_65 (not_65_out, OP4);
  not not_66 (not_66_out, OP2);
  not not_67 (not_67_out, OP0);
  not not_68 (not_68_out, OP4);
  not not_69 (not_69_out, OP3);
  not not_70 (not_70_out, OP2);
  not not_71 (not_71_out, OP4);
  not not_72 (not_72_out, OP2);
  not not_73 (not_73_out, OP4);
  not not_74 (not_74_out, OP3);
  not not_75 (not_75_out, OP1);
  not not_76 (not_76_out, OP0);
  not not_77 (not_77_out, OP5);
  not not_78 (not_78_out, OP4);
  not not_79 (not_79_out, OP3);
  not not_80 (not_80_out, OP2);
  not not_81 (not_81_out, OP1);
  not not_82 (not_82_out, OP0);
  not not_83 (not_83_out, F5);
  not not_84 (not_84_out, F4);
  not not_85 (not_85_out, F3);
  not not_86 (not_86_out, F2);
  not not_87 (not_87_out, F0);
  not not_88 (not_88_out, OP5);
  not not_89 (not_89_out, OP4);
  not not_90 (not_90_out, OP3);
  not not_91 (not_91_out, OP2);
  not not_92 (not_92_out, OP1);
  not not_93 (not_93_out, OP0);
  not not_94 (not_94_out, F4);
  not not_95 (not_95_out, F3);
  not not_96 (not_96_out, F2);
  not not_97 (not_97_out, F0);
  not not_98 (not_98_out, OP5);
  not not_99 (not_99_out, OP4);
  not not_100 (not_100_out, OP3);
  not not_101 (not_101_out, OP2);
  not not_102 (not_102_out, OP1);
  not not_103 (not_103_out, OP0);
  not not_104 (not_104_out, F4);
  not not_105 (not_105_out, F3);
  not not_106 (not_106_out, F1);
  not not_107 (not_107_out, F0);
  not not_108 (not_108_out, OP5);
  not not_109 (not_109_out, OP4);
  not not_110 (not_110_out, OP3);
  not not_111 (not_111_out, OP2);
  not not_112 (not_112_out, OP1);
  not not_113 (not_113_out, OP0);
  not not_114 (not_114_out, F4);
  not not_115 (not_115_out, F3);
  not not_116 (not_116_out, OP5);
  not not_117 (not_117_out, OP4);
  not not_118 (not_118_out, OP3);
  not not_119 (not_119_out, OP2);
  not not_120 (not_120_out, OP1);
  not not_121 (not_121_out, OP0);
  not not_122 (not_122_out, F4);
  not not_123 (not_123_out, F2);
  not not_124 (not_124_out, F0);
  not not_125 (not_125_out, OP5);
  not not_126 (not_126_out, OP4);
  not not_127 (not_127_out, OP1);
  not not_128 (not_128_out, OP0);
  not not_129 (not_129_out, OP5);
  not not_130 (not_130_out, OP4);
  not not_131 (not_131_out, OP2);
  not not_132 (not_132_out, OP0);
  not not_133 (not_133_out, OP5);
  not not_134 (not_134_out, OP4);
  not not_135 (not_135_out, OP3);
  not not_136 (not_136_out, OP2);
  not not_137 (not_137_out, OP1);
  not not_138 (not_138_out, OP0);
  not not_139 (not_139_out, F4);
  not not_140 (not_140_out, F3);
  not not_141 (not_141_out, F2);
  not not_142 (not_142_out, F1);
  not not_143 (not_143_out, F0);
  not not_144 (not_144_out, OP5);
  not not_145 (not_145_out, OP4);
  not not_146 (not_146_out, OP3);
  not not_147 (not_147_out, OP2);
  not not_148 (not_148_out, OP1);
  not not_149 (not_149_out, OP0);
  not not_150 (not_150_out, F4);
  not not_151 (not_151_out, F3);
  not not_152 (not_152_out, F2);
  not not_153 (not_153_out, F1);
  not not_154 (not_154_out, OP5);
  not not_155 (not_155_out, OP4);
  not not_156 (not_156_out, OP3);
  not not_157 (not_157_out, OP2);
  not not_158 (not_158_out, OP1);
  not not_159 (not_159_out, OP0);
  not not_160 (not_160_out, F4);
  not not_161 (not_161_out, F3);
  not not_162 (not_162_out, F2);
  not not_163 (not_163_out, F0);
  not not_164 (not_164_out, OP5);
  not not_165 (not_165_out, OP4);
  not not_166 (not_166_out, OP3);
  not not_167 (not_167_out, OP2);
  not not_168 (not_168_out, OP1);
  not not_169 (not_169_out, OP0);
  not not_170 (not_170_out, F4);
  not not_171 (not_171_out, F3);
  not not_172 (not_172_out, F1);
  not not_173 (not_173_out, F0);
  not not_174 (not_174_out, OP5);
  not not_175 (not_175_out, OP4);
  not not_176 (not_176_out, OP3);
  not not_177 (not_177_out, OP2);
  not not_178 (not_178_out, OP1);
  not not_179 (not_179_out, OP0);
  not not_180 (not_180_out, F4);
  not not_181 (not_181_out, F2);
  not not_182 (not_182_out, OP5);
  not not_183 (not_183_out, OP4);
  not not_184 (not_184_out, OP2);
  not not_185 (not_185_out, OP1);
  not not_186 (not_186_out, OP0);
  not not_187 (not_187_out, OP5);
  not not_188 (not_188_out, OP4);
  not not_189 (not_189_out, OP1);
  not not_190 (not_190_out, OP0);
  not not_191 (not_191_out, OP5);
  not not_192 (not_192_out, OP4);
  not not_193 (not_193_out, OP2);
  not not_194 (not_194_out, OP1);
  not not_195 (not_195_out, OP4);
  not not_196 (not_196_out, OP3);
  not not_197 (not_197_out, OP2);
  not not_198 (not_198_out, OP4);
  not not_199 (not_199_out, OP2);
  not not_200 (not_200_out, OP5);
  not not_201 (not_201_out, OP4);
  not not_202 (not_202_out, OP3);
  not not_203 (not_203_out, OP2);
  not not_204 (not_204_out, OP1);
  not not_205 (not_205_out, OP0);
  not not_206 (not_206_out, F5);
  not not_207 (not_207_out, F2);
  not not_208 (not_208_out, OP4);
  not not_209 (not_209_out, OP3);
  not not_210 (not_210_out, OP1);
  not not_211 (not_211_out, OP0);
  not not_212 (not_212_out, OP5);
  not not_213 (not_213_out, OP4);
  not not_214 (not_214_out, OP3);
  not not_215 (not_215_out, OP2);
  not not_216 (not_216_out, OP1);
  not not_217 (not_217_out, OP0);
  not not_218 (not_218_out, F4);
  not not_219 (not_219_out, F3);
  not not_220 (not_220_out, F1);
  not not_221 (not_221_out, OP5);
  not not_222 (not_222_out, OP4);
  not not_223 (not_223_out, OP3);
  not not_224 (not_224_out, OP2);
  not not_225 (not_225_out, OP1);
  not not_226 (not_226_out, OP0);
  not not_227 (not_227_out, F4);
  not not_228 (not_228_out, F3);
  not not_229 (not_229_out, OP5);
  not not_230 (not_230_out, OP4);
  not not_231 (not_231_out, OP3);
  not not_232 (not_232_out, OP2);
  not not_233 (not_233_out, OP1);
  not not_234 (not_234_out, OP0);
  not not_235 (not_235_out, F4);
  not not_236 (not_236_out, F2);
  not not_237 (not_237_out, F0);
  not not_238 (not_238_out, OP5);
  not not_239 (not_239_out, OP4);
  not not_240 (not_240_out, OP3);
  not not_241 (not_241_out, OP2);
  not not_242 (not_242_out, OP1);
  not not_243 (not_243_out, OP0);
  not not_244 (not_244_out, F4);
  not not_245 (not_245_out, F2);
  not not_246 (not_246_out, OP5);
  not not_247 (not_247_out, OP4);
  not not_248 (not_248_out, OP2);
  not not_249 (not_249_out, OP0);
  not not_250 (not_250_out, OP5);
  not not_251 (not_251_out, OP4);
  not not_252 (not_252_out, OP1);
  and and_1 (and_1_out, not_1_out, not_2_out, not_3_out, not_4_out, not_5_out, not_6_out, not_7_out, not_8_out, not_9_out, not_10_out, F1, F0);
  and and_2 (and_2_out, not_11_out, not_12_out, not_13_out, not_14_out, not_15_out, not_16_out, F5, not_17_out, not_18_out, not_19_out, not_20_out, not_21_out);
  and and_3 (and_3_out, not_22_out, not_23_out, not_24_out, not_25_out, not_26_out, not_27_out, F5, not_28_out, not_29_out, not_30_out, not_31_out, F0);
  and and_4 (and_4_out, not_32_out, not_33_out, not_34_out, not_35_out, not_36_out, not_37_out, F5, not_38_out, not_39_out, F2, not_40_out, not_41_out);
  and and_5 (and_5_out, not_42_out, not_43_out, not_44_out, not_45_out, not_46_out, not_47_out, F5, not_48_out, F3, not_49_out, F1, not_50_out);
  and and_6 (and_6_out, not_51_out, not_52_out, OP3, not_53_out, not_54_out, not_55_out);
  and and_7 (and_7_out, not_56_out, not_57_out, OP3, OP2, not_58_out, not_59_out);
  and and_8 (and_8_out, not_60_out, not_61_out, OP3, not_62_out, not_63_out, OP0);
  and and_9 (and_9_out, not_64_out, not_65_out, OP3, not_66_out, OP1, not_67_out);
  and and_10 (and_10_out, OP5, not_68_out, not_69_out, not_70_out, OP1, OP0);
  and and_11 (and_11_out, OP5, not_71_out, OP3, not_72_out, OP1, OP0);
  and and_12 (and_12_out, OP5, not_73_out, not_74_out, OP2, not_75_out, not_76_out);
  and and_13 (and_13_out, not_77_out, not_78_out, not_79_out, not_80_out, not_81_out, not_82_out, not_83_out, not_84_out, not_85_out, not_86_out, F1, not_87_out);
  and and_14 (and_14_out, not_88_out, not_89_out, not_90_out, not_91_out, not_92_out, not_93_out, F5, not_94_out, not_95_out, not_96_out, F1, not_97_out);
  and and_15 (and_15_out, not_98_out, not_99_out, not_100_out, not_101_out, not_102_out, not_103_out, F5, not_104_out, not_105_out, F2, not_106_out, not_107_out);
  and and_16 (and_16_out, not_108_out, not_109_out, not_110_out, not_111_out, not_112_out, not_113_out, F5, not_114_out, not_115_out, F2, F1, F0);
  and and_17 (and_17_out, not_116_out, not_117_out, not_118_out, not_119_out, not_120_out, not_121_out, F5, not_122_out, F3, not_123_out, F1, not_124_out);
  and and_18 (and_18_out, not_125_out, not_126_out, OP3, OP2, not_127_out, not_128_out);
  and and_19 (and_19_out, not_129_out, not_130_out, OP3, not_131_out, OP1, not_132_out);
  and and_20 (and_20_out, not_133_out, not_134_out, not_135_out, not_136_out, not_137_out, not_138_out, F5, not_139_out, not_140_out, not_141_out, not_142_out, not_143_out);
  and and_21 (and_21_out, not_144_out, not_145_out, not_146_out, not_147_out, not_148_out, not_149_out, F5, not_150_out, not_151_out, not_152_out, not_153_out, F0);
  and and_22 (and_22_out, not_154_out, not_155_out, not_156_out, not_157_out, not_158_out, not_159_out, F5, not_160_out, not_161_out, not_162_out, F1, not_163_out);
  and and_23 (and_23_out, not_164_out, not_165_out, not_166_out, not_167_out, not_168_out, not_169_out, F5, not_170_out, not_171_out, F2, not_172_out, not_173_out);
  and and_24 (and_24_out, not_174_out, not_175_out, not_176_out, not_177_out, not_178_out, not_179_out, F5, not_180_out, F3, not_181_out, F1, F0);
  and and_25 (and_25_out, not_182_out, not_183_out, OP3, not_184_out, not_185_out, not_186_out);
  and and_26 (and_26_out, not_187_out, not_188_out, OP3, OP2, not_189_out, not_190_out);
  and and_27 (and_27_out, not_191_out, not_192_out, OP3, not_193_out, not_194_out, OP0);
  and and_28 (and_28_out, OP5, not_195_out, not_196_out, not_197_out, OP1, OP0);
  and and_29 (and_29_out, OP5, not_198_out, OP3, not_199_out, OP1, OP0);
  and and_30 (and_30_out, not_200_out, not_201_out, not_202_out, not_203_out, not_204_out, not_205_out, not_206_out, F4, F3, not_207_out, F1, F0);
  and and_31 (and_31_out, OP5, not_208_out, not_209_out, OP2, not_210_out, not_211_out);
  and and_32 (and_32_out, not_212_out, not_213_out, not_214_out, not_215_out, not_216_out, not_217_out, F5, not_218_out, not_219_out, F2, not_220_out, F0);
  and and_33 (and_33_out, not_221_out, not_222_out, not_223_out, not_224_out, not_225_out, not_226_out, F5, not_227_out, not_228_out, F2, F1, F0);
  and and_34 (and_34_out, not_229_out, not_230_out, not_231_out, not_232_out, not_233_out, not_234_out, F5, not_235_out, F3, not_236_out, F1, not_237_out);
  and and_35 (and_35_out, not_238_out, not_239_out, not_240_out, not_241_out, not_242_out, not_243_out, F5, not_244_out, F3, not_245_out, F1, F0);
  and and_36 (and_36_out, not_246_out, not_247_out, OP3, not_248_out, OP1, not_249_out);
  and and_37 (and_37_out, not_250_out, not_251_out, OP3, OP2, not_252_out, OP0);
  or or_1 (S1, and_13_out, and_14_out, and_15_out, and_16_out, and_17_out, and_18_out, and_19_out);
  or or_2 (S3, and_32_out, and_33_out, and_34_out, and_35_out, and_36_out, and_37_out);
  or or_3 (S0, and_1_out, and_2_out, and_3_out, and_4_out, and_5_out, and_6_out, and_7_out, and_8_out, and_9_out, and_10_out, and_11_out, and_12_out);
  or or_4 (S2, and_20_out, and_21_out, and_22_out, and_23_out, and_24_out, and_25_out, and_26_out, and_27_out, and_28_out, and_29_out, and_30_out, and_31_out);
endmodule

// 控制信号生成
module \控制信号自动生成  (
  input  OP0,
  input  OP1,
  input  OP2,
  input  OP3,
  input  OP4,
  input  OP5,
  input  F0,
  input  F1,
  input  F2,
  input  F3,
  input  F4,
  input  F5,
  output MemToReg,
  output MemWrite,
  output ALU_SRC,
  output RegWrite,
  output SysCALL,
  output SignedExt,
  output RegDst,
  output BEQ,
  output BNE,
  output JR,
  output JUMP,
  output JAL,
  output DIVU,
  output MFLO,
  output LBU,
  output BGTZ,
  output R1_Used,
  output R2_Used
);

  wire and_1_out, and_2_out, and_4_out, and_5_out, and_6_out, and_7_out, and_8_out, and_9_out, and_10_out,
       and_11_out, and_12_out, and_13_out, and_14_out, and_15_out, and_16_out, and_17_out, and_18_out,
       and_19_out, and_20_out, and_21_out, and_22_out, and_23_out, and_24_out, and_25_out, and_26_out,
       and_27_out, and_28_out, and_29_out, and_30_out, and_31_out, and_33_out, and_34_out, and_35_out,
       and_36_out, and_37_out, and_38_out, and_39_out, and_40_out, and_41_out, and_42_out, and_43_out,
       and_44_out, and_45_out, and_46_out, and_47_out, and_48_out, and_49_out, and_50_out, and_51_out,
       and_52_out, and_56_out, and_57_out, and_58_out, and_64_out, and_65_out, and_66_out, and_67_out,
       and_68_out, and_69_out, and_70_out, and_71_out, and_72_out, and_73_out, and_74_out, and_75_out,
       and_76_out, and_77_out, and_78_out, and_79_out, and_80_out, and_81_out, and_82_out, and_83_out,
       and_84_out, and_85_out, and_86_out, and_87_out, and_88_out, and_89_out, and_90_out, and_91_out,
       and_92_out, and_93_out, and_94_out, and_95_out, and_96_out, and_97_out, and_98_out, and_99_out,
       and_100_out, and_101_out, and_102_out, and_103_out, and_104_out, not_1_out, not_2_out, not_3_out,
       not_4_out, not_5_out, not_6_out, not_7_out, not_8_out, not_9_out, not_10_out, not_11_out, not_12_out,
       not_13_out, not_14_out, not_15_out, not_16_out, not_17_out, not_18_out, not_19_out, not_20_out,
       not_21_out, not_22_out, not_23_out, not_24_out, not_25_out, not_26_out, not_27_out, not_28_out,
       not_29_out, not_30_out, not_31_out, not_32_out, not_33_out, not_34_out, not_35_out, not_36_out,
       not_37_out, not_38_out, not_39_out, not_40_out, not_41_out, not_42_out, not_43_out, not_44_out,
       not_45_out, not_46_out, not_47_out, not_48_out, not_49_out, not_50_out, not_51_out, not_52_out,
       not_53_out, not_54_out, not_55_out, not_56_out, not_57_out, not_58_out, not_59_out, not_60_out,
       not_61_out, not_62_out, not_63_out, not_64_out, not_65_out, not_66_out, not_67_out, not_68_out,
       not_69_out, not_70_out, not_71_out, not_72_out, not_73_out, not_74_out, not_75_out, not_76_out,
       not_77_out, not_78_out, not_79_out, not_80_out, not_81_out, not_82_out, not_83_out, not_84_out,
       not_85_out, not_86_out, not_87_out, not_88_out, not_89_out, not_90_out, not_91_out, not_92_out,
       not_93_out, not_94_out, not_95_out, not_96_out, not_97_out, not_98_out, not_99_out, not_100_out,
       not_101_out, not_102_out, not_103_out, not_104_out, not_105_out, not_106_out, not_107_out,
       not_108_out, not_109_out, not_110_out, not_111_out, not_112_out, not_113_out, not_114_out,
       not_115_out, not_116_out, not_117_out, not_118_out, not_119_out, not_120_out, not_121_out,
       not_122_out, not_123_out, not_124_out, not_125_out, not_126_out, not_127_out, not_128_out,
       not_129_out, not_130_out, not_131_out, not_132_out, not_133_out, not_134_out, not_135_out,
       not_136_out, not_137_out, not_138_out, not_139_out, not_140_out, not_141_out, not_142_out,
       not_143_out, not_144_out, not_145_out, not_146_out, not_147_out, not_148_out, not_149_out,
       not_150_out, not_151_out, not_152_out, not_153_out, not_154_out, not_155_out, not_156_out,
       not_157_out, not_158_out, not_159_out, not_160_out, not_161_out, not_162_out, not_163_out,
       not_164_out, not_165_out, not_166_out, not_167_out, not_168_out, not_169_out, not_170_out,
       not_171_out, not_172_out, not_173_out, not_174_out, not_175_out, not_176_out, not_177_out,
       not_178_out, not_179_out, not_180_out, not_181_out, not_182_out, not_183_out, not_184_out,
       not_185_out, not_186_out, not_187_out, not_188_out, not_189_out, not_190_out, not_191_out,
       not_192_out, not_193_out, not_194_out, not_195_out, not_196_out, not_197_out, not_198_out,
       not_199_out, not_200_out, not_201_out, not_202_out, not_203_out, not_204_out, not_205_out,
       not_206_out, not_207_out, not_208_out, not_209_out, not_210_out, not_211_out, not_212_out,
       not_213_out, not_214_out, not_215_out, not_216_out, not_217_out, not_218_out, not_219_out,
       not_220_out, not_221_out, not_222_out, not_223_out, not_224_out, not_225_out, not_226_out,
       not_227_out, not_228_out, not_229_out, not_230_out, not_231_out, not_232_out, not_233_out,
       not_234_out, not_235_out, not_236_out, not_237_out, not_238_out, not_239_out, not_240_out,
       not_241_out, not_242_out, not_243_out, not_244_out, not_245_out, not_246_out, not_247_out,
       not_248_out, not_249_out, not_250_out, not_251_out, not_252_out, not_253_out, not_254_out,
       not_255_out, not_256_out, not_257_out, not_258_out, not_259_out, not_260_out, not_261_out,
       not_262_out, not_263_out, not_264_out, not_265_out, not_266_out, not_267_out, not_268_out,
       not_269_out, not_270_out, not_271_out, not_272_out, not_273_out, not_274_out, not_275_out,
       not_276_out, not_277_out, not_278_out, not_279_out, not_280_out, not_281_out, not_282_out,
       not_283_out, not_284_out, not_285_out, not_286_out, not_287_out, not_288_out, not_289_out,
       not_290_out, not_291_out, not_292_out, not_293_out, not_294_out, not_295_out, not_296_out,
       not_297_out, not_298_out, not_299_out, not_300_out, not_301_out, not_302_out, not_303_out,
       not_304_out, not_305_out, not_306_out, not_307_out, not_308_out, not_309_out, not_310_out,
       not_311_out, not_312_out, not_313_out, not_314_out, not_315_out, not_316_out, not_317_out,
       not_318_out, not_319_out, not_320_out, not_321_out, not_322_out, not_323_out, not_324_out,
       not_325_out, not_326_out, not_327_out, not_328_out, not_329_out, not_330_out, not_331_out,
       not_332_out, not_333_out, not_334_out, not_335_out, not_336_out, not_337_out, not_338_out,
       not_339_out, not_340_out, not_341_out, not_342_out, not_343_out, not_344_out, not_345_out,
       not_346_out, not_347_out, not_348_out, not_349_out, not_350_out, not_351_out, not_352_out,
       not_353_out, not_354_out, not_355_out, not_356_out, not_357_out, not_358_out, not_359_out,
       not_360_out, not_361_out, not_362_out, not_363_out, not_364_out, not_365_out, not_366_out,
       not_367_out, not_368_out, not_369_out, not_370_out, not_371_out, not_372_out, not_373_out,
       not_374_out, not_375_out, not_376_out, not_377_out, not_378_out, not_379_out, not_380_out,
       not_381_out, not_382_out, not_383_out, not_384_out, not_385_out, not_386_out, not_387_out,
       not_388_out, not_389_out, not_390_out, not_391_out, not_392_out, not_393_out, not_394_out,
       not_395_out, not_396_out, not_397_out, not_398_out, not_399_out, not_400_out, not_401_out,
       not_402_out, not_403_out, not_404_out, not_405_out, not_406_out, not_407_out, not_408_out,
       not_409_out, not_410_out, not_411_out, not_412_out, not_413_out, not_414_out, not_415_out,
       not_416_out, not_417_out, not_418_out, not_419_out, not_420_out, not_421_out, not_422_out,
       not_423_out, not_424_out, not_425_out, not_426_out, not_427_out, not_428_out, not_429_out,
       not_430_out, not_431_out, not_432_out, not_433_out, not_434_out, not_435_out, not_436_out,
       not_437_out, not_438_out, not_439_out, not_440_out, not_441_out, not_442_out, not_443_out,
       not_444_out, not_445_out, not_446_out, not_447_out, not_448_out, not_449_out, not_450_out,
       not_451_out, not_452_out, not_453_out, not_454_out, not_455_out, not_456_out, not_457_out,
       not_458_out, not_459_out, not_460_out, not_461_out, not_462_out, not_463_out, not_464_out,
       not_465_out, not_466_out, not_467_out, not_468_out, not_469_out, not_470_out, not_471_out,
       not_472_out, not_473_out, not_474_out, not_475_out, not_476_out, not_477_out, not_478_out,
       not_479_out, not_480_out, not_481_out, not_482_out, not_483_out, not_484_out, not_485_out,
       not_486_out, not_487_out, not_488_out, not_489_out, not_490_out, not_491_out, not_492_out,
       not_493_out, not_494_out, not_495_out, not_496_out, not_497_out, not_498_out, not_499_out,
       not_500_out, not_501_out, not_502_out, not_503_out, not_504_out, not_505_out, not_506_out,
       not_507_out, not_508_out, not_509_out, not_510_out, not_511_out, not_512_out, not_513_out,
       not_514_out, not_515_out, not_516_out, not_517_out, not_518_out, not_519_out, not_520_out,
       not_521_out, not_522_out, not_523_out, not_524_out, not_525_out, not_526_out, not_527_out,
       not_528_out, not_529_out, not_530_out, not_531_out, not_532_out, not_533_out, not_534_out,
       not_535_out, not_536_out, not_537_out, not_538_out, not_539_out, not_540_out, not_541_out,
       not_542_out, not_543_out, not_544_out, not_545_out, not_546_out, not_547_out, not_548_out,
       not_549_out, not_550_out, not_551_out, not_552_out, not_553_out, not_554_out, not_555_out,
       not_556_out, not_557_out, not_558_out, not_559_out, not_560_out, not_561_out, not_562_out,
       not_563_out, not_564_out, not_565_out, not_566_out, not_567_out, not_568_out, not_569_out,
       not_570_out, not_571_out, not_572_out, not_573_out, not_574_out, not_575_out, not_576_out,
       not_577_out, not_578_out, not_579_out, not_580_out, not_581_out, not_582_out, not_583_out,
       not_584_out, not_585_out, not_586_out, not_587_out, not_588_out, not_589_out, not_590_out,
       not_591_out, not_592_out, not_593_out, not_594_out, not_595_out, not_596_out, not_597_out,
       not_598_out, not_599_out, not_600_out, not_601_out, not_602_out, not_603_out, not_604_out,
       not_605_out, not_606_out, not_607_out, not_608_out, not_609_out, not_610_out, not_611_out,
       not_612_out, not_613_out, not_614_out, not_615_out, not_616_out, not_617_out, not_618_out,
       not_619_out, not_620_out, not_621_out, not_622_out, not_623_out, not_624_out, not_625_out,
       not_626_out, not_627_out, not_628_out, not_629_out, not_630_out, not_631_out, not_632_out,
       not_633_out, not_634_out, not_635_out, not_636_out, not_637_out, not_638_out, not_639_out,
       not_640_out, not_641_out, not_642_out, not_643_out, not_644_out, not_645_out, not_646_out,
       not_647_out, not_648_out, not_649_out, not_650_out, not_651_out, not_652_out, not_653_out,
       not_654_out, not_655_out, not_656_out, not_657_out, not_658_out, not_659_out, not_660_out,
       not_661_out, not_662_out, not_663_out, not_664_out, not_665_out, not_666_out, not_667_out,
       not_668_out, not_669_out, not_670_out, not_671_out, not_672_out, not_673_out, not_674_out,
       not_675_out, not_676_out, not_677_out, not_678_out, not_679_out, not_680_out, not_681_out,
       not_682_out, not_683_out, not_684_out, not_685_out, not_686_out, not_687_out, not_688_out,
       not_689_out, not_690_out, not_691_out, not_692_out, not_693_out, not_694_out, not_695_out,
       not_696_out, not_697_out, not_698_out, not_699_out, not_700_out, not_701_out, not_702_out,
       not_703_out, not_704_out, not_705_out, not_706_out, not_707_out, not_708_out, not_709_out,
       not_710_out, not_711_out, not_712_out, not_713_out, not_714_out, not_715_out, not_716_out,
       not_717_out, not_718_out, not_719_out, not_720_out, not_721_out, not_722_out, not_723_out;

  not not_1 (not_1_out, OP4);
  not not_2 (not_2_out, OP3);
  not not_3 (not_3_out, OP2);
  not not_4 (not_4_out, OP4);
  not not_5 (not_5_out, OP3);
  not not_6 (not_6_out, OP1);
  not not_7 (not_7_out, OP0);
  not not_8 (not_8_out, OP4);
  not not_9 (not_9_out, OP2);
  not not_10 (not_10_out, OP5);
  not not_11 (not_11_out, OP4);
  not not_12 (not_12_out, OP2);
  not not_13 (not_13_out, OP1);
  not not_14 (not_14_out, OP0);
  not not_15 (not_15_out, OP5);
  not not_16 (not_16_out, OP4);
  not not_17 (not_17_out, OP1);
  not not_18 (not_18_out, OP0);
  not not_19 (not_19_out, OP5);
  not not_20 (not_20_out, OP4);
  not not_21 (not_21_out, OP2);
  not not_22 (not_22_out, OP1);
  not not_23 (not_23_out, OP5);
  not not_24 (not_24_out, OP4);
  not not_25 (not_25_out, OP2);
  not not_26 (not_26_out, OP0);
  not not_27 (not_27_out, OP5);
  not not_28 (not_28_out, OP4);
  not not_29 (not_29_out, OP1);
  not not_30 (not_30_out, OP4);
  not not_31 (not_31_out, OP3);
  not not_32 (not_32_out, OP2);
  not not_33 (not_33_out, OP4);
  not not_34 (not_34_out, OP2);
  not not_35 (not_35_out, OP4);
  not not_36 (not_36_out, OP3);
  not not_37 (not_37_out, OP1);
  not not_38 (not_38_out, OP0);
  not not_39 (not_39_out, OP5);
  not not_40 (not_40_out, OP4);
  not not_41 (not_41_out, OP3);
  not not_42 (not_42_out, OP2);
  not not_43 (not_43_out, OP1);
  not not_44 (not_44_out, OP0);
  not not_45 (not_45_out, F5);
  not not_46 (not_46_out, F4);
  not not_47 (not_47_out, F3);
  not not_48 (not_48_out, F2);
  not not_49 (not_49_out, F1);
  not not_50 (not_50_out, F0);
  not not_51 (not_51_out, OP5);
  not not_52 (not_52_out, OP4);
  not not_53 (not_53_out, OP3);
  not not_54 (not_54_out, OP2);
  not not_55 (not_55_out, OP1);
  not not_56 (not_56_out, OP0);
  not not_57 (not_57_out, F5);
  not not_58 (not_58_out, F4);
  not not_59 (not_59_out, F3);
  not not_60 (not_60_out, F2);
  not not_61 (not_61_out, OP5);
  not not_62 (not_62_out, OP4);
  not not_63 (not_63_out, OP3);
  not not_64 (not_64_out, OP2);
  not not_65 (not_65_out, OP1);
  not not_66 (not_66_out, OP0);
  not not_67 (not_67_out, F5);
  not not_68 (not_68_out, F4);
  not not_69 (not_69_out, F3);
  not not_70 (not_70_out, F2);
  not not_71 (not_71_out, F0);
  not not_72 (not_72_out, OP5);
  not not_73 (not_73_out, OP4);
  not not_74 (not_74_out, OP3);
  not not_75 (not_75_out, OP2);
  not not_76 (not_76_out, OP1);
  not not_77 (not_77_out, OP0);
  not not_78 (not_78_out, F4);
  not not_79 (not_79_out, F3);
  not not_80 (not_80_out, F2);
  not not_81 (not_81_out, F1);
  not not_82 (not_82_out, F0);
  not not_83 (not_83_out, OP5);
  not not_84 (not_84_out, OP4);
  not not_85 (not_85_out, OP3);
  not not_86 (not_86_out, OP2);
  not not_87 (not_87_out, OP1);
  not not_88 (not_88_out, OP0);
  not not_89 (not_89_out, F4);
  not not_90 (not_90_out, F3);
  not not_91 (not_91_out, F2);
  not not_92 (not_92_out, F1);
  not not_93 (not_93_out, OP5);
  not not_94 (not_94_out, OP4);
  not not_95 (not_95_out, OP3);
  not not_96 (not_96_out, OP2);
  not not_97 (not_97_out, OP1);
  not not_98 (not_98_out, OP0);
  not not_99 (not_99_out, F4);
  not not_100 (not_100_out, F3);
  not not_101 (not_101_out, F2);
  not not_102 (not_102_out, F0);
  not not_103 (not_103_out, OP5);
  not not_104 (not_104_out, OP4);
  not not_105 (not_105_out, OP3);
  not not_106 (not_106_out, OP2);
  not not_107 (not_107_out, OP1);
  not not_108 (not_108_out, OP0);
  not not_109 (not_109_out, F4);
  not not_110 (not_110_out, F3);
  not not_111 (not_111_out, F1);
  not not_112 (not_112_out, F0);
  not not_113 (not_113_out, OP5);
  not not_114 (not_114_out, OP4);
  not not_115 (not_115_out, OP3);
  not not_116 (not_116_out, OP2);
  not not_117 (not_117_out, OP1);
  not not_118 (not_118_out, OP0);
  not not_119 (not_119_out, F4);
  not not_120 (not_120_out, F3);
  not not_121 (not_121_out, F1);
  not not_122 (not_122_out, OP5);
  not not_123 (not_123_out, OP4);
  not not_124 (not_124_out, OP3);
  not not_125 (not_125_out, OP2);
  not not_126 (not_126_out, OP1);
  not not_127 (not_127_out, OP0);
  not not_128 (not_128_out, F4);
  not not_129 (not_129_out, F3);
  not not_130 (not_130_out, OP5);
  not not_131 (not_131_out, OP4);
  not not_132 (not_132_out, OP3);
  not not_133 (not_133_out, OP2);
  not not_134 (not_134_out, OP1);
  not not_135 (not_135_out, OP0);
  not not_136 (not_136_out, F4);
  not not_137 (not_137_out, F2);
  not not_138 (not_138_out, F0);
  not not_139 (not_139_out, OP5);
  not not_140 (not_140_out, OP4);
  not not_141 (not_141_out, OP3);
  not not_142 (not_142_out, OP2);
  not not_143 (not_143_out, OP1);
  not not_144 (not_144_out, OP0);
  not not_145 (not_145_out, F4);
  not not_146 (not_146_out, F2);
  not not_147 (not_147_out, OP5);
  not not_148 (not_148_out, OP4);
  not not_149 (not_149_out, OP3);
  not not_150 (not_150_out, OP2);
  not not_151 (not_151_out, OP5);
  not not_152 (not_152_out, OP4);
  not not_153 (not_153_out, OP2);
  not not_154 (not_154_out, OP1);
  not not_155 (not_155_out, OP0);
  not not_156 (not_156_out, OP5);
  not not_157 (not_157_out, OP4);
  not not_158 (not_158_out, OP1);
  not not_159 (not_159_out, OP0);
  not not_160 (not_160_out, OP5);
  not not_161 (not_161_out, OP4);
  not not_162 (not_162_out, OP2);
  not not_163 (not_163_out, OP1);
  not not_164 (not_164_out, OP5);
  not not_165 (not_165_out, OP4);
  not not_166 (not_166_out, OP2);
  not not_167 (not_167_out, OP0);
  not not_168 (not_168_out, OP5);
  not not_169 (not_169_out, OP4);
  not not_170 (not_170_out, OP1);
  not not_171 (not_171_out, OP4);
  not not_172 (not_172_out, OP3);
  not not_173 (not_173_out, OP2);
  not not_174 (not_174_out, OP5);
  not not_175 (not_175_out, OP4);
  not not_176 (not_176_out, OP3);
  not not_177 (not_177_out, OP2);
  not not_178 (not_178_out, OP1);
  not not_179 (not_179_out, OP0);
  not not_180 (not_180_out, F5);
  not not_181 (not_181_out, F3);
  not not_182 (not_182_out, F2);
  not not_183 (not_183_out, F0);
  not not_184 (not_184_out, OP4);
  not not_185 (not_185_out, OP3);
  not not_186 (not_186_out, OP1);
  not not_187 (not_187_out, OP0);
  not not_188 (not_188_out, OP5);
  not not_189 (not_189_out, OP4);
  not not_190 (not_190_out, OP3);
  not not_191 (not_191_out, OP2);
  not not_192 (not_192_out, OP1);
  not not_193 (not_193_out, OP0);
  not not_194 (not_194_out, F5);
  not not_195 (not_195_out, F4);
  not not_196 (not_196_out, F1);
  not not_197 (not_197_out, F0);
  not not_198 (not_198_out, OP5);
  not not_199 (not_199_out, OP4);
  not not_200 (not_200_out, OP3);
  not not_201 (not_201_out, OP1);
  not not_202 (not_202_out, OP0);
  not not_203 (not_203_out, OP5);
  not not_204 (not_204_out, OP4);
  not not_205 (not_205_out, OP3);
  not not_206 (not_206_out, OP1);
  not not_207 (not_207_out, OP5);
  not not_208 (not_208_out, OP4);
  not not_209 (not_209_out, OP2);
  not not_210 (not_210_out, OP1);
  not not_211 (not_211_out, OP0);
  not not_212 (not_212_out, OP5);
  not not_213 (not_213_out, OP4);
  not not_214 (not_214_out, OP2);
  not not_215 (not_215_out, OP1);
  not not_216 (not_216_out, OP5);
  not not_217 (not_217_out, OP4);
  not not_218 (not_218_out, OP2);
  not not_219 (not_219_out, OP0);
  not not_220 (not_220_out, OP4);
  not not_221 (not_221_out, OP3);
  not not_222 (not_222_out, OP2);
  not not_223 (not_223_out, OP4);
  not not_224 (not_224_out, OP2);
  not not_225 (not_225_out, OP4);
  not not_226 (not_226_out, OP3);
  not not_227 (not_227_out, OP1);
  not not_228 (not_228_out, OP0);
  not not_229 (not_229_out, OP5);
  not not_230 (not_230_out, OP4);
  not not_231 (not_231_out, OP3);
  not not_232 (not_232_out, OP5);
  not not_233 (not_233_out, OP4);
  not not_234 (not_234_out, OP3);
  not not_235 (not_235_out, OP2);
  not not_236 (not_236_out, OP1);
  not not_237 (not_237_out, OP0);
  not not_238 (not_238_out, F5);
  not not_239 (not_239_out, F4);
  not not_240 (not_240_out, F3);
  not not_241 (not_241_out, F2);
  not not_242 (not_242_out, F1);
  not not_243 (not_243_out, F0);
  not not_244 (not_244_out, OP5);
  not not_245 (not_245_out, OP4);
  not not_246 (not_246_out, OP3);
  not not_247 (not_247_out, OP2);
  not not_248 (not_248_out, OP1);
  not not_249 (not_249_out, OP0);
  not not_250 (not_250_out, F5);
  not not_251 (not_251_out, F4);
  not not_252 (not_252_out, F3);
  not not_253 (not_253_out, F2);
  not not_254 (not_254_out, OP5);
  not not_255 (not_255_out, OP4);
  not not_256 (not_256_out, OP3);
  not not_257 (not_257_out, OP2);
  not not_258 (not_258_out, OP1);
  not not_259 (not_259_out, OP0);
  not not_260 (not_260_out, F5);
  not not_261 (not_261_out, F4);
  not not_262 (not_262_out, F3);
  not not_263 (not_263_out, F2);
  not not_264 (not_264_out, F0);
  not not_265 (not_265_out, OP5);
  not not_266 (not_266_out, OP4);
  not not_267 (not_267_out, OP3);
  not not_268 (not_268_out, OP2);
  not not_269 (not_269_out, OP1);
  not not_270 (not_270_out, OP0);
  not not_271 (not_271_out, F4);
  not not_272 (not_272_out, F3);
  not not_273 (not_273_out, F2);
  not not_274 (not_274_out, F1);
  not not_275 (not_275_out, F0);
  not not_276 (not_276_out, OP5);
  not not_277 (not_277_out, OP4);
  not not_278 (not_278_out, OP3);
  not not_279 (not_279_out, OP2);
  not not_280 (not_280_out, OP1);
  not not_281 (not_281_out, OP0);
  not not_282 (not_282_out, F4);
  not not_283 (not_283_out, F3);
  not not_284 (not_284_out, F2);
  not not_285 (not_285_out, F1);
  not not_286 (not_286_out, OP5);
  not not_287 (not_287_out, OP4);
  not not_288 (not_288_out, OP3);
  not not_289 (not_289_out, OP2);
  not not_290 (not_290_out, OP1);
  not not_291 (not_291_out, OP0);
  not not_292 (not_292_out, F4);
  not not_293 (not_293_out, F3);
  not not_294 (not_294_out, F2);
  not not_295 (not_295_out, F0);
  not not_296 (not_296_out, OP5);
  not not_297 (not_297_out, OP4);
  not not_298 (not_298_out, OP3);
  not not_299 (not_299_out, OP2);
  not not_300 (not_300_out, OP1);
  not not_301 (not_301_out, OP0);
  not not_302 (not_302_out, F4);
  not not_303 (not_303_out, F3);
  not not_304 (not_304_out, F1);
  not not_305 (not_305_out, F0);
  not not_306 (not_306_out, OP5);
  not not_307 (not_307_out, OP4);
  not not_308 (not_308_out, OP3);
  not not_309 (not_309_out, OP2);
  not not_310 (not_310_out, OP1);
  not not_311 (not_311_out, OP0);
  not not_312 (not_312_out, F4);
  not not_313 (not_313_out, F3);
  not not_314 (not_314_out, F1);
  not not_315 (not_315_out, OP5);
  not not_316 (not_316_out, OP4);
  not not_317 (not_317_out, OP3);
  not not_318 (not_318_out, OP2);
  not not_319 (not_319_out, OP1);
  not not_320 (not_320_out, OP0);
  not not_321 (not_321_out, F4);
  not not_322 (not_322_out, F3);
  not not_323 (not_323_out, OP5);
  not not_324 (not_324_out, OP4);
  not not_325 (not_325_out, OP3);
  not not_326 (not_326_out, OP2);
  not not_327 (not_327_out, OP1);
  not not_328 (not_328_out, OP0);
  not not_329 (not_329_out, F4);
  not not_330 (not_330_out, F2);
  not not_331 (not_331_out, F0);
  not not_332 (not_332_out, OP5);
  not not_333 (not_333_out, OP4);
  not not_334 (not_334_out, OP3);
  not not_335 (not_335_out, OP2);
  not not_336 (not_336_out, OP1);
  not not_337 (not_337_out, OP0);
  not not_338 (not_338_out, F4);
  not not_339 (not_339_out, F2);
  not not_340 (not_340_out, OP5);
  not not_341 (not_341_out, OP4);
  not not_342 (not_342_out, OP3);
  not not_343 (not_343_out, OP1);
  not not_344 (not_344_out, OP0);
  not not_345 (not_345_out, OP5);
  not not_346 (not_346_out, OP4);
  not not_347 (not_347_out, OP3);
  not not_348 (not_348_out, OP1);
  not not_349 (not_349_out, OP5);
  not not_350 (not_350_out, OP4);
  not not_351 (not_351_out, OP3);
  not not_352 (not_352_out, OP2);
  not not_353 (not_353_out, OP1);
  not not_354 (not_354_out, OP0);
  not not_355 (not_355_out, F5);
  not not_356 (not_356_out, F4);
  not not_357 (not_357_out, F2);
  not not_358 (not_358_out, F1);
  not not_359 (not_359_out, F0);
  not not_360 (not_360_out, OP5);
  not not_361 (not_361_out, OP4);
  not not_362 (not_362_out, OP3);
  not not_363 (not_363_out, OP2);
  not not_364 (not_364_out, OP1);
  not not_365 (not_365_out, OP0);
  not not_366 (not_366_out, F5);
  not not_367 (not_367_out, F4);
  not not_368 (not_368_out, F2);
  not not_369 (not_369_out, F1);
  not not_370 (not_370_out, F0);
  not not_371 (not_371_out, OP5);
  not not_372 (not_372_out, OP4);
  not not_373 (not_373_out, OP3);
  not not_374 (not_374_out, OP2);
  not not_375 (not_375_out, OP0);
  not not_376 (not_376_out, OP5);
  not not_377 (not_377_out, OP4);
  not not_378 (not_378_out, OP3);
  not not_379 (not_379_out, OP2);
  not not_380 (not_380_out, OP5);
  not not_381 (not_381_out, OP4);
  not not_382 (not_382_out, OP3);
  not not_383 (not_383_out, OP2);
  not not_384 (not_384_out, OP5);
  not not_385 (not_385_out, OP4);
  not not_386 (not_386_out, OP3);
  not not_387 (not_387_out, OP2);
  not not_388 (not_388_out, OP1);
  not not_389 (not_389_out, OP0);
  not not_390 (not_390_out, F5);
  not not_391 (not_391_out, F2);
  not not_392 (not_392_out, OP5);
  not not_393 (not_393_out, OP4);
  not not_394 (not_394_out, OP3);
  not not_395 (not_395_out, OP2);
  not not_396 (not_396_out, OP1);
  not not_397 (not_397_out, OP0);
  not not_398 (not_398_out, F5);
  not not_399 (not_399_out, F3);
  not not_400 (not_400_out, F2);
  not not_401 (not_401_out, F0);
  not not_402 (not_402_out, OP4);
  not not_403 (not_403_out, OP3);
  not not_404 (not_404_out, OP1);
  not not_405 (not_405_out, OP0);
  not not_406 (not_406_out, OP5);
  not not_407 (not_407_out, OP4);
  not not_408 (not_408_out, OP3);
  not not_409 (not_409_out, OP5);
  not not_410 (not_410_out, OP4);
  not not_411 (not_411_out, OP3);
  not not_412 (not_412_out, OP2);
  not not_413 (not_413_out, OP1);
  not not_414 (not_414_out, OP0);
  not not_415 (not_415_out, F5);
  not not_416 (not_416_out, F4);
  not not_417 (not_417_out, F3);
  not not_418 (not_418_out, F2);
  not not_419 (not_419_out, F1);
  not not_420 (not_420_out, F0);
  not not_421 (not_421_out, OP5);
  not not_422 (not_422_out, OP4);
  not not_423 (not_423_out, OP3);
  not not_424 (not_424_out, OP2);
  not not_425 (not_425_out, OP1);
  not not_426 (not_426_out, OP0);
  not not_427 (not_427_out, F5);
  not not_428 (not_428_out, F4);
  not not_429 (not_429_out, F3);
  not not_430 (not_430_out, F2);
  not not_431 (not_431_out, OP5);
  not not_432 (not_432_out, OP4);
  not not_433 (not_433_out, OP3);
  not not_434 (not_434_out, OP2);
  not not_435 (not_435_out, OP1);
  not not_436 (not_436_out, OP0);
  not not_437 (not_437_out, F5);
  not not_438 (not_438_out, F4);
  not not_439 (not_439_out, F3);
  not not_440 (not_440_out, F2);
  not not_441 (not_441_out, F0);
  not not_442 (not_442_out, OP5);
  not not_443 (not_443_out, OP4);
  not not_444 (not_444_out, OP3);
  not not_445 (not_445_out, OP2);
  not not_446 (not_446_out, OP1);
  not not_447 (not_447_out, OP0);
  not not_448 (not_448_out, F4);
  not not_449 (not_449_out, F3);
  not not_450 (not_450_out, F2);
  not not_451 (not_451_out, F1);
  not not_452 (not_452_out, F0);
  not not_453 (not_453_out, OP5);
  not not_454 (not_454_out, OP4);
  not not_455 (not_455_out, OP3);
  not not_456 (not_456_out, OP2);
  not not_457 (not_457_out, OP1);
  not not_458 (not_458_out, OP0);
  not not_459 (not_459_out, F4);
  not not_460 (not_460_out, F3);
  not not_461 (not_461_out, F2);
  not not_462 (not_462_out, F1);
  not not_463 (not_463_out, OP5);
  not not_464 (not_464_out, OP4);
  not not_465 (not_465_out, OP3);
  not not_466 (not_466_out, OP2);
  not not_467 (not_467_out, OP1);
  not not_468 (not_468_out, OP0);
  not not_469 (not_469_out, F4);
  not not_470 (not_470_out, F3);
  not not_471 (not_471_out, F2);
  not not_472 (not_472_out, F0);
  not not_473 (not_473_out, OP5);
  not not_474 (not_474_out, OP4);
  not not_475 (not_475_out, OP3);
  not not_476 (not_476_out, OP2);
  not not_477 (not_477_out, OP1);
  not not_478 (not_478_out, OP0);
  not not_479 (not_479_out, F4);
  not not_480 (not_480_out, F3);
  not not_481 (not_481_out, F1);
  not not_482 (not_482_out, F0);
  not not_483 (not_483_out, OP5);
  not not_484 (not_484_out, OP4);
  not not_485 (not_485_out, OP3);
  not not_486 (not_486_out, OP2);
  not not_487 (not_487_out, OP1);
  not not_488 (not_488_out, OP0);
  not not_489 (not_489_out, F4);
  not not_490 (not_490_out, F3);
  not not_491 (not_491_out, F1);
  not not_492 (not_492_out, OP5);
  not not_493 (not_493_out, OP4);
  not not_494 (not_494_out, OP3);
  not not_495 (not_495_out, OP2);
  not not_496 (not_496_out, OP1);
  not not_497 (not_497_out, OP0);
  not not_498 (not_498_out, F4);
  not not_499 (not_499_out, F3);
  not not_500 (not_500_out, OP5);
  not not_501 (not_501_out, OP4);
  not not_502 (not_502_out, OP3);
  not not_503 (not_503_out, OP2);
  not not_504 (not_504_out, OP1);
  not not_505 (not_505_out, OP0);
  not not_506 (not_506_out, F4);
  not not_507 (not_507_out, F2);
  not not_508 (not_508_out, F0);
  not not_509 (not_509_out, OP5);
  not not_510 (not_510_out, OP4);
  not not_511 (not_511_out, OP3);
  not not_512 (not_512_out, OP2);
  not not_513 (not_513_out, OP1);
  not not_514 (not_514_out, OP0);
  not not_515 (not_515_out, F4);
  not not_516 (not_516_out, F2);
  not not_517 (not_517_out, OP5);
  not not_518 (not_518_out, OP4);
  not not_519 (not_519_out, OP3);
  not not_520 (not_520_out, OP2);
  not not_521 (not_521_out, OP1);
  not not_522 (not_522_out, OP0);
  not not_523 (not_523_out, F5);
  not not_524 (not_524_out, F4);
  not not_525 (not_525_out, F2);
  not not_526 (not_526_out, F1);
  not not_527 (not_527_out, F0);
  not not_528 (not_528_out, OP5);
  not not_529 (not_529_out, OP4);
  not not_530 (not_530_out, OP3);
  not not_531 (not_531_out, OP2);
  not not_532 (not_532_out, OP1);
  not not_533 (not_533_out, OP0);
  not not_534 (not_534_out, F5);
  not not_535 (not_535_out, F4);
  not not_536 (not_536_out, F1);
  not not_537 (not_537_out, F0);
  not not_538 (not_538_out, OP5);
  not not_539 (not_539_out, OP4);
  not not_540 (not_540_out, OP3);
  not not_541 (not_541_out, OP1);
  not not_542 (not_542_out, OP0);
  not not_543 (not_543_out, OP5);
  not not_544 (not_544_out, OP4);
  not not_545 (not_545_out, OP3);
  not not_546 (not_546_out, OP1);
  not not_547 (not_547_out, OP5);
  not not_548 (not_548_out, OP4);
  not not_549 (not_549_out, OP2);
  not not_550 (not_550_out, OP1);
  not not_551 (not_551_out, OP0);
  not not_552 (not_552_out, OP5);
  not not_553 (not_553_out, OP4);
  not not_554 (not_554_out, OP1);
  not not_555 (not_555_out, OP0);
  not not_556 (not_556_out, OP5);
  not not_557 (not_557_out, OP4);
  not not_558 (not_558_out, OP2);
  not not_559 (not_559_out, OP1);
  not not_560 (not_560_out, OP5);
  not not_561 (not_561_out, OP4);
  not not_562 (not_562_out, OP2);
  not not_563 (not_563_out, OP0);
  not not_564 (not_564_out, OP5);
  not not_565 (not_565_out, OP4);
  not not_566 (not_566_out, OP1);
  not not_567 (not_567_out, OP4);
  not not_568 (not_568_out, OP3);
  not not_569 (not_569_out, OP2);
  not not_570 (not_570_out, OP4);
  not not_571 (not_571_out, OP2);
  not not_572 (not_572_out, OP5);
  not not_573 (not_573_out, OP4);
  not not_574 (not_574_out, OP3);
  not not_575 (not_575_out, OP2);
  not not_576 (not_576_out, OP1);
  not not_577 (not_577_out, OP0);
  not not_578 (not_578_out, F5);
  not not_579 (not_579_out, F2);
  not not_580 (not_580_out, OP4);
  not not_581 (not_581_out, OP3);
  not not_582 (not_582_out, OP1);
  not not_583 (not_583_out, OP0);
  not not_584 (not_584_out, OP5);
  not not_585 (not_585_out, OP4);
  not not_586 (not_586_out, OP3);
  not not_587 (not_587_out, OP5);
  not not_588 (not_588_out, OP4);
  not not_589 (not_589_out, OP3);
  not not_590 (not_590_out, OP2);
  not not_591 (not_591_out, OP1);
  not not_592 (not_592_out, OP0);
  not not_593 (not_593_out, F5);
  not not_594 (not_594_out, F4);
  not not_595 (not_595_out, F3);
  not not_596 (not_596_out, F2);
  not not_597 (not_597_out, F1);
  not not_598 (not_598_out, F0);
  not not_599 (not_599_out, OP5);
  not not_600 (not_600_out, OP4);
  not not_601 (not_601_out, OP3);
  not not_602 (not_602_out, OP2);
  not not_603 (not_603_out, OP1);
  not not_604 (not_604_out, OP0);
  not not_605 (not_605_out, F5);
  not not_606 (not_606_out, F4);
  not not_607 (not_607_out, F3);
  not not_608 (not_608_out, F2);
  not not_609 (not_609_out, OP5);
  not not_610 (not_610_out, OP4);
  not not_611 (not_611_out, OP3);
  not not_612 (not_612_out, OP2);
  not not_613 (not_613_out, OP1);
  not not_614 (not_614_out, OP0);
  not not_615 (not_615_out, F5);
  not not_616 (not_616_out, F4);
  not not_617 (not_617_out, F3);
  not not_618 (not_618_out, F2);
  not not_619 (not_619_out, F0);
  not not_620 (not_620_out, OP5);
  not not_621 (not_621_out, OP4);
  not not_622 (not_622_out, OP3);
  not not_623 (not_623_out, OP2);
  not not_624 (not_624_out, OP1);
  not not_625 (not_625_out, OP0);
  not not_626 (not_626_out, F4);
  not not_627 (not_627_out, F3);
  not not_628 (not_628_out, F2);
  not not_629 (not_629_out, F1);
  not not_630 (not_630_out, F0);
  not not_631 (not_631_out, OP5);
  not not_632 (not_632_out, OP4);
  not not_633 (not_633_out, OP3);
  not not_634 (not_634_out, OP2);
  not not_635 (not_635_out, OP1);
  not not_636 (not_636_out, OP0);
  not not_637 (not_637_out, F4);
  not not_638 (not_638_out, F3);
  not not_639 (not_639_out, F2);
  not not_640 (not_640_out, F1);
  not not_641 (not_641_out, OP5);
  not not_642 (not_642_out, OP4);
  not not_643 (not_643_out, OP3);
  not not_644 (not_644_out, OP2);
  not not_645 (not_645_out, OP1);
  not not_646 (not_646_out, OP0);
  not not_647 (not_647_out, F4);
  not not_648 (not_648_out, F3);
  not not_649 (not_649_out, F2);
  not not_650 (not_650_out, F0);
  not not_651 (not_651_out, OP5);
  not not_652 (not_652_out, OP4);
  not not_653 (not_653_out, OP3);
  not not_654 (not_654_out, OP2);
  not not_655 (not_655_out, OP1);
  not not_656 (not_656_out, OP0);
  not not_657 (not_657_out, F4);
  not not_658 (not_658_out, F3);
  not not_659 (not_659_out, F1);
  not not_660 (not_660_out, F0);
  not not_661 (not_661_out, OP5);
  not not_662 (not_662_out, OP4);
  not not_663 (not_663_out, OP3);
  not not_664 (not_664_out, OP2);
  not not_665 (not_665_out, OP1);
  not not_666 (not_666_out, OP0);
  not not_667 (not_667_out, F4);
  not not_668 (not_668_out, F3);
  not not_669 (not_669_out, F1);
  not not_670 (not_670_out, OP5);
  not not_671 (not_671_out, OP4);
  not not_672 (not_672_out, OP3);
  not not_673 (not_673_out, OP2);
  not not_674 (not_674_out, OP1);
  not not_675 (not_675_out, OP0);
  not not_676 (not_676_out, F4);
  not not_677 (not_677_out, F3);
  not not_678 (not_678_out, OP5);
  not not_679 (not_679_out, OP4);
  not not_680 (not_680_out, OP3);
  not not_681 (not_681_out, OP2);
  not not_682 (not_682_out, OP1);
  not not_683 (not_683_out, OP0);
  not not_684 (not_684_out, F4);
  not not_685 (not_685_out, F2);
  not not_686 (not_686_out, F0);
  not not_687 (not_687_out, OP5);
  not not_688 (not_688_out, OP4);
  not not_689 (not_689_out, OP3);
  not not_690 (not_690_out, OP2);
  not not_691 (not_691_out, OP1);
  not not_692 (not_692_out, OP0);
  not not_693 (not_693_out, F4);
  not not_694 (not_694_out, F2);
  not not_695 (not_695_out, OP5);
  not not_696 (not_696_out, OP4);
  not not_697 (not_697_out, OP3);
  not not_698 (not_698_out, OP2);
  not not_699 (not_699_out, OP1);
  not not_700 (not_700_out, OP0);
  not not_701 (not_701_out, F5);
  not not_702 (not_702_out, F4);
  not not_703 (not_703_out, F1);
  not not_704 (not_704_out, F0);
  not not_705 (not_705_out, OP5);
  not not_706 (not_706_out, OP4);
  not not_707 (not_707_out, OP3);
  not not_708 (not_708_out, OP1);
  not not_709 (not_709_out, OP0);
  not not_710 (not_710_out, OP5);
  not not_711 (not_711_out, OP4);
  not not_712 (not_712_out, OP3);
  not not_713 (not_713_out, OP1);
  not not_714 (not_714_out, OP4);
  not not_715 (not_715_out, OP2);
  not not_716 (not_716_out, OP5);
  not not_717 (not_717_out, OP4);
  not not_718 (not_718_out, OP3);
  not not_719 (not_719_out, OP2);
  not not_720 (not_720_out, OP1);
  not not_721 (not_721_out, OP0);
  not not_722 (not_722_out, F5);
  not not_723 (not_723_out, F2);
  and and_1 (and_1_out, OP5, not_1_out, not_2_out, not_3_out, OP1, OP0);
  and and_2 (and_2_out, OP5, not_4_out, not_5_out, OP2, not_6_out, not_7_out);
  and and_3 (MemWrite, OP5, not_8_out, OP3, not_9_out, OP1, OP0);
  and and_4 (and_4_out, not_10_out, not_11_out, OP3, not_12_out, not_13_out, not_14_out);
  and and_5 (and_5_out, not_15_out, not_16_out, OP3, OP2, not_17_out, not_18_out);
  and and_6 (and_6_out, not_19_out, not_20_out, OP3, not_21_out, not_22_out, OP0);
  and and_7 (and_7_out, not_23_out, not_24_out, OP3, not_25_out, OP1, not_26_out);
  and and_8 (and_8_out, not_27_out, not_28_out, OP3, OP2, not_29_out, OP0);
  and and_9 (and_9_out, OP5, not_30_out, not_31_out, not_32_out, OP1, OP0);
  and and_10 (and_10_out, OP5, not_33_out, OP3, not_34_out, OP1, OP0);
  and and_11 (and_11_out, OP5, not_35_out, not_36_out, OP2, not_37_out, not_38_out);
  and and_12 (and_12_out, not_39_out, not_40_out, not_41_out, not_42_out, not_43_out, not_44_out, not_45_out, not_46_out, not_47_out, not_48_out, not_49_out, not_50_out);
  and and_13 (and_13_out, not_51_out, not_52_out, not_53_out, not_54_out, not_55_out, not_56_out, not_57_out, not_58_out, not_59_out, not_60_out, F1, F0);
  and and_14 (and_14_out, not_61_out, not_62_out, not_63_out, not_64_out, not_65_out, not_66_out, not_67_out, not_68_out, not_69_out, not_70_out, F1, not_71_out);
  and and_15 (and_15_out, not_72_out, not_73_out, not_74_out, not_75_out, not_76_out, not_77_out, F5, not_78_out, not_79_out, not_80_out, not_81_out, not_82_out);
  and and_16 (and_16_out, not_83_out, not_84_out, not_85_out, not_86_out, not_87_out, not_88_out, F5, not_89_out, not_90_out, not_91_out, not_92_out, F0);
  and and_17 (and_17_out, not_93_out, not_94_out, not_95_out, not_96_out, not_97_out, not_98_out, F5, not_99_out, not_100_out, not_101_out, F1, not_102_out);
  and and_18 (and_18_out, not_103_out, not_104_out, not_105_out, not_106_out, not_107_out, not_108_out, F5, not_109_out, not_110_out, F2, not_111_out, not_112_out);
  and and_19 (and_19_out, not_113_out, not_114_out, not_115_out, not_116_out, not_117_out, not_118_out, F5, not_119_out, not_120_out, F2, not_121_out, F0);
  and and_20 (and_20_out, not_122_out, not_123_out, not_124_out, not_125_out, not_126_out, not_127_out, F5, not_128_out, not_129_out, F2, F1, F0);
  and and_21 (and_21_out, not_130_out, not_131_out, not_132_out, not_133_out, not_134_out, not_135_out, F5, not_136_out, F3, not_137_out, F1, not_138_out);
  and and_22 (and_22_out, not_139_out, not_140_out, not_141_out, not_142_out, not_143_out, not_144_out, F5, not_145_out, F3, not_146_out, F1, F0);
  and and_23 (and_23_out, not_147_out, not_148_out, not_149_out, not_150_out, OP1, OP0);
  and and_24 (and_24_out, not_151_out, not_152_out, OP3, not_153_out, not_154_out, not_155_out);
  and and_25 (and_25_out, not_156_out, not_157_out, OP3, OP2, not_158_out, not_159_out);
  and and_26 (and_26_out, not_160_out, not_161_out, OP3, not_162_out, not_163_out, OP0);
  and and_27 (and_27_out, not_164_out, not_165_out, OP3, not_166_out, OP1, not_167_out);
  and and_28 (and_28_out, not_168_out, not_169_out, OP3, OP2, not_170_out, OP0);
  and and_29 (and_29_out, OP5, not_171_out, not_172_out, not_173_out, OP1, OP0);
  and and_30 (and_30_out, not_174_out, not_175_out, not_176_out, not_177_out, not_178_out, not_179_out, not_180_out, F4, not_181_out, not_182_out, F1, not_183_out);
  and and_31 (and_31_out, OP5, not_184_out, not_185_out, OP2, not_186_out, not_187_out);
  and and_32 (SysCALL, not_188_out, not_189_out, not_190_out, not_191_out, not_192_out, not_193_out, not_194_out, not_195_out, F3, F2, not_196_out, not_197_out);
  and and_33 (and_33_out, not_198_out, not_199_out, not_200_out, OP2, not_201_out, not_202_out);
  and and_34 (and_34_out, not_203_out, not_204_out, not_205_out, OP2, not_206_out, OP0);
  and and_35 (and_35_out, not_207_out, not_208_out, OP3, not_209_out, not_210_out, not_211_out);
  and and_36 (and_36_out, not_212_out, not_213_out, OP3, not_214_out, not_215_out, OP0);
  and and_37 (and_37_out, not_216_out, not_217_out, OP3, not_218_out, OP1, not_219_out);
  and and_38 (and_38_out, OP5, not_220_out, not_221_out, not_222_out, OP1, OP0);
  and and_39 (and_39_out, OP5, not_223_out, OP3, not_224_out, OP1, OP0);
  and and_40 (and_40_out, OP5, not_225_out, not_226_out, OP2, not_227_out, not_228_out);
  and and_41 (and_41_out, not_229_out, not_230_out, not_231_out, OP2, OP1, OP0);
  and and_42 (and_42_out, not_232_out, not_233_out, not_234_out, not_235_out, not_236_out, not_237_out, not_238_out, not_239_out, not_240_out, not_241_out, not_242_out, not_243_out);
  and and_43 (and_43_out, not_244_out, not_245_out, not_246_out, not_247_out, not_248_out, not_249_out, not_250_out, not_251_out, not_252_out, not_253_out, F1, F0);
  and and_44 (and_44_out, not_254_out, not_255_out, not_256_out, not_257_out, not_258_out, not_259_out, not_260_out, not_261_out, not_262_out, not_263_out, F1, not_264_out);
  and and_45 (and_45_out, not_265_out, not_266_out, not_267_out, not_268_out, not_269_out, not_270_out, F5, not_271_out, not_272_out, not_273_out, not_274_out, not_275_out);
  and and_46 (and_46_out, not_276_out, not_277_out, not_278_out, not_279_out, not_280_out, not_281_out, F5, not_282_out, not_283_out, not_284_out, not_285_out, F0);
  and and_47 (and_47_out, not_286_out, not_287_out, not_288_out, not_289_out, not_290_out, not_291_out, F5, not_292_out, not_293_out, not_294_out, F1, not_295_out);
  and and_48 (and_48_out, not_296_out, not_297_out, not_298_out, not_299_out, not_300_out, not_301_out, F5, not_302_out, not_303_out, F2, not_304_out, not_305_out);
  and and_49 (and_49_out, not_306_out, not_307_out, not_308_out, not_309_out, not_310_out, not_311_out, F5, not_312_out, not_313_out, F2, not_314_out, F0);
  and and_50 (and_50_out, not_315_out, not_316_out, not_317_out, not_318_out, not_319_out, not_320_out, F5, not_321_out, not_322_out, F2, F1, F0);
  and and_51 (and_51_out, not_323_out, not_324_out, not_325_out, not_326_out, not_327_out, not_328_out, F5, not_329_out, F3, not_330_out, F1, not_331_out);
  and and_52 (and_52_out, not_332_out, not_333_out, not_334_out, not_335_out, not_336_out, not_337_out, F5, not_338_out, F3, not_339_out, F1, F0);
  and and_53 (BEQ, not_340_out, not_341_out, not_342_out, OP2, not_343_out, not_344_out);
  and and_54 (BNE, not_345_out, not_346_out, not_347_out, OP2, not_348_out, OP0);
  and and_55 (JR, not_349_out, not_350_out, not_351_out, not_352_out, not_353_out, not_354_out, not_355_out, not_356_out, F3, not_357_out, not_358_out, not_359_out);
  and and_56 (and_56_out, not_360_out, not_361_out, not_362_out, not_363_out, not_364_out, not_365_out, not_366_out, not_367_out, F3, not_368_out, not_369_out, not_370_out);
  and and_57 (and_57_out, not_371_out, not_372_out, not_373_out, not_374_out, OP1, not_375_out);
  and and_58 (and_58_out, not_376_out, not_377_out, not_378_out, not_379_out, OP1, OP0);
  and and_59 (JAL, not_380_out, not_381_out, not_382_out, not_383_out, OP1, OP0);
  and and_60 (DIVU, not_384_out, not_385_out, not_386_out, not_387_out, not_388_out, not_389_out, not_390_out, F4, F3, not_391_out, F1, F0);
  and and_61 (MFLO, not_392_out, not_393_out, not_394_out, not_395_out, not_396_out, not_397_out, not_398_out, F4, not_399_out, not_400_out, F1, not_401_out);
  and and_62 (LBU, OP5, not_402_out, not_403_out, OP2, not_404_out, not_405_out);
  and and_63 (BGTZ, not_406_out, not_407_out, not_408_out, OP2, OP1, OP0);
  and and_64 (and_64_out, not_409_out, not_410_out, not_411_out, not_412_out, not_413_out, not_414_out, not_415_out, not_416_out, not_417_out, not_418_out, not_419_out, not_420_out);
  and and_65 (and_65_out, not_421_out, not_422_out, not_423_out, not_424_out, not_425_out, not_426_out, not_427_out, not_428_out, not_429_out, not_430_out, F1, F0);
  and and_66 (and_66_out, not_431_out, not_432_out, not_433_out, not_434_out, not_435_out, not_436_out, not_437_out, not_438_out, not_439_out, not_440_out, F1, not_441_out);
  and and_67 (and_67_out, not_442_out, not_443_out, not_444_out, not_445_out, not_446_out, not_447_out, F5, not_448_out, not_449_out, not_450_out, not_451_out, not_452_out);
  and and_68 (and_68_out, not_453_out, not_454_out, not_455_out, not_456_out, not_457_out, not_458_out, F5, not_459_out, not_460_out, not_461_out, not_462_out, F0);
  and and_69 (and_69_out, not_463_out, not_464_out, not_465_out, not_466_out, not_467_out, not_468_out, F5, not_469_out, not_470_out, not_471_out, F1, not_472_out);
  and and_70 (and_70_out, not_473_out, not_474_out, not_475_out, not_476_out, not_477_out, not_478_out, F5, not_479_out, not_480_out, F2, not_481_out, not_482_out);
  and and_71 (and_71_out, not_483_out, not_484_out, not_485_out, not_486_out, not_487_out, not_488_out, F5, not_489_out, not_490_out, F2, not_491_out, F0);
  and and_72 (and_72_out, not_492_out, not_493_out, not_494_out, not_495_out, not_496_out, not_497_out, F5, not_498_out, not_499_out, F2, F1, F0);
  and and_73 (and_73_out, not_500_out, not_501_out, not_502_out, not_503_out, not_504_out, not_505_out, F5, not_506_out, F3, not_507_out, F1, not_508_out);
  and and_74 (and_74_out, not_509_out, not_510_out, not_511_out, not_512_out, not_513_out, not_514_out, F5, not_515_out, F3, not_516_out, F1, F0);
  and and_75 (and_75_out, not_517_out, not_518_out, not_519_out, not_520_out, not_521_out, not_522_out, not_523_out, not_524_out, F3, not_525_out, not_526_out, not_527_out);
  and and_76 (and_76_out, not_528_out, not_529_out, not_530_out, not_531_out, not_532_out, not_533_out, not_534_out, not_535_out, F3, F2, not_536_out, not_537_out);
  and and_77 (and_77_out, not_538_out, not_539_out, not_540_out, OP2, not_541_out, not_542_out);
  and and_78 (and_78_out, not_543_out, not_544_out, not_545_out, OP2, not_546_out, OP0);
  and and_79 (and_79_out, not_547_out, not_548_out, OP3, not_549_out, not_550_out, not_551_out);
  and and_80 (and_80_out, not_552_out, not_553_out, OP3, OP2, not_554_out, not_555_out);
  and and_81 (and_81_out, not_556_out, not_557_out, OP3, not_558_out, not_559_out, OP0);
  and and_82 (and_82_out, not_560_out, not_561_out, OP3, not_562_out, OP1, not_563_out);
  and and_83 (and_83_out, not_564_out, not_565_out, OP3, OP2, not_566_out, OP0);
  and and_84 (and_84_out, OP5, not_567_out, not_568_out, not_569_out, OP1, OP0);
  and and_85 (and_85_out, OP5, not_570_out, OP3, not_571_out, OP1, OP0);
  and and_86 (and_86_out, not_572_out, not_573_out, not_574_out, not_575_out, not_576_out, not_577_out, not_578_out, F4, F3, not_579_out, F1, F0);
  and and_87 (and_87_out, OP5, not_580_out, not_581_out, OP2, not_582_out, not_583_out);
  and and_88 (and_88_out, not_584_out, not_585_out, not_586_out, OP2, OP1, OP0);
  and and_89 (and_89_out, not_587_out, not_588_out, not_589_out, not_590_out, not_591_out, not_592_out, not_593_out, not_594_out, not_595_out, not_596_out, not_597_out, not_598_out);
  and and_90 (and_90_out, not_599_out, not_600_out, not_601_out, not_602_out, not_603_out, not_604_out, not_605_out, not_606_out, not_607_out, not_608_out, F1, F0);
  and and_91 (and_91_out, not_609_out, not_610_out, not_611_out, not_612_out, not_613_out, not_614_out, not_615_out, not_616_out, not_617_out, not_618_out, F1, not_619_out);
  and and_92 (and_92_out, not_620_out, not_621_out, not_622_out, not_623_out, not_624_out, not_625_out, F5, not_626_out, not_627_out, not_628_out, not_629_out, not_630_out);
  and and_93 (and_93_out, not_631_out, not_632_out, not_633_out, not_634_out, not_635_out, not_636_out, F5, not_637_out, not_638_out, not_639_out, not_640_out, F0);
  and and_94 (and_94_out, not_641_out, not_642_out, not_643_out, not_644_out, not_645_out, not_646_out, F5, not_647_out, not_648_out, not_649_out, F1, not_650_out);
  and and_95 (and_95_out, not_651_out, not_652_out, not_653_out, not_654_out, not_655_out, not_656_out, F5, not_657_out, not_658_out, F2, not_659_out, not_660_out);
  and and_96 (and_96_out, not_661_out, not_662_out, not_663_out, not_664_out, not_665_out, not_666_out, F5, not_667_out, not_668_out, F2, not_669_out, F0);
  and and_97 (and_97_out, not_670_out, not_671_out, not_672_out, not_673_out, not_674_out, not_675_out, F5, not_676_out, not_677_out, F2, F1, F0);
  and and_98 (and_98_out, not_678_out, not_679_out, not_680_out, not_681_out, not_682_out, not_683_out, F5, not_684_out, F3, not_685_out, F1, not_686_out);
  and and_99 (and_99_out, not_687_out, not_688_out, not_689_out, not_690_out, not_691_out, not_692_out, F5, not_693_out, F3, not_694_out, F1, F0);
  and and_100 (and_100_out, not_695_out, not_696_out, not_697_out, not_698_out, not_699_out, not_700_out, not_701_out, not_702_out, F3, F2, not_703_out, not_704_out);
  and and_101 (and_101_out, not_705_out, not_706_out, not_707_out, OP2, not_708_out, not_709_out);
  and and_102 (and_102_out, not_710_out, not_711_out, not_712_out, OP2, not_713_out, OP0);
  and and_103 (and_103_out, OP5, not_714_out, OP3, not_715_out, OP1, OP0);
  and and_104 (and_104_out, not_716_out, not_717_out, not_718_out, not_719_out, not_720_out, not_721_out, not_722_out, F4, F3, not_723_out, F1, F0);
  or or_1 (MemToReg, and_1_out, and_2_out);
  or or_2 (ALU_SRC, and_4_out, and_5_out, and_6_out, and_7_out, and_8_out, and_9_out, and_10_out, and_11_out);
  or or_3 (SignedExt, and_33_out, and_34_out, and_35_out, and_36_out, and_37_out, and_38_out, and_39_out, and_40_out, and_41_out);
  or or_4 (RegDst, and_42_out, and_43_out, and_44_out, and_45_out, and_46_out, and_47_out, and_48_out, and_49_out, and_50_out, and_51_out, and_52_out);
  or or_5 (JUMP, and_56_out, and_57_out, and_58_out);
  or or_6 (RegWrite, and_12_out, and_13_out, and_14_out, and_15_out, and_16_out, and_17_out, and_18_out, and_19_out, and_20_out, and_21_out, and_22_out, and_23_out, and_24_out, and_25_out, and_26_out, and_27_out, and_28_out, and_29_out, and_30_out, and_31_out);
  or or_7 (R1_Used, and_64_out, and_65_out, and_66_out, and_67_out, and_68_out, and_69_out, and_70_out, and_71_out, and_72_out, and_73_out, and_74_out, and_75_out, and_76_out, and_77_out, and_78_out, and_79_out, and_80_out, and_81_out, and_82_out, and_83_out, and_84_out, and_85_out, and_86_out, and_87_out, and_88_out);
  or or_8 (R2_Used, and_89_out, and_90_out, and_91_out, and_92_out, and_93_out, and_94_out, and_95_out, and_96_out, and_97_out, and_98_out, and_99_out, and_100_out, and_101_out, and_102_out, and_103_out, and_104_out);
endmodule

// ALU
module MIPS_ALU (
  input  [4:0] shamt,
  input  [31:0] X,
  input  [31:0] Y,
  input  [3:0] AluOP,
  output Equal,
  output [31:0] Result,
  output [31:0] Result_2
);

  wire [0:0] comparator_1_lt, comparator_2_lt;
  wire [31:0] adder_1_out, AND_out, divider_1_out, divider_1_rem, multiplier_1_cout, multiplier_1_out,
       NOR_out, OR_out, shifter_1_out, shifter_2_out, shifter_3_out, subtractor_1_out, XOR_out;

  assign AND_out = X & Y;  // AND_Gate AND, 32 bits wide
  assign OR_out = X | Y;  // OR_Gate OR, 32 bits wide
  Shifter #(.width(32), .shift("ll")) shifter_1 (.in(Y), .\dist (shamt), .out(shifter_1_out));
  Shifter #(.width(32), .shift("ar")) shifter_2 (.in(Y), .\dist (shamt), .out(shifter_2_out));
  Shifter #(.width(32), .shift("lr")) shifter_3 (.in(Y), .\dist (shamt), .out(shifter_3_out));
  Multiplier #(.width(32)) multiplier_1 (.a(X), .b(Y), .out(multiplier_1_out), .cout(multiplier_1_cout));  // open: cin
  Divider #(.width(32)) divider_1 (.a(X), .b(Y), .out(divider_1_out), .rem(divider_1_rem));  // open: upper
  Adder #(.width(32)) adder_1 (.a(X), .b(Y), .out(adder_1_out));  // open: cin, cout
  Subtractor #(.width(32)) subtractor_1 (.a(X), .b(Y), .out(subtractor_1_out));  // open: bin, bout
  assign XOR_out = X ^ Y;  // XOR_Gate XOR, 32 bits wide
  assign NOR_out = ~(X | Y);  // NOR_Gate NOR, 32 bits wide
  Comparator #(.width(32), .mode("twosComplement")) comparator_1 (
    .a(X), .b(Y), .eq(Equal), .lt(comparator_1_lt[0]));  // open: gt
  Comparator #(.width(32), .mode("unsigned")) comparator_2 (.a(X), .b(Y), .lt(comparator_2_lt[0]));  // open: gt, eq
  Multiplexer #(.select(4), .width(32), .disabled("Z"), .enable("false")) multiplexer_1 (
    .in0(shifter_1_out), .in1(shifter_2_out), .in2(shifter_3_out), .in3(multiplier_1_out),
    .in4(divider_1_out), .in5(adder_1_out), .in6(subtractor_1_out), .in7(AND_out), .in8(OR_out),
    .in9(XOR_out), .in10(NOR_out), .in11({{31{1'b0}}, comparator_1_lt[0]}),
    .in12({{31{1'b0}}, comparator_2_lt[0]}), .in13({32{1'b0}}), .in14({32{1'b0}}), .in15({32{1'b0}}),
    .out(Result), .sel(AluOP));
  Multiplexer #(.select(4), .width(32), .disabled("Z"), .enable("false")) multiplexer_2 (
    .in0({32{1'b0}}), .in1({32{1'b0}}), .in2({32{1'b0}}), .in3(multiplier_1_cout), .in4(divider_1_rem),
    .in5({32{1'b0}}), .in6({32{1'b0}}), .in7({32{1'b0}}), .in8({32{1'b0}}), .in9({32{1'b0}}),
    .in10({32{1'b0}}), .in11({32{1'b0}}), .in12({32{1'b0}}), .in13({32{1'b0}}), .in14({32{1'b0}}),
    .in15({32{1'b0}}), .out(Result_2), .sel(AluOP));

  // Other names for the same wires on the sheet: Result2[31:0] = Result_2; S[3:0] = AluOP

  // Notes on the sheet:
  //   不要改变此引脚区域内容，也不要改变ALU封装形式
  //   输入引脚
  //   输出引脚
endmodule

module MIPS_Regifile (
  input  [31:0] Din,
  input  Clk,
  input  WE,
  input  [4:0] R1_num,
  input  [4:0] W_num,
  input  [4:0] R2_num,
  output [31:0] R1,
  output [31:0] R2
);

  // RegisterFile registerfile_1: pin names not known; wires that end beside it: Din, Clk, WE, W_num, R1_num, R2_num, R1, R2
endmodule

module \理想流水线  (
  output RegWrite,
  output MemWrite,
  output [31:0] IF_PC,
  output [31:0] ID_PC,
  output [31:0] EX_PC,
  output [31:0] M_PC,
  output [31:0] WB_PC,
  output [31:0] RDin,
  output [31:0] MDin,
  output [31:0] LedData
);

  wire AluSrc, and_1_out, and_3_out, BEQ, BNE, CLK, clock_1_out, clock_2_out, comparator_1_eq,
       comparator_1_lt, comparator_2_eq, d_ff_1_q, Equal, Go, Halt, IR1, IR2, IR3, mips_probe_6_p2,
       nand_1_out, not_1_out, not_2_out, PC_q, RST, W1, W2, W3;
  wire [3:0] AluOp;
  wire [4:0] EX_MEM_out_17, ID_EX_out_18, ID_EX_out_19, mem_wb_1_out_17, multiplexer_1_out,
       multiplexer_2_out, multiplexer_3_out, multiplexer_4_out;
  wire [12:0] CNT_num;
  wire [15:0] EX_MEM_out_13, ID_EX_out_14, \LoadUse次数 , mem_wb_1_out_13, \总周期数 , \插入气泡数 , \无条件分支数 , \条件分支成功数 ;
  wire [15:2] CRTL;
  wire [25:0] ADDR;
  wire [31:0] adder_1_out, adder_2_out, bit_extender_1_out, bit_extender_2_out, EX_IR, EX_MEM_out_14,
       EX_MEM_out_16, ID_EX_out_15, ID_EX_out_16, ID_EX_out_17, IF_IR, IMME32, MEM_IR, mem_wb_1_out_14,
       mem_wb_1_out_15, mem_wb_1_out_16, mips_regifile_1_r2, multiplexer_6_out, multiplexer_7_out, PC_JR,
       ram_1_data, Res1, WB_IR;
  wire [31:26] ID_IR;

  Button \u_总复位  (.out(RST));
  Button _1 (.out(IR1));
  Button _2 (.out(IR2));
  Button _3 (.out(IR3));
  // Probe on \总周期数 
  // Probe on \总周期数 
  Button \u_继续运行  (.out(Go));
  LED #(.active("true")) led_1 (.in(W1));
  LED #(.active("true")) led_2 (.in(W2));
  LED #(.active("true")) led_3 (.in(W3));
  Adder #(.width(32)) adder_1 (.a(IF_PC), .b(32'h4), .out(adder_1_out));  // open: cin, cout
  Register #(.width(1), .trigger("rising"), .Select("low")) PC (
    .D(Halt), .en(not_1_out), .Q(PC_q), .clk(CLK));  // open: clr
  not not_1 (not_1_out, PC_q);
  Hex_Digit_Display hex_digit_display_1 (.value(LedData[31:28]));  // open: dp
  // Probe on IF_PC[19:0]
  // Mips_Probe mips_probe_1: pin names not known; wires that end beside it: IF_IR
  Hex_Digit_Display hex_digit_display_2 (.value(LedData[23:20]));  // open: dp
  Hex_Digit_Display hex_digit_display_3 (.value(LedData[27:24]));  // open: dp
  // Probe on ID_PC[19:0]
  // Mips_Probe mips_probe_2: pin names not known; wires that end beside it: {ID_IR, ADDR}
  Register #(.width(32), .trigger("rising"), .Select("low")) PC_2 (
    .D(adder_1_out), .en(not_1_out), .Q(IF_PC), .clk(CLK));  // open: clr
  Counter #(.width(16), .max('hffff), .ongoal("wrap"), .trigger("rising"), .behavior("new")) counter_1 (
    .Q(\总周期数 ), .clk(and_1_out));  // open: load, D, count, carry, clr, preset, down
  and and_1 (and_1_out, CLK, not_1_out);
  Hex_Digit_Display hex_digit_display_4 (.value(LedData[19:16]));  // open: dp
  Hex_Digit_Display hex_digit_display_5 (.value(LedData[15:12]));  // open: dp
  Hex_Digit_Display hex_digit_display_6 (.value(LedData[7:4]));  // open: dp
  Hex_Digit_Display hex_digit_display_7 (.value(LedData[11:8]));  // open: dp
  Clock #(.highDuration(1), .lowDuration(1)) clock_1 (.out(clock_1_out));
  // Probe on EX_PC[19:0]
  // Mips_Probe mips_probe_3: pin names not known; wires that end beside it: clock_1_out, EX_IR, CLK
  ROM #(.addrWidth(10), .dataWidth(32), .Select("high")) rom_1 (.addr(IF_PC[11:2]), .data(IF_IR));
  Hex_Digit_Display hex_digit_display_8 (.value(LedData[3:0]));  // open: dp
  // Mips_Probe mips_probe_4: pin names not known; wires that end beside it: IF_IR
  // Probe on \总周期数 
  // Probe on M_PC[19:0]
  // Mips_Probe mips_probe_5: pin names not known; wires that end beside it: MEM_IR
  IF_ID IF_ID (
    .PC(IF_PC), .IR(IF_IR), .PC_2(ID_PC), .IR_2({ID_IR, ADDR}), .CLK(CLK), .SYNC_RESET(RST), .\使能 (not_1_out));
  // Probe on \总周期数 
  // Probe on \无条件分支数 
  // Probe on \条件分支成功数 
  // Probe on \插入气泡数 
  // Probe on \LoadUse次数 
  // Probe on IF_PC[11:0]
  // Probe on WB_PC[19:0]
  // Mips_Probe mips_probe_6: pin names not known; wires that end beside it: WB_IR, mips_probe_6_p2, mips_probe_6_p2
  // Probe on EX_PC[11:0]
  // Probe on ID_PC[11:0]
  // Probe on M_PC[11:0]
  D_Flip_Flop #(.trigger("high"), .Pre_Clr_Positions("LEGACY"), .NegatePresetClear("false"), .enable("true"), .NewFFLayout("false")) d_ff_1 (.Q(d_ff_1_q));  // open: clk, D, Qn, preset, en, reset
  // Probe on 13'hc
  \单周期硬布线控制器  \u_单周期硬布线控制器_1  (
    .Func(ADDR[5:0]), .OP(ID_IR), .ALU_OP(AluOp), .MemToReg(CRTL[2]), .MemWrite(CRTL[3]), .ALU_SRC(AluSrc),
    .RegWrite(CRTL[9]), .SysCALL(CRTL[12]), .SignedExt(CRTL[15]), .RegDst(CRTL[11]), .JR(CRTL[14]),
    .JMP(CRTL[13]), .Beq(BEQ), .JAL(CRTL[10]), .Bne(BNE));  // open: DIVU, MFLO, LBU, BGTZ, R1_Used, R2_Used
  // Probe on WB_PC[11:0]
  Comparator #(.width(13), .mode("twosComplement")) comparator_1 (
    .a(CNT_num), .b(13'hc), .eq(comparator_1_eq), .lt(comparator_1_lt));  // open: gt
  Clock #(.highDuration(1), .lowDuration(1)) clock_2 (.out(clock_2_out));
  nand nand_1 (nand_1_out, d_ff_1_q, comparator_1_eq);
  Counter #(.width(13), .max('h1fff), .ongoal("stay"), .trigger("rising"), .behavior("old")) counter_2 (
    .count(comparator_1_lt), .Q(CNT_num), .clk(clock_2_out));  // open: load, D, carry, clr, preset
  assign CLK = nand_1_out ? clock_2_out : 1'bz;  // Controlled_Buffer controlled_buffer_1
  Multiplexer #(.select(1), .width(5), .disabled("Z"), .enable("false")) multiplexer_1 (
    .in0(ADDR[20:16]), .in1(ADDR[15:11]), .out(multiplexer_1_out), .sel(CRTL[11]));
  Pull_Resistor #(.pull(1)) pull_resistor_1 (.node(CLK));
  assign bit_extender_1_out = {{16{1'b0}}, ADDR[15:0]};  // Bit_Extender bit_extender_1
  assign bit_extender_2_out = {{16{ADDR[15]}}, ADDR[15:0]};  // Bit_Extender bit_extender_2
  Multiplexer #(.select(1), .width(5), .disabled("Z"), .enable("false")) multiplexer_2 (
    .in0(ADDR[25:21]), .in1(5'b00010), .out(multiplexer_2_out), .sel(CRTL[12]));
  Multiplexer #(.select(1), .width(5), .disabled("Z"), .enable("false")) multiplexer_3 (
    .in0(ADDR[20:16]), .in1(5'b00100), .out(multiplexer_3_out), .sel(CRTL[12]));
  Multiplexer #(.select(1), .width(5), .disabled("Z"), .enable("false")) multiplexer_4 (
    .in0(multiplexer_1_out), .in1({5{1'b1}}), .out(multiplexer_4_out), .sel(CRTL[10]));
  Multiplexer #(.select(1), .width(32), .disabled("Z"), .enable("false")) multiplexer_5 (
    .in0(bit_extender_1_out), .in1(bit_extender_2_out), .out(IMME32), .sel(CRTL[15]));
  MIPS_Regifile mips_regifile_1 (
    .Din(RDin), .Clk(CLK), .R1(PC_JR), .R2(mips_regifile_1_r2), .WE(RegWrite), .W_num(mem_wb_1_out_17),
    .R1_num(multiplexer_2_out), .R2_num(multiplexer_3_out));
  ID_EX ID_EX (
    .PC(ID_PC), .IR({ID_IR, ADDR}), .CTRL({CRTL[15:9], AluSrc, AluOp, CRTL[3:2], BNE, BEQ}), .R1(PC_JR),
    .R2(mips_regifile_1_r2), .IMME(IMME32), .SHAMT(ADDR[10:6]), .WB(multiplexer_4_out), .out_12(EX_PC),
    .out_13(EX_IR), .out_14(ID_EX_out_14), .out_15(ID_EX_out_15), .out_16(ID_EX_out_16),
    .out_17(ID_EX_out_17), .out_18(ID_EX_out_18), .out_19(ID_EX_out_19), .SYNC_RESET(RST), .\使能 (not_1_out),
    .CLK(CLK));
  Multiplexer #(.select(1), .width(32), .disabled("Z"), .enable("false")) multiplexer_6 (
    .in0(ID_EX_out_16), .in1(ID_EX_out_17), .out(multiplexer_6_out), .sel(ID_EX_out_14[8]));
  MIPS_ALU mips_alu_1 (
    .X(ID_EX_out_15), .Y(multiplexer_6_out), .AluOP(ID_EX_out_14[7:4]), .Equal(Equal), .Result(Res1),
    .shamt(ID_EX_out_18));  // open: Result_2
  EX_MEM EX_MEM (
    .PC(EX_PC), .IR(EX_IR), .CTRL(ID_EX_out_14), .Res1(Res1), .MDin(ID_EX_out_16), .WB(ID_EX_out_19),
    .out_11(M_PC), .out_12(MEM_IR), .out_13({EX_MEM_out_13[15:4], MemWrite, EX_MEM_out_13[2:0]}),
    .out_14(EX_MEM_out_14), .out_15(MDin), .out_17(EX_MEM_out_17), .SYNC_RESET(RST), .\使能 (not_1_out),
    .CLK(CLK), .R1(ID_EX_out_15), .out_16(EX_MEM_out_16));
  RAM #(.addrWidth(10), .dataWidth(32), .bus("separate"), .Select("high")) ram_1 (
    .addr(EX_MEM_out_14[11:2]), .din(MDin), .data(ram_1_data), .str(MemWrite), .clk(CLK));  // open: sel, ld, clr
  Multiplexer #(.select(1), .width(32), .disabled("Z"), .enable("false")) multiplexer_7 (
    .in0(EX_MEM_out_14), .in1(ram_1_data), .out(multiplexer_7_out), .sel(EX_MEM_out_13[2]));
  MEM_WB mem_wb_1 (
    .PC(M_PC), .IR(MEM_IR), .CTRL({EX_MEM_out_13[15:4], MemWrite, EX_MEM_out_13[2:0]}),
    .MDin(multiplexer_7_out), .WB(EX_MEM_out_17), .out_11(WB_PC), .out_12(WB_IR),
    .out_13({mem_wb_1_out_13[15:10], RegWrite, mem_wb_1_out_13[8:0]}), .out_14(mem_wb_1_out_14),
    .out_17(mem_wb_1_out_17), .SYNC_RESET(RST), .\使能 (not_1_out), .CLK(CLK), .R1(EX_MEM_out_16),
    .out_15(mem_wb_1_out_15), .R2(MDin), .out_16(mem_wb_1_out_16));
  Comparator #(.width(32), .mode("twosComplement")) comparator_2 (
    .a(mem_wb_1_out_15), .b(32'ha), .eq(comparator_2_eq));  // open: gt, lt
  and and_2 (Halt, mem_wb_1_out_13[12], comparator_2_eq);
  not not_2 (not_2_out, comparator_2_eq);
  and and_3 (and_3_out, not_2_out, mem_wb_1_out_13[12]);
  Counter #(.width(32), .max('hffffffff), .ongoal("wrap"), .trigger("rising"), .behavior("old")) counter_3 (
    .load(and_3_out), .D(mem_wb_1_out_16), .count(1'b0), .Q(LedData), .clk(CLK));  // open: carry, clr, preset
  Multiplexer #(.select(1), .width(32), .disabled("Z"), .enable("false")) multiplexer_8 (
    .in0(mem_wb_1_out_14), .in1(adder_2_out), .out(RDin), .sel(mem_wb_1_out_13[10]));
  Adder #(.width(32)) adder_2 (.a(WB_PC), .b(32'h4), .out(adder_2_out));  // open: cin, cout

  // Other names for the same wires on the sheet: CRTL (some bits) = {AluSrc, AluOp, BNE, BEQ}; MemToReg = CRTL[2];
  //   JAL = CRTL[10]; RegDst = CRTL[11]; SysCall = CRTL[12]; JMP = CRTL[13]; JR = CRTL[14]; SignedExt = CRTL[15];
  //   ID_IR[25:0] = ADDR; IMME[15:0] = ADDR[15:0]; SHAMT[4:0] = ADDR[10:6]; RD[4:0] = ADDR[15:11];
  //   RT[4:0] = ADDR[20:16]; RS[4:0] = ADDR[25:21]; IR[31:0] = IF_IR; MEM_PC[31:0] = M_PC; PC[31:0] = IF_PC

  // Notes on the sheet:
  //   中断源
  //   时空图监测，可删除
  //   中断等待指示
  //   数码管输出
  //   指令存储器
  //   contents of rom_1 (hex, n*v repeats v):
  //   20100000 20110000 20120000 20130000 36100000 36310001 36520002 36730003 ae100000 ae110004 ae120008
  //   ae13000c 2002000a 20110000 20120000 20130000 c
  //   指令字
  //   控制位
  //   流水调试日志用
  //   暂停节拍，不能为0
  //   JMP
  //   JR
  //   戳工具置1进入计数暂停模式，ctrl+k时钟自动运行到对应节拍暂停
  //   ctrl+k关闭时钟连续运行，将控制位置零，进入单步调试模式调试
  //   用这个时钟源需要去掉电路中的其他时钟源
  //   可计数暂停的时钟源
  //   为方便自动评测，需要输出流水线各段保存的PC值，注意是PC不是PC+4，另外ID段寄存器写入信息，Mem段内存写入信息也要输出
endmodule
module \气泡流水线  (
  output RegWrite,
  output MemWrite,
  output [31:0] IF_PC,
  output [31:0] ID_PC,
  output [31:0] EX_PC,
  output [31:0] M_PC,
  output [31:0] WB_PC,
  output [31:0] RDin,
  output [31:0] MDin,
  output [31:0] LedData
);

  wire AluSrc, and_1_out, and_2_out, and_3_out, and_4_out, and_5_out, and_6_out, and_7_out, and_8_out,
       and_9_out, and_10_out, and_11_out, and_13_out, BEQ, BGTZ, BNE, CLK, clock_1_out, clock_2_out,
       comparator_1_eq, comparator_2_eq, comparator_3_eq, comparator_4_eq, comparator_5_eq, comparator_6_eq,
       comparator_7_eq, comparator_8_eq, comparator_9_eq, comparator_9_lt, comparator_10_gt,
       comparator_12_eq, d_ff_1_q, Equal, EX_RegWrite, Go, Halt, IR1, IR2, IR3, JMP, JMP_IF, JR,
       MEM_RegWrite, nand_1_out, NeedJmp, not_1_out, not_2_out, not_3_out, not_4_out, not_5_out, not_6_out,
       not_7_out, not_8_out, not_9_out, or_1_out, or_2_out, or_4_out, PC_q, Reg_Related, RST, W1, W2, W3;
  wire [3:0] AluOp;
  wire [4:0] EX_RegWrite_num, \id_ex气泡_1_out_21 , ID_R1_num, ID_R2_num, MEM_RegWrite_num,
       \mem_wb气泡_1_out_18 , multiplexer_1_out, multiplexer_2_out, multiplexer_4_out, multiplexer_7_out;
  wire [12:0] CNT_num;
  wire [15:0] \LoadUse次数 , \总周期数 , \插入气泡数 , \无条件分支数 , \条件分支成功数 ;
  wire [21:0] CRTL, \ex_mem气泡_1_out_14 , \mem_wb气泡_1_out_15 ;
  wire [21:2] \id_ex气泡_1_out_17 ;
  wire [25:0] ADDR;
  wire [27:0] PC_4;
  wire [31:0] adder_1_out, adder_4_out, bit_extender_1_out, bit_extender_2_out, EX_IR, \ex_mem气泡_1_out_15 ,
       \ex_mem气泡_1_out_18 , \id_ex气泡_1_out_19 , ID_IR, IF_IR, IMME32, IMME32_EX, MEM_IR, \mem_wb气泡_1_out_16 ,
       \mem_wb气泡_1_out_17 , \mem_wb气泡_1_out_19 , \mem_wb气泡_1_out_20 , mips_regifile_1_r1, mips_regifile_1_r2,
       multiplexer_3_out, multiplexer_9_out, multiplexer_11_out, PC_4_IMME, PC_Next, R1, ram_1_data, Res1,
       shifter_1_out, WB_IR;
  wire [31:28] JmpPc;

  Button \u_总复位  (.out(RST));
  Button _1 (.out(IR1));
  Button _2 (.out(IR2));
  Button _3 (.out(IR3));
  // Probe on \总周期数 
  // Probe on \总周期数 
  Button \u_继续运行  (.out(Go));
  LED #(.active("true")) led_1 (.in(W1));
  LED #(.active("true")) led_2 (.in(W2));
  LED #(.active("true")) led_3 (.in(W3));
  Multiplexer #(.select(1), .width(5), .disabled("Z"), .enable("false")) multiplexer_1 (
    .in0({5{1'b0}}), .in1(ID_R1_num), .out(multiplexer_1_out), .sel(CRTL[20]));
  Multiplexer #(.select(1), .width(5), .disabled("Z"), .enable("false")) multiplexer_2 (
    .in0({5{1'b0}}), .in1(ID_R2_num), .out(multiplexer_2_out), .sel(CRTL[21]));
  Hex_Digit_Display hex_digit_display_1 (.value(LedData[31:28]));  // open: dp
  // Probe on IF_PC[19:0]
  // Mips_Probe mips_probe_1: pin names not known; wires that end beside it: IF_IR
  Adder #(.width(32)) adder_1 (.a(IF_PC), .b(32'h4), .out(adder_1_out));  // open: cin, cout
  Hex_Digit_Display hex_digit_display_2 (.value(LedData[27:24]));  // open: dp
  Hex_Digit_Display hex_digit_display_3 (.value(LedData[23:20]));  // open: dp
  // Probe on ID_PC[19:0]
  // Mips_Probe mips_probe_2: pin names not known; wires that end beside it: ID_IR
  Comparator #(.width(5), .mode("twosComplement")) comparator_1 (
    .a(multiplexer_1_out), .b(EX_RegWrite_num), .eq(comparator_1_eq));  // open: gt, lt
  Comparator #(.width(5), .mode("twosComplement")) comparator_2 (
    .a(multiplexer_1_out), .b(MEM_RegWrite_num), .eq(comparator_2_eq));  // open: gt, lt
  Comparator #(.width(5), .mode("twosComplement")) comparator_3 (
    .a(multiplexer_2_out), .b(EX_RegWrite_num), .eq(comparator_3_eq));  // open: gt, lt
  Comparator #(.width(5), .mode("twosComplement")) comparator_4 (
    .a(multiplexer_2_out), .b(MEM_RegWrite_num), .eq(comparator_4_eq));  // open: gt, lt
  Multiplexer #(.select(1), .width(32), .disabled("Z"), .enable("false")) multiplexer_3 (
    .in0(adder_1_out), .in1(PC_Next), .out(multiplexer_3_out), .sel(NeedJmp));
  Register #(.width(1), .trigger("rising"), .Select("low")) PC (
    .D(Halt), .en(not_1_out), .Q(PC_q), .clk(CLK));  // open: clr
  not not_1 (not_1_out, PC_q);
  Hex_Digit_Display hex_digit_display_4 (.value(LedData[19:16]));  // open: dp
  Hex_Digit_Display hex_digit_display_5 (.value(LedData[15:12]));  // open: dp
  Comparator #(.width(5), .mode("twosComplement")) comparator_5 (
    .a(multiplexer_1_out), .b({5{1'b0}}), .eq(comparator_5_eq));  // open: gt, lt
  Comparator #(.width(5), .mode("twosComplement")) comparator_6 (
    .a(multiplexer_1_out), .b({5{1'b0}}), .eq(comparator_6_eq));  // open: gt, lt
  Comparator #(.width(5), .mode("twosComplement")) comparator_7 (
    .a(multiplexer_2_out), .b({5{1'b0}}), .eq(comparator_7_eq));  // open: gt, lt
  Comparator #(.width(5), .mode("twosComplement")) comparator_8 (
    .a(multiplexer_2_out), .b({5{1'b0}}), .eq(comparator_8_eq));  // open: gt, lt
  and and_1 (and_1_out, not_1_out, not_2_out);
  not not_2 (not_2_out, Reg_Related);
  Hex_Digit_Display hex_digit_display_6 (.value(LedData[11:8]));  // open: dp
  Hex_Digit_Display hex_digit_display_7 (.value(LedData[7:4]));  // open: dp
  Clock #(.highDuration(1), .lowDuration(1)) clock_1 (.out(clock_1_out));
  // Probe on EX_PC[19:0]
  // Mips_Probe mips_probe_3: pin names not known; wires that end beside it: clock_1_out, CLK, EX_IR
  not not_3 (not_3_out, comparator_5_eq);
  and and_2 (and_2_out, not_3_out, comparator_1_eq);
  not not_4 (not_4_out, comparator_6_eq);
  and and_3 (and_3_out, not_4_out, comparator_2_eq);
  not not_5 (not_5_out, comparator_7_eq);
  and and_4 (and_4_out, not_5_out, comparator_3_eq);
  not not_6 (not_6_out, comparator_8_eq);
  and and_5 (and_5_out, not_6_out, comparator_4_eq);
  Register #(.width(32), .trigger("rising"), .Select("low")) PC_2 (
    .D(multiplexer_3_out), .en(and_1_out), .Q(IF_PC), .clk(CLK));  // open: clr
  and and_6 (and_6_out, CLK, not_1_out);
  Hex_Digit_Display hex_digit_display_8 (.value(LedData[3:0]));  // open: dp
  or or_1 (or_1_out, and_2_out, and_4_out);
  or or_2 (or_2_out, and_3_out, and_5_out);
  Counter #(.width(16), .max('hffff), .ongoal("wrap"), .trigger("rising"), .behavior("new")) counter_1 (
    .Q(\总周期数 ), .clk(and_6_out));  // open: load, D, count, carry, clr, preset, down
  // Probe on \总周期数 
  // Probe on M_PC[19:0]
  // Mips_Probe mips_probe_4: pin names not known; wires that end beside it: MEM_IR
  ROM #(.addrWidth(10), .dataWidth(32), .Select("high")) rom_1 (.addr(IF_PC[11:2]), .data(IF_IR));
  // Probe on \总周期数 
  // Probe on \无条件分支数 
  // Probe on \条件分支成功数 
  // Probe on \插入气泡数 
  // Probe on \LoadUse次数 
  and and_7 (and_7_out, or_1_out, EX_RegWrite);
  and and_8 (and_8_out, or_2_out, MEM_RegWrite);
  // Mips_Probe mips_probe_5: pin names not known; wires that end beside it: IF_IR, CRTL[21]
  // Probe on IF_PC[11:0]
  // Probe on WB_PC[19:0]
  // Mips_Probe mips_probe_6: pin names not known; wires that end beside it: WB_IR
  or or_3 (Reg_Related, and_7_out, and_8_out);
  \IF_ID气泡  \if_id气泡_1  (
    .PC(IF_PC), .IR(IF_IR), .PC_2(ID_PC), .IR_2(ID_IR), .SYNC_RESET(NeedJmp), .\使能 (not_7_out), .CLK(CLK));
  not not_7 (not_7_out, Reg_Related);
  // Probe on ID_PC[11:0]
  // Probe on EX_PC[11:0]
  // Probe on M_PC[11:0]
  D_Flip_Flop #(.trigger("high"), .Pre_Clr_Positions("LEGACY"), .NegatePresetClear("false"), .enable("true"), .NewFFLayout("false")) d_ff_1 (.Q(d_ff_1_q));  // open: clk, D, Qn, preset, en, reset
  // Probe on 13'he24
  // Probe on WB_PC[11:0]
  Comparator #(.width(13), .mode("twosComplement")) comparator_9 (
    .a(CNT_num), .b(13'he24), .eq(comparator_9_eq), .lt(comparator_9_lt));  // open: gt
  Clock #(.highDuration(1), .lowDuration(1)) clock_2 (.out(clock_2_out));
  nand nand_1 (nand_1_out, d_ff_1_q, comparator_9_eq);
  Counter #(.width(13), .max('h1fff), .ongoal("stay"), .trigger("rising"), .behavior("old")) counter_2 (
    .count(comparator_9_lt), .Q(CNT_num), .clk(clock_2_out));  // open: load, D, carry, clr, preset
  \单周期硬布线控制器  \u_单周期硬布线控制器_1  (
    .Func(ID_IR[5:0]), .OP(ID_IR[31:26]), .ALU_OP(AluOp), .MemToReg(CRTL[2]), .MemWrite(CRTL[3]),
    .ALU_SRC(AluSrc), .RegWrite(CRTL[9]), .SysCALL(CRTL[12]), .SignedExt(CRTL[15]), .RegDst(CRTL[11]),
    .JR(CRTL[14]), .JMP(CRTL[13]), .Beq(CRTL[0]), .JAL(CRTL[10]), .Bne(CRTL[1]), .DIVU(CRTL[16]),
    .MFLO(CRTL[17]), .LBU(CRTL[18]), .BGTZ(CRTL[19]), .R1_Used(CRTL[20]), .R2_Used(CRTL[21]));
  assign CLK = nand_1_out ? clock_2_out : 1'bz;  // Controlled_Buffer controlled_buffer_1
  Pull_Resistor #(.pull(1)) pull_resistor_1 (.node(CLK));
  Multiplexer #(.select(1), .width(5), .disabled("Z"), .enable("false")) multiplexer_4 (
    .in0(ID_IR[20:16]), .in1(ID_IR[15:11]), .out(multiplexer_4_out), .sel(CRTL[11]));
  assign bit_extender_1_out = {{16{1'b0}}, ID_IR[15:0]};  // Bit_Extender bit_extender_1
  assign bit_extender_2_out = {{16{ID_IR[15]}}, ID_IR[15:0]};  // Bit_Extender bit_extender_2
  Multiplexer #(.select(1), .width(5), .disabled("Z"), .enable("false")) multiplexer_5 (
    .in0(ID_IR[25:21]), .in1(5'b00010), .out(ID_R1_num), .sel(CRTL[12]));
  Multiplexer #(.select(1), .width(5), .disabled("Z"), .enable("false")) multiplexer_6 (
    .in0(ID_IR[20:16]), .in1(5'b00100), .out(ID_R2_num), .sel(CRTL[12]));
  Multiplexer #(.select(1), .width(5), .disabled("Z"), .enable("false")) multiplexer_7 (
    .in0(multiplexer_4_out), .in1({5{1'b1}}), .out(multiplexer_7_out), .sel(CRTL[10]));
  Multiplexer #(.select(1), .width(32), .disabled("Z"), .enable("false")) multiplexer_8 (
    .in0(bit_extender_1_out), .in1(bit_extender_2_out), .out(IMME32), .sel(CRTL[15]));
  MIPS_Regifile mips_regifile_1 (
    .Din(RDin), .Clk(CLK), .R1(mips_regifile_1_r1), .R2(mips_regifile_1_r2), .WE(RegWrite),
    .W_num(\mem_wb气泡_1_out_18 ), .R1_num(ID_R1_num), .R2_num(ID_R2_num));
  \ID_EX气泡  \id_ex气泡_1  (
    .PC(ID_PC), .IR(ID_IR), .CTRL({CRTL[21:9], AluSrc, AluOp, CRTL[3:0]}), .R1(mips_regifile_1_r1),
    .R2(mips_regifile_1_r2), .IMME(IMME32), .SHAMT(ID_IR[10:6]), .WB(multiplexer_7_out), .out_15(EX_PC),
    .out_16(EX_IR),
    .out_17({\id_ex气泡_1_out_17 [21:20], BGTZ, \id_ex气泡_1_out_17 [18:15], JR, JMP, \id_ex气泡_1_out_17 [12:10], EX_RegWrite, \id_ex气泡_1_out_17 [8:2], BNE, BEQ}),
    .out_18(R1), .out_19(\id_ex气泡_1_out_19 ), .out_20(IMME32_EX), .out_21(\id_ex气泡_1_out_21 ),
    .out_22(EX_RegWrite_num), .SYNC_RESET(or_4_out), .\使能 (not_1_out), .CLK(CLK), .ADDR(ID_IR[25:0]),
    .out_23(ADDR));  // open: R1_Fwd, out_24, R2_Fwd, out_25
  or or_4 (or_4_out, Reg_Related, NeedJmp);
  Shifter #(.width(32), .shift("ll")) shifter_1 (.in(IMME32_EX), .\dist (5'b00010), .out(shifter_1_out));
  and and_9 (and_9_out, BEQ, Equal);
  and and_10 (and_10_out, BNE, not_8_out);
  not not_8 (not_8_out, Equal);
  Comparator #(.width(32), .mode("twosComplement")) comparator_10 (
    .a(R1), .b({32{1'b0}}), .gt(comparator_10_gt));  // open: eq, lt
  Adder #(.width(32)) adder_2 (.a(EX_PC), .b(32'h4), .out({JmpPc, PC_4}));  // open: cin, cout
  Adder #(.width(32)) adder_3 (.a({JmpPc, PC_4}), .b(shifter_1_out), .out(PC_4_IMME));  // open: cin, cout
  or or_5 (JMP_IF, and_9_out, and_10_out, and_11_out);
  and and_11 (and_11_out, comparator_10_gt, BGTZ);
  Multiplexer #(.select(1), .width(32), .disabled("Z"), .enable("false")) multiplexer_9 (
    .in0(\id_ex气泡_1_out_19 ), .in1(IMME32_EX), .out(multiplexer_9_out), .sel(\id_ex气泡_1_out_17 [8]));
  MIPS_ALU mips_alu_1 (
    .X(R1), .Y(multiplexer_9_out), .AluOP(\id_ex气泡_1_out_17 [7:4]), .Equal(Equal), .Result(Res1),
    .shamt(\id_ex气泡_1_out_21 ));  // open: Result_2
  Multiplexer #(.select(3), .width(32), .disabled("Z"), .enable("false")) multiplexer_10 (
    .in0({JmpPc, PC_4}), .in1(PC_4_IMME), .in2({JmpPc, ADDR, 2'b00}), .in6(R1), .out(PC_Next),
    .sel({JR, JMP, JMP_IF}));  // open: in3, in4, in5, in7
  Comparator #(.width(3), .mode("unsigned")) comparator_11 (
    .a({JR, JMP, JMP_IF}), .b(3'b000), .gt(NeedJmp));  // open: eq, lt
  \EX_MEM气泡  \ex_mem气泡_1  (
    .PC(EX_PC), .IR(EX_IR),
    .CTRL({\id_ex气泡_1_out_17 [21:20], BGTZ, \id_ex气泡_1_out_17 [18:15], JR, JMP, \id_ex气泡_1_out_17 [12:10], EX_RegWrite, \id_ex气泡_1_out_17 [8:2], BNE, BEQ}),
    .Res1(Res1), .MDin(\id_ex气泡_1_out_19 ), .R1(R1), .WB(EX_RegWrite_num), .out_12(M_PC), .out_13(MEM_IR),
    .out_14({\ex_mem气泡_1_out_14 [21:10], MEM_RegWrite, \ex_mem气泡_1_out_14 [8:4], MemWrite, \ex_mem气泡_1_out_14 [2:0]}),
    .out_15(\ex_mem气泡_1_out_15 ), .out_17(MDin), .out_18(\ex_mem气泡_1_out_18 ), .out_19(MEM_RegWrite_num),
    .SYNC_RESET(1'b0), .\使能 (not_1_out), .CLK(CLK));  // open: Res2, out_16
  RAM #(.addrWidth(10), .dataWidth(32), .bus("separate"), .Select("high")) ram_1 (
    .addr(\ex_mem气泡_1_out_15 [11:2]), .din(MDin), .data(ram_1_data), .str(MemWrite), .clk(CLK));  // open: sel, ld, clr
  \MEM_WB气泡  \mem_wb气泡_1  (
    .PC(M_PC), .IR(MEM_IR),
    .CTRL({\ex_mem气泡_1_out_14 [21:10], MEM_RegWrite, \ex_mem气泡_1_out_14 [8:4], MemWrite, \ex_mem气泡_1_out_14 [2:0]}),
    .R1(\ex_mem气泡_1_out_18 ), .R2(MDin), .WB(MEM_RegWrite_num), .out_13(WB_PC), .out_14(WB_IR),
    .out_15({\mem_wb气泡_1_out_15 [21:10], RegWrite, \mem_wb气泡_1_out_15 [8:0]}), .out_16(\mem_wb气泡_1_out_16 ),
    .out_17(\mem_wb气泡_1_out_17 ), .out_18(\mem_wb气泡_1_out_18 ), .SYNC_RESET(1'b0), .\使能 (not_1_out),
    .CLK(CLK), .ALU_RES(\ex_mem气泡_1_out_15 ), .out_19(\mem_wb气泡_1_out_19 ), .MEM_RES(ram_1_data),
    .out_20(\mem_wb气泡_1_out_20 ));  // open: ALU_RES2, out_21
  Comparator #(.width(32), .mode("twosComplement")) comparator_12 (
    .a(\mem_wb气泡_1_out_16 ), .b(32'h32), .eq(comparator_12_eq));  // open: gt, lt
  and and_12 (Halt, \mem_wb气泡_1_out_15 [12], comparator_12_eq);
  not not_9 (not_9_out, comparator_12_eq);
  and and_13 (and_13_out, not_9_out, \mem_wb气泡_1_out_15 [12]);
  Counter #(.width(32), .max('hffffffff), .ongoal("wrap"), .trigger("rising"), .behavior("old")) counter_3 (
    .load(and_13_out), .D(\mem_wb气泡_1_out_17 ), .count(1'b0), .Q(LedData), .clk(CLK));  // open: carry, clr, preset
  Multiplexer #(.select(1), .width(32), .disabled("Z"), .enable("false")) multiplexer_11 (
    .in0(\mem_wb气泡_1_out_19 ), .in1(\mem_wb气泡_1_out_20 ), .out(multiplexer_11_out),
    .sel(\mem_wb气泡_1_out_15 [2]));
  Multiplexer #(.select(1), .width(32), .disabled("Z"), .enable("false")) multiplexer_12 (
    .in0(multiplexer_11_out), .in1(adder_4_out), .out(RDin), .sel(\mem_wb气泡_1_out_15 [10]));
  Adder #(.width(32)) adder_4 (.a(WB_PC), .b(32'h4), .out(adder_4_out));  // open: cin, cout

  // Other names for the same wires on the sheet: PCSrc[2:0] = {JR, JMP, JMP_IF}; MemToReg = CRTL[2];
  //   CRTL[8:4] = {AluSrc, AluOp}; JAL = CRTL[10]; RegDst = CRTL[11]; SysCall = CRTL[12]; SignedExt = CRTL[15];
  //   DIVU = CRTL[16]; MFLO = CRTL[17]; LBU = CRTL[18]; R1_Used = CRTL[20]; R2_Used = CRTL[21];
  //   IMME[15:0] = ID_IR[15:0]; SHAMT[4:0] = ID_IR[10:6]; RD[4:0] = ID_IR[15:11]; RT[4:0] = ID_IR[20:16];
  //   RS[4:0] = ID_IR[25:21]; IR[31:0] = IF_IR; JmpPc[27:2] = ADDR; PC_4[31:28] = JmpPc; MEM_PC[31:0] = M_PC;
  //   PC[31:0] = IF_PC

  // Notes on the sheet:
  //   中断源
  //   时空图监测，可删除
  //   中断等待指示
  //   数码管输出
  //   指令存储器
  //   contents of rom_1 (hex, n*v repeats v):
  //   20110001 8000c05 20110001 20120002 20130003 8000c09 20110001 20120002 20130003 8000c0d 20110001
  //   20120002 20130003 8000c11 20110001 20120002 20130003 c000cb8 20100001 20110001 118fc0 112020
  //   20020022 c 118882 12200001 8000c15 112020 20020022 c 20110001 118880 112020 20020022 c 12200001
  //   8000c1f 20110001 118fc0 112020 20020022 c 1188c3 112020 20020022 c 118903 112020 20020022 c 118903
  //   112020 20020022 c 118903 112020 20020022 c 118903 112020 20020022 c 118903 112020 20020022 c 118903
  //   112020 20020022 c 118903 112020 20020022 c 20100001 109fc0 139fc3 8021 2012000c 24160003 26100001
  //   3210000f 20080008 20090001 139900 2709825 132020 20020022 c 1094022 1500fff9 22100001 2018000f
  //   2188024 108700 20080008 20090001 139902 2709825 132021 20020022 c 1094022 1500fff9 108702 2c9b022
  //   12c00001 8000c50 4020 1084027 84400 3508ffff 82021 20020022 c 2010ffff 20110000 ae300000 22100001
  //   22310004 ae300000 22100001 22310004 ae300000 22100001 22310004 ae300000 22100001 22310004 ae300000
  //   22100001 22310004 ae300000 22100001 22310004 ae300000 22100001 22310004 ae300000 22100001 22310004
  //   ae300000 22100001 22310004 ae300000 22100001 22310004 ae300000 22100001 22310004 ae300000 22100001
  //   22310004 ae300000 22100001 22310004 ae300000 22100001 22310004 ae300000 22100001 22310004 ae300000
  //   22100001 22310004 22100001 8020 2011003c 8e130000 8e340000 274402a 11000002 ae330000 ae140000
  //   2231fffc 1611fff8 102020 20020022 c 22100004 2011003c 1611fff2 20020032 c 20100000 22100001 102020
  //   20020022 c 22100002 102020 20020022 c 22100003 102020 20020022 c 22100004 102020 20020022 c 22100005
  //   102020 20020022 c 22100006 102020 20020022 c 22100007 102020 20020022 c 22100008 102020 20020022
  //   20020022 c 3e00008
  //   指令字
  //   控制位
  //   流水调试日志用
  //   暂停节拍，不能为0
  //   戳工具置1进入计数暂停模式，ctrl+k时钟自动运行到对应节拍暂停
  //   ctrl+k关闭时钟连续运行，将控制位置零，进入单步调试模式调试
  //   JMP
  //   JR
  //   可计数暂停的时钟源
  //   为方便自动评测，需要输出流水线各段保存的PC值，注意是PC不是PC+4，另外ID段寄存器写入信息，Mem段内存写入信息也要输出
endmodule

module \重定向流水线  (
  output RegWrite,
  output MemWrite,
  output [31:0] LedData,
  output [31:0] IF_PC,
  output [31:0] ID_PC,
  output [31:0] EX_PC,
  output [31:0] M_PC,
  output [31:0] WB_PC,
  output [31:0] RDin,
  output [31:0] MDin,
  output [31:0] LedData_2
);

  wire AluSrc, and_1_out, and_2_out, and_3_out, and_4_out, and_5_out, and_6_out, and_7_out, and_12_out,
       and_14_out, and_15_out, and_17_out, and_18_out, and_19_out, and_20_out, and_22_out, BEQ, BGTZ, BNE,
       CLK, clock_1_out, clock_2_out, comparator_1_eq, comparator_2_eq, comparator_3_eq, comparator_4_eq,
       comparator_5_eq, comparator_6_eq, comparator_7_eq, comparator_8_eq, comparator_9_eq, comparator_10_eq,
       comparator_11_eq, comparator_11_lt, comparator_12_gt, comparator_14_eq, d_ff_1_q, Equal, EX_MFLO,
       EX_RegWrite, Go, Halt, IR1, IR2, IR3, JMP, JMP_IF, JR, load_use, MEM_MEMToReg, MEM_MFLO, MEM_RegWrite,
       multiplexer_3_out, nand_1_out, NeedJmp, not_1_out, not_2_out, not_3_out, not_4_out, not_5_out,
       not_6_out, not_7_out, not_8_out, not_9_out, not_10_out, not_11_out, or_1_out, or_2_out, or_3_out,
       or_5_out, or_7_out, or_9_out, or_11_out, PC_q, R1_EX, R1_MEM, R2_EX, R2_MEM, RST, W1, W2, W3,
       WB_MEMToReg, WB_MFLO;
  wire [1:0] R1_Fwd, R1_Fwd_ID, R2_Fwd, R2_Fwd_ID;
  wire [3:0] AluOp;
  wire [4:0] EX_RegWrite_num, \id_ex气泡_1_out_21 , ID_R1_num, ID_R2_num, MEM_RegWrite_num,
       \mem_wb气泡_1_out_18 , multiplexer_1_out, multiplexer_2_out, multiplexer_7_out, multiplexer_10_out;
  wire [7:0] multiplexer_14_out, ram_1_data, ram_1_data_2, ram_1_data_3, ram_1_data_4;
  wire [12:0] CNT_num;
  wire [15:0] adder_4_out, counter_6_q, \LoadUse次数 , \总周期数 , \插入气泡数 , \无条件分支数 , \条件分支成功数 ;
  wire [21:0] CRTL, \ex_mem气泡_1_out_14 , \mem_wb气泡_1_out_15 ;
  wire [21:2] \id_ex气泡_1_out_17 ;
  wire [25:0] ADDR;
  wire [27:0] PC_4;
  wire [31:0] adder_1_out, bit_extender_1_out, bit_extender_2_out, bit_extender_3_out, EX_IR,
       \ex_mem气泡_1_out_16 , \ex_mem气泡_1_out_18 , HI, ID_IR, IF_IR, IMME32, IMME32_EX, MEM_ALURes, MEM_IR,
       \mem_wb气泡_1_out_16 , \mem_wb气泡_1_out_17 , \mem_wb气泡_1_out_21 , mips_alu_1_result_2,
       mips_regifile_1_r1, mips_regifile_1_r2, multiplexer_4_out, multiplexer_12_out, multiplexer_15_out,
       multiplexer_16_out, multiplexer_17_out, PC_4_IMME, PC_Next, R1, R1_Final, R2, R2_Final, Res1,
       shifter_1_out, WB_ALURes, WB_IR, WB_JALRes, WB_MEMRes;
  wire [31:28] JmpPc;

  Button \u_总复位  (.out(RST));
  Button _1 (.out(IR1));
  Button _2 (.out(IR2));
  Button _3 (.out(IR3));
  // Probe on \总周期数 
  // Probe on \总周期数 
  Button \u_继续运行  (.out(Go));
  LED #(.active("true")) led_1 (.in(W1));
  LED #(.active("true")) led_2 (.in(W2));
  LED #(.active("true")) led_3 (.in(W3));
  Hex_Digit_Display hex_digit_display_1 (.value(LedData_2[31:28]));  // open: dp
  // Probe on IF_PC[19:0]
  // Mips_Probe mips_probe_1: pin names not known; wires that end beside it: IF_IR
  Multiplexer #(.select(1), .width(5), .disabled("Z"), .enable("false")) multiplexer_1 (
    .in0({5{1'b0}}), .in1(ID_R1_num), .out(multiplexer_1_out), .sel(CRTL[20]));
  Multiplexer #(.select(1), .width(5), .disabled("Z"), .enable("false")) multiplexer_2 (
    .in0({5{1'b0}}), .in1(ID_R2_num), .out(multiplexer_2_out), .sel(CRTL[21]));
  or or_1 (or_1_out, CRTL[17], EX_MFLO, MEM_MFLO, WB_MFLO);
  Hex_Digit_Display hex_digit_display_2 (.value(LedData_2[27:24]));  // open: dp
  Hex_Digit_Display hex_digit_display_3 (.value(LedData_2[23:20]));  // open: dp
  // Probe on ID_PC[19:0]
  // Mips_Probe mips_probe_2: pin names not known; wires that end beside it: ID_IR
  Comparator #(.width(5), .mode("twosComplement")) comparator_1 (
    .a(multiplexer_1_out), .b(EX_RegWrite_num), .eq(comparator_1_eq));  // open: gt, lt
  Comparator #(.width(5), .mode("twosComplement")) comparator_2 (
    .a(multiplexer_1_out), .b(MEM_RegWrite_num), .eq(comparator_2_eq));  // open: gt, lt
  Comparator #(.width(5), .mode("twosComplement")) comparator_3 (
    .a(multiplexer_2_out), .b(EX_RegWrite_num), .eq(comparator_3_eq));  // open: gt, lt
  Comparator #(.width(5), .mode("twosComplement")) comparator_4 (
    .a(multiplexer_2_out), .b(MEM_RegWrite_num), .eq(comparator_4_eq));  // open: gt, lt
  Adder #(.width(32)) adder_1 (.a(IF_PC), .b(32'h4), .out(adder_1_out));  // open: cin, cout
  Register #(.width(1), .trigger("rising"), .Select("low")) PC (
    .D(Halt), .en(not_6_out), .Q(PC_q), .clk(CLK), .clr(Go));
  Multiplexer #(.select(1), .width(1), .disabled("Z"), .enable("false")) multiplexer_3 (
    .in0(1'b1), .in1(1'b0), .out(multiplexer_3_out), .sel(or_1_out));
  and and_1 (and_1_out, multiplexer_3_out, not_1_out);
  not not_1 (not_1_out, load_use);
  Hex_Digit_Display hex_digit_display_4 (.value(LedData_2[15:12]));  // open: dp
  Hex_Digit_Display hex_digit_display_5 (.value(LedData_2[19:16]));  // open: dp
  Comparator #(.width(5), .mode("twosComplement")) comparator_5 (
    .a(multiplexer_1_out), .b({5{1'b0}}), .eq(comparator_5_eq));  // open: gt, lt
  not not_2 (not_2_out, comparator_5_eq);
  Comparator #(.width(5), .mode("twosComplement")) comparator_6 (
    .a(multiplexer_1_out), .b({5{1'b0}}), .eq(comparator_6_eq));  // open: gt, lt
  not not_3 (not_3_out, comparator_6_eq);
  Comparator #(.width(5), .mode("twosComplement")) comparator_7 (
    .a(multiplexer_2_out), .b({5{1'b0}}), .eq(comparator_7_eq));  // open: gt, lt
  not not_4 (not_4_out, comparator_7_eq);
  Comparator #(.width(5), .mode("twosComplement")) comparator_8 (
    .a(multiplexer_2_out), .b({5{1'b0}}), .eq(comparator_8_eq));  // open: gt, lt
  not not_5 (not_5_out, comparator_8_eq);
  Multiplexer #(.select(1), .width(32), .disabled("Z"), .enable("false")) multiplexer_4 (
    .in0(adder_1_out), .in1(PC_Next), .out(multiplexer_4_out), .sel(NeedJmp));
  and and_2 (and_2_out, not_6_out, and_1_out);
  not not_6 (not_6_out, PC_q);
  Hex_Digit_Display hex_digit_display_6 (.value(LedData_2[11:8]));  // open: dp
  Hex_Digit_Display hex_digit_display_7 (.value(LedData_2[7:4]));  // open: dp
  Clock #(.highDuration(1), .lowDuration(1)) clock_1 (.out(clock_1_out));
  // Probe on EX_PC[19:0]
  // Mips_Probe mips_probe_3: pin names not known; wires that end beside it: clock_1_out, CLK, EX_IR
  and and_3 (and_3_out, not_2_out, comparator_1_eq);
  and and_4 (and_4_out, not_3_out, comparator_2_eq);
  and and_5 (and_5_out, not_4_out, comparator_3_eq);
  and and_6 (and_6_out, not_5_out, comparator_4_eq);
  Register #(.width(32), .trigger("rising"), .Select("low")) PC_2 (
    .D(multiplexer_4_out), .en(and_2_out), .Q(IF_PC), .clk(CLK));  // open: clr
  and and_7 (and_7_out, CLK, not_6_out);
  Hex_Digit_Display hex_digit_display_8 (.value(LedData_2[3:0]));  // open: dp
  and and_8 (R1_EX, and_3_out, EX_RegWrite);
  and and_9 (R1_MEM, and_4_out, MEM_RegWrite);
  and and_10 (R2_EX, and_5_out, EX_RegWrite);
  and and_11 (R2_MEM, and_6_out, MEM_RegWrite);
  Counter #(.width(16), .max('hffff), .ongoal("wrap"), .trigger("rising"), .behavior("new")) counter_1 (
    .Q(\总周期数 ), .clk(and_7_out));  // open: load, D, count, carry, clr, preset, down
  // Probe on \总周期数 
  // Probe on M_PC[19:0]
  // Mips_Probe mips_probe_4: pin names not known; wires that end beside it: MEM_IR
  ROM #(.addrWidth(10), .dataWidth(32), .Select("high")) rom_1 (.addr(IF_PC[11:2]), .data(IF_IR));
  // Probe on \总周期数 
  // Probe on \无条件分支数 
  // Probe on \条件分支成功数 
  // Probe on \插入气泡数 
  // Probe on \LoadUse次数 
  // Mips_Probe mips_probe_5: pin names not known; wires that end beside it: IF_IR, CRTL[21]
  not not_7 (not_7_out, load_use);
  or or_2 (or_2_out, or_3_out, NeedJmp);
  or or_3 (or_3_out, CRTL[17], EX_MFLO, MEM_MFLO, WB_MFLO);
  // Probe on IF_PC[11:0]
  // Probe on WB_PC[19:0]
  // Mips_Probe mips_probe_6: pin names not known; wires that end beside it: WB_IR
  // Probe on EX_PC[11:0]
  // Probe on ID_PC[11:0]
  \IF_ID气泡  \if_id气泡_1  (
    .PC(IF_PC), .IR(IF_IR), .PC_2(ID_PC), .IR_2(ID_IR), .SYNC_RESET(or_2_out), .\使能 (not_7_out), .CLK(CLK));
  // Probe on M_PC[11:0]
  D_Flip_Flop #(.trigger("high"), .Pre_Clr_Positions("LEGACY"), .NegatePresetClear("false"), .enable("true"), .NewFFLayout("false")) d_ff_1 (.Q(d_ff_1_q));  // open: clk, D, Qn, preset, en, reset
  // Probe on 13'hea
  Multiplexer #(.select(2), .width(32), .disabled("Z"), .enable("false")) multiplexer_5 (
    .in0(R1), .in1(MEM_ALURes), .in2(WB_ALURes), .in3(WB_MEMRes), .out(R1_Final), .sel(R1_Fwd));
  not not_8 (not_8_out, R1_EX);
  and and_12 (and_12_out, R1_MEM, MEM_MEMToReg);
  Comparator #(.width(6), .mode("twosComplement")) comparator_9 (
    .a(EX_IR[31:26]), .b(6'b100011), .eq(comparator_9_eq));  // open: gt, lt
  Comparator #(.width(6), .mode("twosComplement")) comparator_10 (
    .a(EX_IR[31:26]), .b(6'b100100), .eq(comparator_10_eq));  // open: gt, lt
  // Probe on WB_PC[11:0]
  Comparator #(.width(13), .mode("twosComplement")) comparator_11 (
    .a(CNT_num), .b(13'hea), .eq(comparator_11_eq), .lt(comparator_11_lt));  // open: gt
  Clock #(.highDuration(1), .lowDuration(1)) clock_2 (.out(clock_2_out));
  and and_13 (R1_Fwd_ID[1], not_8_out, R1_MEM);
  or or_4 (R1_Fwd_ID[0], R1_EX, and_12_out);
  or or_5 (or_5_out, comparator_9_eq, comparator_10_eq);
  nand nand_1 (nand_1_out, d_ff_1_q, comparator_11_eq);
  Counter #(.width(13), .max('h1fff), .ongoal("stay"), .trigger("rising"), .behavior("old")) counter_2 (
    .count(comparator_11_lt), .Q(CNT_num), .clk(clock_2_out));  // open: load, D, carry, clr, preset
  and and_14 (and_14_out, R1_EX, or_5_out);
  and and_15 (and_15_out, R2_EX, or_5_out);
  \单周期硬布线控制器  \u_单周期硬布线控制器_1  (
    .Func(ID_IR[5:0]), .OP(ID_IR[31:26]), .ALU_OP(AluOp), .MemToReg(CRTL[2]), .MemWrite(CRTL[3]),
    .ALU_SRC(AluSrc), .RegWrite(CRTL[9]), .SysCALL(CRTL[12]), .SignedExt(CRTL[15]), .RegDst(CRTL[11]),
    .JR(CRTL[14]), .JMP(CRTL[13]), .Beq(CRTL[0]), .JAL(CRTL[10]), .Bne(CRTL[1]), .DIVU(CRTL[16]),
    .MFLO(CRTL[17]), .LBU(CRTL[18]), .BGTZ(CRTL[19]), .R1_Used(CRTL[20]), .R2_Used(CRTL[21]));
  assign CLK = nand_1_out ? clock_2_out : 1'bz;  // Controlled_Buffer controlled_buffer_1
  Pull_Resistor #(.pull(1)) pull_resistor_1 (.node(CLK));
  or or_6 (load_use, and_14_out, and_15_out);
  Multiplexer #(.select(2), .width(32), .disabled("Z"), .enable("false")) multiplexer_6 (
    .in0(R2), .in1(MEM_ALURes), .in2(WB_ALURes), .in3(WB_MEMRes), .out(R2_Final), .sel(R2_Fwd));
  not not_9 (not_9_out, R2_EX);
  Multiplexer #(.select(1), .width(5), .disabled("Z"), .enable("false")) multiplexer_7 (
    .in0(ID_IR[20:16]), .in1(ID_IR[15:11]), .out(multiplexer_7_out), .sel(or_7_out));
  or or_7 (or_7_out, CRTL[11], CRTL[17]);
  and and_16 (R2_Fwd_ID[1], not_9_out, R2_MEM);
  or or_8 (R2_Fwd_ID[0], R2_EX, and_17_out);
  and and_17 (and_17_out, R2_MEM, MEM_MEMToReg);
  assign bit_extender_1_out = {{16{1'b0}}, ID_IR[15:0]};  // Bit_Extender bit_extender_1
  assign bit_extender_2_out = {{16{ID_IR[15]}}, ID_IR[15:0]};  // Bit_Extender bit_extender_2
  Multiplexer #(.select(1), .width(5), .disabled("Z"), .enable("false")) multiplexer_8 (
    .in0(ID_IR[25:21]), .in1(5'b00010), .out(ID_R1_num), .sel(CRTL[12]));
  Multiplexer #(.select(1), .width(5), .disabled("Z"), .enable("false")) multiplexer_9 (
    .in0(ID_IR[20:16]), .in1(5'b00100), .out(ID_R2_num), .sel(CRTL[12]));
  Multiplexer #(.select(1), .width(5), .disabled("Z"), .enable("false")) multiplexer_10 (
    .in0(multiplexer_7_out), .in1({5{1'b1}}), .out(multiplexer_10_out), .sel(CRTL[10]));
  Multiplexer #(.select(1), .width(32), .disabled("Z"), .enable("false")) multiplexer_11 (
    .in0(bit_extender_1_out), .in1(bit_extender_2_out), .out(IMME32), .sel(CRTL[15]));
  MIPS_Regifile mips_regifile_1 (
    .Din(RDin), .Clk(CLK), .R1(mips_regifile_1_r1), .R2(mips_regifile_1_r2), .WE(RegWrite),
    .W_num(\mem_wb气泡_1_out_18 ), .R1_num(ID_R1_num), .R2_num(ID_R2_num));
  or or_9 (or_9_out, load_use, NeedJmp);
  \ID_EX气泡  \id_ex气泡_1  (
    .PC(ID_PC), .IR(ID_IR), .CTRL({CRTL[21:9], AluSrc, AluOp, CRTL[3:0]}), .R1(mips_regifile_1_r1),
    .R2(mips_regifile_1_r2), .IMME(IMME32), .SHAMT(ID_IR[10:6]), .WB(multiplexer_10_out), .out_15(EX_PC),
    .out_16(EX_IR),
    .out_17({\id_ex气泡_1_out_17 [21:20], BGTZ, \id_ex气泡_1_out_17 [18], EX_MFLO, \id_ex气泡_1_out_17 [16:15], JR, JMP, \id_ex气泡_1_out_17 [12:10], EX_RegWrite, \id_ex气泡_1_out_17 [8:2], BNE, BEQ}),
    .out_18(R1), .out_19(R2), .out_20(IMME32_EX), .out_21(\id_ex气泡_1_out_21 ), .out_22(EX_RegWrite_num),
    .SYNC_RESET(or_9_out), .\使能 (not_6_out), .CLK(CLK), .ADDR(ID_IR[25:0]), .out_23(ADDR),
    .R1_Fwd(R1_Fwd_ID), .out_24(R1_Fwd), .R2_Fwd(R2_Fwd_ID), .out_25(R2_Fwd));
  Shifter #(.width(32), .shift("ll")) shifter_1 (.in(IMME32_EX), .\dist (5'b00010), .out(shifter_1_out));
  and and_18 (and_18_out, BEQ, Equal);
  and and_19 (and_19_out, BNE, not_10_out);
  not not_10 (not_10_out, Equal);
  Comparator #(.width(32), .mode("twosComplement")) comparator_12 (
    .a(R1), .b({32{1'b0}}), .gt(comparator_12_gt));  // open: eq, lt
  Counter #(.width(16), .max('hffff), .ongoal("stay"), .trigger("rising"), .behavior("old")) counter_3 (
    .count(JMP), .Q(\无条件分支数 ), .clk(CLK));  // open: load, D, carry, clr, preset
  Counter #(.width(16), .max('hffff), .ongoal("stay"), .trigger("rising"), .behavior("old")) counter_4 (
    .count(JMP_IF), .Q(\条件分支成功数 ), .clk(CLK));  // open: load, D, carry, clr, preset
  Adder #(.width(32)) adder_2 (.a(EX_PC), .b(32'h4), .out({JmpPc, PC_4}));  // open: cin, cout
  Adder #(.width(32)) adder_3 (.a({JmpPc, PC_4}), .b(shifter_1_out), .out(PC_4_IMME));  // open: cin, cout
  or or_10 (JMP_IF, and_18_out, and_19_out, and_20_out);
  and and_20 (and_20_out, comparator_12_gt, BGTZ);
  Multiplexer #(.select(1), .width(32), .disabled("Z"), .enable("false")) multiplexer_12 (
    .in0(R2_Final), .in1(IMME32_EX), .out(multiplexer_12_out), .sel(\id_ex气泡_1_out_17 [8]));
  MIPS_ALU mips_alu_1 (
    .X(R1_Final), .Y(multiplexer_12_out), .AluOP(\id_ex气泡_1_out_17 [7:4]), .Equal(Equal), .Result(Res1),
    .Result_2(mips_alu_1_result_2), .shamt(\id_ex气泡_1_out_21 ));
  or or_11 (or_11_out, load_use, NeedJmp);
  Counter #(.width(16), .max('hffff), .ongoal("stay"), .trigger("rising"), .behavior("old")) counter_5 (
    .count(load_use), .Q(\LoadUse次数 ), .clk(CLK));  // open: load, D, carry, clr, preset
  Counter #(.width(16), .max('hffff), .ongoal("stay"), .trigger("rising"), .behavior("old")) counter_6 (
    .count(or_11_out), .Q(counter_6_q), .clk(CLK));  // open: load, D, carry, clr, preset
  Multiplexer #(.select(3), .width(32), .disabled("Z"), .enable("false")) multiplexer_13 (
    .in0({JmpPc, PC_4}), .in1(PC_4_IMME), .in2({JmpPc, ADDR, 2'b00}), .in6(R1), .out(PC_Next),
    .sel({JR, JMP, JMP_IF}));  // open: in3, in4, in5, in7
  Comparator #(.width(3), .mode("unsigned")) comparator_13 (
    .a({JR, JMP, JMP_IF}), .b(3'b000), .gt(NeedJmp));  // open: eq, lt
  Adder #(.width(16)) adder_4 (.a(counter_6_q), .b(\无条件分支数 ), .out(adder_4_out));  // open: cin, cout
  Adder #(.width(16)) adder_5 (.a(adder_4_out), .b(\条件分支成功数 ), .out(\插入气泡数 ));  // open: cin, cout
  \EX_MEM气泡  \ex_mem气泡_1  (
    .PC(EX_PC), .IR(EX_IR),
    .CTRL({\id_ex气泡_1_out_17 [21:20], BGTZ, \id_ex气泡_1_out_17 [18], EX_MFLO, \id_ex气泡_1_out_17 [16:15], JR, JMP, \id_ex气泡_1_out_17 [12:10], EX_RegWrite, \id_ex气泡_1_out_17 [8:2], BNE, BEQ}),
    .Res1(Res1), .MDin(R2_Final), .R1(R1_Final), .WB(EX_RegWrite_num), .out_12(M_PC), .out_13(MEM_IR),
    .out_14({\ex_mem气泡_1_out_14 [21:18], MEM_MFLO, \ex_mem气泡_1_out_14 [16:10], MEM_RegWrite, \ex_mem气泡_1_out_14 [8:4], MemWrite, MEM_MEMToReg, \ex_mem气泡_1_out_14 [1:0]}),
    .out_15(MEM_ALURes), .out_17(MDin), .out_18(\ex_mem气泡_1_out_18 ), .out_19(MEM_RegWrite_num),
    .SYNC_RESET(1'b0), .\使能 (not_6_out), .CLK(CLK), .Res2(mips_alu_1_result_2), .out_16(\ex_mem气泡_1_out_16 ));
  Multiplexer #(.select(2), .width(8), .disabled("Z"), .enable("false")) multiplexer_14 (
    .in0(ram_1_data), .in1(ram_1_data_2), .in2(ram_1_data_3), .in3(ram_1_data_4), .out(multiplexer_14_out),
    .sel(MEM_ALURes[1:0]));
  assign bit_extender_3_out = {{24{1'b0}}, multiplexer_14_out};  // Bit_Extender bit_extender_3
  RAM #(.addrWidth(10), .dataWidth(32), .bus("separate"), .Select("high")) ram_1 (
    .addr(MEM_ALURes[11:2]), .din(MDin), .data({ram_1_data_4, ram_1_data_3, ram_1_data_2, ram_1_data}),
    .str(MemWrite), .clk(CLK));  // open: sel, ld, clr
  Multiplexer #(.select(1), .width(32), .disabled("Z"), .enable("false")) multiplexer_15 (
    .in0({ram_1_data_4, ram_1_data_3, ram_1_data_2, ram_1_data}), .in1(bit_extender_3_out),
    .out(multiplexer_15_out), .sel(\ex_mem气泡_1_out_14 [18]));
  // Probe on \mem_wb气泡_1_out_17 
  \MEM_WB气泡  \mem_wb气泡_1  (
    .PC(M_PC), .IR(MEM_IR),
    .CTRL({\ex_mem气泡_1_out_14 [21:18], MEM_MFLO, \ex_mem气泡_1_out_14 [16:10], MEM_RegWrite, \ex_mem气泡_1_out_14 [8:4], MemWrite, MEM_MEMToReg, \ex_mem气泡_1_out_14 [1:0]}),
    .R1(\ex_mem气泡_1_out_18 ), .R2(MDin), .WB(MEM_RegWrite_num), .out_13(WB_PC), .out_14(WB_IR),
    .out_15({\mem_wb气泡_1_out_15 [21:18], WB_MFLO, \mem_wb气泡_1_out_15 [16:3], WB_MEMToReg, \mem_wb气泡_1_out_15 [1:0]}),
    .out_16(\mem_wb气泡_1_out_16 ), .out_17(\mem_wb气泡_1_out_17 ), .out_18(\mem_wb气泡_1_out_18 ),
    .SYNC_RESET(1'b0), .\使能 (not_6_out), .CLK(CLK), .ALU_RES(MEM_ALURes), .out_19(WB_ALURes),
    .MEM_RES(multiplexer_15_out), .out_20(WB_MEMRes), .ALU_RES2(\ex_mem气泡_1_out_16 ),
    .out_21(\mem_wb气泡_1_out_21 ));
  Comparator #(.width(32), .mode("twosComplement")) comparator_14 (
    .a(\mem_wb气泡_1_out_16 ), .b(32'h32), .eq(comparator_14_eq));  // open: gt, lt
  not not_11 (not_11_out, comparator_14_eq);
  and and_21 (Halt, \mem_wb气泡_1_out_15 [12], comparator_14_eq);
  and and_22 (and_22_out, not_11_out, \mem_wb气泡_1_out_15 [12]);
  Counter #(.width(32), .max('hffffffff), .ongoal("wrap"), .trigger("rising"), .behavior("old")) counter_7 (
    .load(and_22_out), .D(\mem_wb气泡_1_out_17 ), .count(1'b0), .Q(LedData_2), .clk(CLK));  // open: carry, clr, preset
  Multiplexer #(.select(1), .width(32), .disabled("Z"), .enable("false")) multiplexer_16 (
    .in0(WB_ALURes), .in1(WB_MEMRes), .out(multiplexer_16_out), .sel(WB_MEMToReg));
  or or_12 (RegWrite, \mem_wb气泡_1_out_15 [9], WB_MFLO);
  Multiplexer #(.select(1), .width(32), .disabled("Z"), .enable("false")) multiplexer_17 (
    .in0(multiplexer_16_out), .in1(WB_JALRes), .out(multiplexer_17_out), .sel(\mem_wb气泡_1_out_15 [10]));
  Adder #(.width(32)) adder_6 (.a(WB_PC), .b(32'h4), .out(WB_JALRes));  // open: cin, cout
  Multiplexer #(.select(1), .width(32), .disabled("Z"), .enable("false")) multiplexer_18 (
    .in0(multiplexer_17_out), .in1(LedData), .out(RDin), .sel(WB_MFLO));
  Register #(.width(32), .trigger("falling"), .Select("low")) register_1 (
    .D(WB_ALURes), .en(\mem_wb气泡_1_out_15 [16]), .Q(LedData), .clk(CLK));  // open: clr
  Register #(.width(32), .trigger("falling"), .Select("low")) register_2 (
    .D(\mem_wb气泡_1_out_21 ), .en(\mem_wb气泡_1_out_15 [16]), .Q(HI), .clk(CLK));  // open: clr

  // Other names for the same wires on the sheet: PCSrc[2:0] = {JR, JMP, JMP_IF}; MemToReg = CRTL[2];
  //   CRTL[8:4] = {AluSrc, AluOp}; JAL = CRTL[10]; RegDst = CRTL[11]; SysCall = CRTL[12]; SignedExt = CRTL[15];
  //   DIVU = CRTL[16]; MFLO = CRTL[17]; LBU = CRTL[18]; R1_Used = CRTL[20]; R2_Used = CRTL[21];
  //   EX_OPCode[5:0] = EX_IR[31:26]; IMME[15:0] = ID_IR[15:0]; SHAMT[4:0] = ID_IR[10:6]; RD[4:0] = ID_IR[15:11];
  //   RT[4:0] = ID_IR[20:16]; RS[4:0] = ID_IR[25:21]; IR[31:0] = IF_IR; JmpPc[27:2] = ADDR; PC_4[31:28] = JmpPc;
  //   LedData_t[31:0] = LedData_2; LO[31:0] = LedData; MEM_PC[31:0] = M_PC; PC[31:0] = IF_PC

  // Notes on the sheet:
  //   中断源
  //   时空图监测，可删除
  //   中断等待指示
  //   数码管输出
  //   指令存储器
  //   contents of rom_1 (hex, n*v repeats v):
  //   20110001 8000c05 20110001 20120002 20130003 8000c09 20110001 20120002 20130003 8000c0d 20110001
  //   20120002 20130003 8000c11 20110001 20120002 20130003 c000cfa 20100001 20110001 118fc0 112020
  //   20020022 c 118882 12200001 8000c15 112020 20020022 c 20110001 118880 112020 20020022 c 12200001
  //   8000c1f 20110001 118fc0 112020 20020022 c 1188c3 112020 20020022 c 118903 112020 20020022 c 118903
  //   112020 20020022 c 118903 112020 20020022 c 118903 112020 20020022 c 118903 112020 20020022 c 118903
  //   112020 20020022 c 118903 112020 20020022 c 20100001 109fc0 139fc3 8021 2012000c 24160003 26100001
  //   3210000f 20080008 20090001 139900 2709825 132020 20020022 c 1094022 1500fff9 22100001 2018000f
  //   2188024 108700 20080008 20090001 139902 2709825 132021 20020022 c 1094022 1500fff9 108702 2c9b022
  //   12c00001 8000c50 4020 1084027 84400 3508ffff 82021 20020022 c 2010ffff 20110000 ae300000 22100001
  //   22310004 ae300000 22100001 22310004 ae300000 22100001 22310004 ae300000 22100001 22310004 ae300000
  //   22100001 22310004 ae300000 22100001 22310004 ae300000 22100001 22310004 ae300000 22100001 22310004
  //   ae300000 22100001 22310004 ae300000 22100001 22310004 ae300000 22100001 22310004 ae300000 22100001
  //   22310004 ae300000 22100001 22310004 ae300000 22100001 22310004 ae300000 22100001 22310004 ae300000
  //   22100001 22310004 22100001 8020 2011003c 8e130000 8e340000 274402a 11000002 ae330000 ae140000
  //   2231fffc 1611fff8 102020 20020022 c 22100004 2011003c 1611fff2 20020032 c 5*0 20080002 20111111
  //   118c00 112020 20020022 c 200b001c 228001b 8812 112020 20020022 c 216bffff 1560fff9 20020032 c 5*0
  //   20090000 200b0020 34118483 20120401 118c00 129400 36318281 22520401 ad310000 2328820 21290004
  //   216bffff 1560fffb 20020022 200b0020 20090000 91310000 112020 20020022 c 21290004 216bffff 1560fff9
  //   20020032 c 5*0 2011000f 112020 20020022 c 2231ffff 1e20fffb 2002000a c 20020032 c 20100000 22100001
  //   102020 20020022 c 22100002 102020 20020022 c 22100003 102020 20020022 c 22100004 102020 20020022 c
  //   22100005 102020 20020022 c 22100006 102020 20020022 c 22100007 102020 20020022 c 22100008 102020
  //   20020022 20020022 c 3e00008
  //   指令字
  //   控制位
  //   流水调试日志用
  //   暂停节拍，不能为0
  //   戳工具置1进入计数暂停模式，ctrl+k时钟自动运行到对应节拍暂停
  //   ctrl+k关闭时钟连续运行，将控制位置零，进入单步调试模式调试
  //   ctrl+k关闭时钟连续运行，将控制位置零，进入单步调试模式调试
  //   JMP
  //   JR
  //   可计数暂停的时钟源
  //   为方便自动评测，需要输出流水线各段保存的PC值，注意是PC不是PC+4，另外ID段寄存器写入信息，Mem段内存写入信息也要输出
endmodule

module \中断按键参考电路  (
  input  \同步清零信号 ,
  output \与中断屏蔽位与 
);

  wire \_1号中断_out , and_1_out, clock_1_out, d_ff_1_q, or_1_out, or_2_out;

  Clock #(.highDuration(1), .lowDuration(1)) clock_1 (.out(clock_1_out));
  Button \_1号中断  (.out(\_1号中断_out ));
  LED #(.active("true")) \_1号中断等待指示灯  (.in(or_1_out));
  or or_1 (or_1_out, \与中断屏蔽位与 , d_ff_1_q);
  D_Flip_Flop #(.trigger("rising"), .Pre_Clr_Positions("LEGACY"), .NegatePresetClear("false"), .enable("true"), .NewFFLayout("false")) d_ff_1 (
    .clk(\_1号中断_out ), .D(1'b1), .Q(d_ff_1_q), .reset(\与中断屏蔽位与 ));  // open: Qn, preset, en
  or or_2 (or_2_out, d_ff_1_q, \与中断屏蔽位与 );
  and and_1 (and_1_out, or_2_out, ~\同步清零信号 );  // AND_Gate
  D_Flip_Flop #(.trigger("rising"), .Pre_Clr_Positions("LEGACY"), .NegatePresetClear("false"), .enable("true"), .NewFFLayout("false")) IR1 (
    .clk(clock_1_out), .D(and_1_out), .Q(\与中断屏蔽位与 ));  // open: Qn, preset, en, reset
  \单周期硬布线控制器  \u_单周期硬布线控制器_1  ();  // open: Func, OP, ALU_OP, MemToReg, MemWrite, ALU_SRC, RegWrite, SysCALL, SignedExt, RegDst, JR, JMP, Beq, JAL, Bne, DIVU, MFLO, LBU, BGTZ, R1_Used, R2_Used

  // Notes on the sheet:
  //   中断信号采样参考电路
  //   Reset 
endmodule

module \单周期MIPS_单级中断  (
  input  IR1,
  input  IR2,
  input  IR3,
  output RegWrite,
  output MemWrite,
  output [31:0] PC,
  output [31:0] IR,
  output [31:0] RDin,
  output [31:0] MDin,
  output [31:0] LedData
);

  wire CLK, comparator_1_eq, comparator_2_eq, comparator_3_eq, comparator_4_eq, Go, IR1_t, IR2_t, IR3_t, IRA,
       IRB, IRC, or_1_out, W1, W2, W3;
  wire [15:0] \总周期数 ;

  Clock #(.highDuration(1), .lowDuration(1)) clock_1 (.out(CLK));
  Button _1 ();  // open: out
  Button _2 ();  // open: out
  Button _3 ();  // open: out
  Button \u_继续运行  (.out(Go));
  LED #(.active("true")) led_1 (.in(W1));
  LED #(.active("true")) led_2 (.in(W2));
  LED #(.active("true")) led_3 (.in(W3));
  Hex_Digit_Display hex_digit_display_1 (.value(LedData[31:28]));  // open: dp
  Comparator #(.width(16), .mode("twosComplement")) comparator_1 (
    .a(16'h23b), .b(\总周期数 ), .eq(comparator_1_eq));  // open: gt, lt
  Comparator #(.width(16), .mode("twosComplement")) comparator_2 (
    .a(\总周期数 ), .b(16'h1), .eq(comparator_2_eq));  // open: gt, lt
  Comparator #(.width(16), .mode("twosComplement")) comparator_3 (
    .a(\总周期数 ), .b(16'h4), .eq(comparator_3_eq));  // open: gt, lt
  Comparator #(.width(16), .mode("twosComplement")) comparator_4 (
    .a(\总周期数 ), .b(16'h7), .eq(comparator_4_eq));  // open: gt, lt
  Hex_Digit_Display hex_digit_display_2 (.value(LedData[27:24]));  // open: dp
  Hex_Digit_Display hex_digit_display_3 (.value(LedData[23:20]));  // open: dp
  or or_1 (or_1_out, comparator_1_eq, comparator_2_eq);
  assign IRA = or_1_out ? ~CLK : 1'bz;  // Controlled_Inverter controlled_inverter_1
  assign IRB = comparator_3_eq ? ~CLK : 1'bz;  // Controlled_Inverter controlled_inverter_2
  assign IRC = comparator_4_eq ? ~CLK : 1'bz;  // Controlled_Inverter controlled_inverter_3
  Hex_Digit_Display hex_digit_display_4 (.value(LedData[19:16]));  // open: dp
  Hex_Digit_Display hex_digit_display_5 (.value(LedData[15:12]));  // open: dp
  Pull_Resistor #(.pull(0)) pull_resistor_1 (.node(IRA));
  Pull_Resistor #(.pull(0)) pull_resistor_2 (.node(IRB));
  Pull_Resistor #(.pull(0)) pull_resistor_3 (.node(IRC));
  Hex_Digit_Display hex_digit_display_6 (.value(LedData[11:8]));  // open: dp
  Hex_Digit_Display hex_digit_display_7 (.value(LedData[7:4]));  // open: dp
  // Probe on \总周期数 
  Hex_Digit_Display hex_digit_display_8 (.value(LedData[3:0]));  // open: dp
  or or_2 (IR1_t, IR1, IRA);
  or or_3 (IR2_t, IR2, IRB);
  or or_4 (IR3_t, IR3, IRC);

  // Notes on the sheet:
  //   中断源
  //   中断等待指示
  //   总复位信号应将除ROM以外所有存储组件全部清零
  //   单级中断测试信号模拟器
  //   数码管输出
  //   数码管输出应该用寄存器锁存，否则显示数据只能一闪而过
  //   为方便自动评测，需要输出PC，IR，寄存器堆写如数据RDin
  //   RAM写使能MemWrite、RAM写入数据MDin等信号
endmodule

module \单周期MIPS_多级中断  (
  input  IR1,
  input  IR2,
  input  IR3,
  output RegWrite,
  output MemWrite,
  output [31:0] PC,
  output [31:0] IR,
  output [31:0] RDin,
  output [31:0] MDin,
  output [31:0] LedData
);

  wire CLK, comparator_1_eq, comparator_2_eq, comparator_3_eq, comparator_4_eq, comparator_5_eq, Go, IR1_t,
       IR2_t, IR3_t, IRA, IRB, IRC, or_1_out, or_2_out, W1, W2, W3;
  wire [15:0] \总周期数 ;

  Clock #(.highDuration(1), .lowDuration(1)) clock_1 (.out(CLK));
  Button _1 ();  // open: out
  Button _2 ();  // open: out
  Button _3 ();  // open: out
  Button \u_继续运行  (.out(Go));
  LED #(.active("true")) led_1 (.in(W1));
  LED #(.active("true")) led_2 (.in(W2));
  LED #(.active("true")) led_3 (.in(W3));
  Hex_Digit_Display hex_digit_display_1 (.value(LedData[31:28]));  // open: dp
  Comparator #(.width(16), .mode("twosComplement")) comparator_1 (
    .a(\总周期数 ), .b(16'h7), .eq(comparator_1_eq));  // open: gt, lt
  Comparator #(.width(16), .mode("twosComplement")) comparator_2 (
    .a(\总周期数 ), .b(16'h241), .eq(comparator_2_eq));  // open: gt, lt
  Hex_Digit_Display hex_digit_display_2 (.value(LedData[27:24]));  // open: dp
  Hex_Digit_Display hex_digit_display_3 (.value(LedData[23:20]));  // open: dp
  Comparator #(.width(16), .mode("twosComplement")) comparator_3 (
    .a(16'h258), .b(\总周期数 ), .eq(comparator_3_eq));  // open: gt, lt
  or or_1 (or_1_out, comparator_3_eq, comparator_4_eq);
  Comparator #(.width(16), .mode("twosComplement")) comparator_4 (
    .a(\总周期数 ), .b(16'h1), .eq(comparator_4_eq));  // open: gt, lt
  Comparator #(.width(16), .mode("twosComplement")) comparator_5 (
    .a(\总周期数 ), .b(16'h4), .eq(comparator_5_eq));  // open: gt, lt
  or or_2 (or_2_out, comparator_1_eq, comparator_2_eq);
  Hex_Digit_Display hex_digit_display_4 (.value(LedData[15:12]));  // open: dp
  Hex_Digit_Display hex_digit_display_5 (.value(LedData[19:16]));  // open: dp
  Pull_Resistor #(.pull(0)) pull_resistor_1 (.node(IRA));
  assign IRA = or_1_out ? ~CLK : 1'bz;  // Controlled_Inverter controlled_inverter_1
  Pull_Resistor #(.pull(0)) pull_resistor_2 (.node(IRB));
  assign IRB = comparator_5_eq ? ~CLK : 1'bz;  // Controlled_Inverter controlled_inverter_2
  Pull_Resistor #(.pull(0)) pull_resistor_3 (.node(IRC));
  assign IRC = or_2_out ? ~CLK : 1'bz;  // Controlled_Inverter controlled_inverter_3
  Hex_Digit_Display hex_digit_display_6 (.value(LedData[7:4]));  // open: dp
  Hex_Digit_Display hex_digit_display_7 (.value(LedData[11:8]));  // open: dp
  // Probe on \总周期数 
  Hex_Digit_Display hex_digit_display_8 (.value(LedData[3:0]));  // open: dp
  or or_3 (IR1_t, IR1, IRA);
  or or_4 (IR2_t, IR2, IRB);
  or or_5 (IR3_t, IR3, IRC);

  // Notes on the sheet:
  //   中断源
  //   中断等待指示
  //   总复位信号应将除ROM以外所有存储组件全部清零
  //   多级中断测试信号模拟器
  //   数码管输出
  //   数码管输出应该用寄存器锁存，否则显示数据只能一闪而过
  //   为方便自动评测，需要输出PC，IR，寄存器堆写如数据RDin
  //   RAM写使能MemWrite、RAM写入数据MDin等信号
endmodule

module \封装正确性测试  (
);

  wire IR1, IR2, IR3, MemW, RegW;
  wire [31:0] EX_PC, ID_PC, IF_PC, IR, LED, MDin, MDinr, MEM_PC, PC, RDin, RDinr, WB_PC;

  // 单周期MIPS 单周期mips_1: pin names not known; wires that end beside it: IR1, IR2, IR3, RegW, MemW, PC, IR, RDin, MDin, LED
  \气泡流水线  \u_气泡流水线_1  (
    .RegWrite(RegW), .MemWrite(MemW), .IF_PC(IF_PC), .ID_PC(ID_PC), .EX_PC(EX_PC), .M_PC(MEM_PC),
    .WB_PC(WB_PC), .RDin(RDinr), .MDin(MDinr), .LedData(LED));
  \单周期MIPS_单级中断  \u_单周期mips_单级中断_1  (
    .IR1(IR1), .IR2(IR2), .IR3(IR3), .RegWrite(RegW), .MemWrite(MemW), .PC(PC), .IR(IR), .RDin(RDin),
    .MDin(MDin), .LedData(LED));
  \理想流水线  \u_理想流水线_1  (
    .RegWrite(RegW), .MemWrite(MemW), .IF_PC(IF_PC), .ID_PC(ID_PC), .EX_PC(EX_PC), .M_PC(MEM_PC),
    .WB_PC(WB_PC), .RDin(RDinr), .MDin(MDinr), .LedData(LED));
  \重定向流水线  \u_重定向流水线_1  (
    .RegWrite(RegW), .MemWrite(MemW), .LedData(IF_PC), .IF_PC(ID_PC), .ID_PC(EX_PC), .EX_PC(MEM_PC),
    .M_PC(WB_PC), .WB_PC(RDinr), .RDin(MDinr), .MDin(LED));  // open: LedData_2
  \单周期MIPS_多级中断  \u_单周期mips_多级中断_1  (
    .IR1(IR1), .IR2(IR2), .IR3(IR3), .RegWrite(RegW), .MemWrite(MemW), .PC(PC), .IR(IR), .RDin(RDin),
    .MDin(MDin), .LedData(LED));

  // Notes on the sheet:
  //   单周期封装测试
  //   气泡流水封装测试
  //   单周期+单级中断封装测试
  //   请检查上面封装有无位宽不匹配，引脚标签是否和连接的标签相对应，否则无法在educoder平台上正确测试
  //   理想流水封装测试
  //   重定向流水封装测试
  //   单周期+多级中断封装测试
endmodule

module IF_ID (
  input  [31:0] PC,
  input  [31:0] IR,
  input  SYNC_RESET,
  input  \使能 ,
  input  CLK,
  output [31:0] PC_2,
  output [31:0] IR_2
);

  wire [31:0] multiplexer_1_out, multiplexer_2_out;

  Multiplexer #(.select(1), .width(32), .disabled("Z"), .enable("false")) multiplexer_1 (
    .in0(PC), .in1({32{1'b0}}), .out(multiplexer_1_out), .sel(SYNC_RESET));
  Multiplexer #(.select(1), .width(32), .disabled("Z"), .enable("false")) multiplexer_2 (
    .in0(IR), .in1({32{1'b0}}), .out(multiplexer_2_out), .sel(SYNC_RESET));
  Register #(.width(32), .trigger("rising"), .Select("low")) register_1 (
    .D(multiplexer_1_out), .en(\使能 ), .Q(PC_2), .clk(CLK));  // open: clr
  Register #(.width(32), .trigger("rising"), .Select("low")) register_2 (
    .D(multiplexer_2_out), .en(\使能 ), .Q(IR_2), .clk(CLK));  // open: clr
endmodule

module ID_EX (
  input  [31:0] PC,
  input  [31:0] IR,
  input  [15:0] CTRL,
  input  [31:0] R1,
  input  [31:0] R2,
  input  [31:0] IMME,
  input  [4:0] SHAMT,
  input  [4:0] WB,
  input  SYNC_RESET,
  input  \使能 ,
  input  CLK,
  output [31:0] out_12,
  output [31:0] out_13,
  output [15:0] out_14,
  output [31:0] out_15,
  output [31:0] out_16,
  output [31:0] out_17,
  output [4:0] out_18,
  output [4:0] out_19
);

  wire [4:0] multiplexer_7_out, multiplexer_8_out;
  wire [15:0] multiplexer_3_out;
  wire [31:0] multiplexer_1_out, multiplexer_2_out, multiplexer_4_out, multiplexer_5_out, multiplexer_6_out;

  Multiplexer #(.select(1), .width(32), .disabled("Z"), .enable("false")) multiplexer_1 (
    .in0(PC), .in1({32{1'b0}}), .out(multiplexer_1_out), .sel(SYNC_RESET));
  Multiplexer #(.select(1), .width(32), .disabled("Z"), .enable("false")) multiplexer_2 (
    .in0(IR), .in1({32{1'b0}}), .out(multiplexer_2_out), .sel(SYNC_RESET));
  Multiplexer #(.select(1), .width(16), .disabled("Z"), .enable("false")) multiplexer_3 (
    .in0(CTRL), .in1({16{1'b0}}), .out(multiplexer_3_out), .sel(SYNC_RESET));
  Multiplexer #(.select(1), .width(32), .disabled("Z"), .enable("false")) multiplexer_4 (
    .in0(R1), .in1({32{1'b0}}), .out(multiplexer_4_out), .sel(SYNC_RESET));
  Multiplexer #(.select(1), .width(32), .disabled("Z"), .enable("false")) multiplexer_5 (
    .in0(R2), .in1({32{1'b0}}), .out(multiplexer_5_out), .sel(SYNC_RESET));
  Multiplexer #(.select(1), .width(32), .disabled("Z"), .enable("false")) multiplexer_6 (
    .in0(IMME), .in1({32{1'b0}}), .out(multiplexer_6_out), .sel(SYNC_RESET));
  Multiplexer #(.select(1), .width(5), .disabled("Z"), .enable("false")) multiplexer_7 (
    .in0(SHAMT), .in1({5{1'b0}}), .out(multiplexer_7_out), .sel(SYNC_RESET));
  Multiplexer #(.select(1), .width(5), .disabled("Z"), .enable("false")) multiplexer_8 (
    .in0(WB), .in1({5{1'b0}}), .out(multiplexer_8_out), .sel(SYNC_RESET));
  Register #(.width(32), .trigger("rising"), .Select("low")) register_1 (
    .D(multiplexer_1_out), .en(\使能 ), .Q(out_12), .clk(CLK));  // open: clr
  Register #(.width(32), .trigger("rising"), .Select("low")) register_2 (
    .D(multiplexer_2_out), .en(\使能 ), .Q(out_13), .clk(CLK));  // open: clr
  Register #(.width(16), .trigger("rising"), .Select("low")) register_3 (
    .D(multiplexer_3_out), .en(\使能 ), .Q(out_14), .clk(CLK));  // open: clr
  Register #(.width(32), .trigger("rising"), .Select("low")) register_4 (
    .D(multiplexer_4_out), .en(\使能 ), .Q(out_15), .clk(CLK));  // open: clr
  Register #(.width(32), .trigger("rising"), .Select("low")) register_5 (
    .D(multiplexer_5_out), .en(\使能 ), .Q(out_16), .clk(CLK));  // open: clr
  Register #(.width(32), .trigger("rising"), .Select("low")) register_6 (
    .D(multiplexer_6_out), .en(\使能 ), .Q(out_17), .clk(CLK));  // open: clr
  Register #(.width(5), .trigger("rising"), .Select("low")) register_7 (
    .D(multiplexer_7_out), .en(\使能 ), .Q(out_18), .clk(CLK));  // open: clr
  Register #(.width(5), .trigger("rising"), .Select("low")) register_8 (
    .D(multiplexer_8_out), .en(\使能 ), .Q(out_19), .clk(CLK));  // open: clr
endmodule

module EX_MEM (
  input  [31:0] PC,
  input  [31:0] IR,
  input  [15:0] CTRL,
  input  [31:0] Res1,
  input  [31:0] MDin,
  input  [31:0] R1,
  input  [4:0] WB,
  input  SYNC_RESET,
  input  \使能 ,
  input  CLK,
  output [31:0] out_11,
  output [31:0] out_12,
  output [15:0] out_13,
  output [31:0] out_14,
  output [31:0] out_15,
  output [31:0] out_16,
  output [4:0] out_17
);

  wire [4:0] multiplexer_7_out;
  wire [15:0] multiplexer_3_out;
  wire [31:0] multiplexer_1_out, multiplexer_2_out, multiplexer_4_out, multiplexer_5_out, multiplexer_6_out;

  Multiplexer #(.select(1), .width(32), .disabled("Z"), .enable("false")) multiplexer_1 (
    .in0(PC), .in1({32{1'b0}}), .out(multiplexer_1_out), .sel(SYNC_RESET));
  Multiplexer #(.select(1), .width(32), .disabled("Z"), .enable("false")) multiplexer_2 (
    .in0(IR), .in1({32{1'b0}}), .out(multiplexer_2_out), .sel(SYNC_RESET));
  Multiplexer #(.select(1), .width(16), .disabled("Z"), .enable("false")) multiplexer_3 (
    .in0(CTRL), .in1({16{1'b0}}), .out(multiplexer_3_out), .sel(SYNC_RESET));
  Multiplexer #(.select(1), .width(32), .disabled("Z"), .enable("false")) multiplexer_4 (
    .in0(Res1), .in1({32{1'b0}}), .out(multiplexer_4_out), .sel(SYNC_RESET));
  Multiplexer #(.select(1), .width(32), .disabled("Z"), .enable("false")) multiplexer_5 (
    .in0(MDin), .in1({32{1'b0}}), .out(multiplexer_5_out), .sel(SYNC_RESET));
  Multiplexer #(.select(1), .width(32), .disabled("Z"), .enable("false")) multiplexer_6 (
    .in0(R1), .in1({32{1'b0}}), .out(multiplexer_6_out), .sel(SYNC_RESET));
  Multiplexer #(.select(1), .width(5), .disabled("Z"), .enable("false")) multiplexer_7 (
    .in0(WB), .in1({5{1'b0}}), .out(multiplexer_7_out), .sel(SYNC_RESET));
  Register #(.width(32), .trigger("rising"), .Select("low")) register_1 (
    .D(multiplexer_1_out), .en(\使能 ), .Q(out_11), .clk(CLK));  // open: clr
  Register #(.width(32), .trigger("rising"), .Select("low")) register_2 (
    .D(multiplexer_2_out), .en(\使能 ), .Q(out_12), .clk(CLK));  // open: clr
  Register #(.width(16), .trigger("rising"), .Select("low")) register_3 (
    .D(multiplexer_3_out), .en(\使能 ), .Q(out_13), .clk(CLK));  // open: clr
  Register #(.width(32), .trigger("rising"), .Select("low")) register_4 (
    .D(multiplexer_4_out), .en(\使能 ), .Q(out_14), .clk(CLK));  // open: clr
  Register #(.width(32), .trigger("rising"), .Select("low")) register_5 (
    .D(multiplexer_5_out), .en(\使能 ), .Q(out_15), .clk(CLK));  // open: clr
  Register #(.width(32), .trigger("rising"), .Select("low")) register_6 (
    .D(multiplexer_6_out), .en(\使能 ), .Q(out_16), .clk(CLK));  // open: clr
  Register #(.width(5), .trigger("rising"), .Select("low")) register_7 (
    .D(multiplexer_7_out), .en(\使能 ), .Q(out_17), .clk(CLK));  // open: clr
endmodule

module MEM_WB (
  input  [31:0] PC,
  input  [31:0] IR,
  input  [15:0] CTRL,
  input  [31:0] MDin,
  input  [31:0] R1,
  input  [31:0] R2,
  input  [4:0] WB,
  input  SYNC_RESET,
  input  \使能 ,
  input  CLK,
  output [31:0] out_11,
  output [31:0] out_12,
  output [15:0] out_13,
  output [31:0] out_14,
  output [31:0] out_15,
  output [31:0] out_16,
  output [4:0] out_17
);

  wire [4:0] multiplexer_7_out;
  wire [15:0] multiplexer_3_out;
  wire [31:0] multiplexer_1_out, multiplexer_2_out, multiplexer_4_out, multiplexer_5_out, multiplexer_6_out;

  Multiplexer #(.select(1), .width(32), .disabled("Z"), .enable("false")) multiplexer_1 (
    .in0(PC), .in1({32{1'b0}}), .out(multiplexer_1_out), .sel(SYNC_RESET));
  Multiplexer #(.select(1), .width(32), .disabled("Z"), .enable("false")) multiplexer_2 (
    .in0(IR), .in1({32{1'b0}}), .out(multiplexer_2_out), .sel(SYNC_RESET));
  Multiplexer #(.select(1), .width(16), .disabled("Z"), .enable("false")) multiplexer_3 (
    .in0(CTRL), .in1({16{1'b0}}), .out(multiplexer_3_out), .sel(SYNC_RESET));
  Multiplexer #(.select(1), .width(32), .disabled("Z"), .enable("false")) multiplexer_4 (
    .in0(MDin), .in1({32{1'b0}}), .out(multiplexer_4_out), .sel(SYNC_RESET));
  Multiplexer #(.select(1), .width(32), .disabled("Z"), .enable("false")) multiplexer_5 (
    .in0(R1), .in1({32{1'b0}}), .out(multiplexer_5_out), .sel(SYNC_RESET));
  Multiplexer #(.select(1), .width(32), .disabled("Z"), .enable("false")) multiplexer_6 (
    .in0(R2), .in1({32{1'b0}}), .out(multiplexer_6_out), .sel(SYNC_RESET));
  Multiplexer #(.select(1), .width(5), .disabled("Z"), .enable("false")) multiplexer_7 (
    .in0(WB), .in1({5{1'b0}}), .out(multiplexer_7_out), .sel(SYNC_RESET));
  Register #(.width(32), .trigger("rising"), .Select("low")) register_1 (
    .D(multiplexer_1_out), .en(\使能 ), .Q(out_11), .clk(CLK));  // open: clr
  Register #(.width(32), .trigger("rising"), .Select("low")) register_2 (
    .D(multiplexer_2_out), .en(\使能 ), .Q(out_12), .clk(CLK));  // open: clr
  Register #(.width(16), .trigger("rising"), .Select("low")) register_3 (
    .D(multiplexer_3_out), .en(\使能 ), .Q(out_13), .clk(CLK));  // open: clr
  Register #(.width(32), .trigger("rising"), .Select("low")) register_4 (
    .D(multiplexer_4_out), .en(\使能 ), .Q(out_14), .clk(CLK));  // open: clr
  Register #(.width(32), .trigger("rising"), .Select("low")) register_5 (
    .D(multiplexer_5_out), .en(\使能 ), .Q(out_15), .clk(CLK));  // open: clr
  Register #(.width(32), .trigger("rising"), .Select("low")) register_6 (
    .D(multiplexer_6_out), .en(\使能 ), .Q(out_16), .clk(CLK));  // open: clr
  Register #(.width(5), .trigger("rising"), .Select("low")) register_7 (
    .D(multiplexer_7_out), .en(\使能 ), .Q(out_17), .clk(CLK));  // open: clr
endmodule

module \IF_ID气泡  (
  input  [31:0] PC,
  input  [31:0] IR,
  input  SYNC_RESET,
  input  \使能 ,
  input  CLK,
  output [31:0] PC_2,
  output [31:0] IR_2
);

  wire [31:0] multiplexer_1_out, multiplexer_2_out;

  Multiplexer #(.select(1), .width(32), .disabled("Z"), .enable("false")) multiplexer_1 (
    .in0(PC), .in1({32{1'b0}}), .out(multiplexer_1_out), .sel(SYNC_RESET));
  Multiplexer #(.select(1), .width(32), .disabled("Z"), .enable("false")) multiplexer_2 (
    .in0(IR), .in1({32{1'b0}}), .out(multiplexer_2_out), .sel(SYNC_RESET));
  Register #(.width(32), .trigger("rising"), .Select("low")) register_1 (
    .D(multiplexer_1_out), .en(\使能 ), .Q(PC_2), .clk(CLK));  // open: clr
  Register #(.width(32), .trigger("rising"), .Select("low")) register_2 (
    .D(multiplexer_2_out), .en(\使能 ), .Q(IR_2), .clk(CLK));  // open: clr
endmodule

module \ID_EX气泡  (
  input  [31:0] PC,
  input  [31:0] IR,
  input  [21:0] CTRL,
  input  [31:0] R1,
  input  [31:0] R2,
  input  [31:0] IMME,
  input  [4:0] SHAMT,
  input  [4:0] WB,
  input  [25:0] ADDR,
  input  [1:0] R1_Fwd,
  input  [1:0] R2_Fwd,
  input  SYNC_RESET,
  input  \使能 ,
  input  CLK,
  output [31:0] out_15,
  output [31:0] out_16,
  output [21:0] out_17,
  output [31:0] out_18,
  output [31:0] out_19,
  output [31:0] out_20,
  output [4:0] out_21,
  output [4:0] out_22,
  output [25:0] out_23,
  output [1:0] out_24,
  output [1:0] out_25
);

  wire [1:0] multiplexer_10_out, multiplexer_11_out;
  wire [4:0] multiplexer_7_out, multiplexer_8_out;
  wire [21:0] multiplexer_3_out;
  wire [25:0] multiplexer_9_out;
  wire [31:0] multiplexer_1_out, multiplexer_2_out, multiplexer_4_out, multiplexer_5_out, multiplexer_6_out;

  Multiplexer #(.select(1), .width(32), .disabled("Z"), .enable("false")) multiplexer_1 (
    .in0(PC), .in1({32{1'b0}}), .out(multiplexer_1_out), .sel(SYNC_RESET));
  Multiplexer #(.select(1), .width(32), .disabled("Z"), .enable("false")) multiplexer_2 (
    .in0(IR), .in1({32{1'b0}}), .out(multiplexer_2_out), .sel(SYNC_RESET));
  Multiplexer #(.select(1), .width(22), .disabled("Z"), .enable("false")) multiplexer_3 (
    .in0(CTRL), .in1({22{1'b0}}), .out(multiplexer_3_out), .sel(SYNC_RESET));
  Multiplexer #(.select(1), .width(32), .disabled("Z"), .enable("false")) multiplexer_4 (
    .in0(R1), .in1({32{1'b0}}), .out(multiplexer_4_out), .sel(SYNC_RESET));
  Multiplexer #(.select(1), .width(32), .disabled("Z"), .enable("false")) multiplexer_5 (
    .in0(R2), .in1({32{1'b0}}), .out(multiplexer_5_out), .sel(SYNC_RESET));
  Multiplexer #(.select(1), .width(32), .disabled("Z"), .enable("false")) multiplexer_6 (
    .in0(IMME), .in1({32{1'b0}}), .out(multiplexer_6_out), .sel(SYNC_RESET));
  Multiplexer #(.select(1), .width(5), .disabled("Z"), .enable("false")) multiplexer_7 (
    .in0(SHAMT), .in1({5{1'b0}}), .out(multiplexer_7_out), .sel(SYNC_RESET));
  Multiplexer #(.select(1), .width(5), .disabled("Z"), .enable("false")) multiplexer_8 (
    .in0(WB), .in1({5{1'b0}}), .out(multiplexer_8_out), .sel(SYNC_RESET));
  Multiplexer #(.select(1), .width(26), .disabled("Z"), .enable("false")) multiplexer_9 (
    .in0(ADDR), .in1({26{1'b0}}), .out(multiplexer_9_out), .sel(SYNC_RESET));
  Multiplexer #(.select(1), .width(2), .disabled("Z"), .enable("false")) multiplexer_10 (
    .in0(R1_Fwd), .in1(2'b00), .out(multiplexer_10_out), .sel(SYNC_RESET));
  Multiplexer #(.select(1), .width(2), .disabled("Z"), .enable("false")) multiplexer_11 (
    .in0(R2_Fwd), .in1(2'b00), .out(multiplexer_11_out), .sel(SYNC_RESET));
  Register #(.width(32), .trigger("rising"), .Select("low")) register_1 (
    .D(multiplexer_1_out), .en(\使能 ), .Q(out_15), .clk(CLK));  // open: clr
  Register #(.width(32), .trigger("rising"), .Select("low")) register_2 (
    .D(multiplexer_2_out), .en(\使能 ), .Q(out_16), .clk(CLK));  // open: clr
  Register #(.width(22), .trigger("rising"), .Select("low")) register_3 (
    .D(multiplexer_3_out), .en(\使能 ), .Q(out_17), .clk(CLK));  // open: clr
  Register #(.width(32), .trigger("rising"), .Select("low")) register_4 (
    .D(multiplexer_4_out), .en(\使能 ), .Q(out_18), .clk(CLK));  // open: clr
  Register #(.width(32), .trigger("rising"), .Select("low")) register_5 (
    .D(multiplexer_5_out), .en(\使能 ), .Q(out_19), .clk(CLK));  // open: clr
  Register #(.width(32), .trigger("rising"), .Select("low")) register_6 (
    .D(multiplexer_6_out), .en(\使能 ), .Q(out_20), .clk(CLK));  // open: clr
  Register #(.width(5), .trigger("rising"), .Select("low")) register_7 (
    .D(multiplexer_7_out), .en(\使能 ), .Q(out_21), .clk(CLK));  // open: clr
  Register #(.width(5), .trigger("rising"), .Select("low")) register_8 (
    .D(multiplexer_8_out), .en(\使能 ), .Q(out_22), .clk(CLK));  // open: clr
  Register #(.width(26), .trigger("rising"), .Select("low")) register_9 (
    .D(multiplexer_9_out), .en(\使能 ), .Q(out_23), .clk(CLK));  // open: clr
  Register #(.width(2), .trigger("rising"), .Select("low")) register_10 (
    .D(multiplexer_10_out), .en(\使能 ), .Q(out_24), .clk(CLK));  // open: clr
  Register #(.width(2), .trigger("rising"), .Select("low")) register_11 (
    .D(multiplexer_11_out), .en(\使能 ), .Q(out_25), .clk(CLK));  // open: clr
endmodule

module \EX_MEM气泡  (
  input  [31:0] PC,
  input  [31:0] IR,
  input  [21:0] CTRL,
  input  [31:0] Res1,
  input  [31:0] Res2,
  input  [31:0] MDin,
  input  [31:0] R1,
  input  [4:0] WB,
  input  SYNC_RESET,
  input  \使能 ,
  input  CLK,
  output [31:0] out_12,
  output [31:0] out_13,
  output [21:0] out_14,
  output [31:0] out_15,
  output [31:0] out_16,
  output [31:0] out_17,
  output [31:0] out_18,
  output [4:0] out_19
);

  wire [4:0] multiplexer_8_out;
  wire [21:0] multiplexer_3_out;
  wire [31:0] multiplexer_1_out, multiplexer_2_out, multiplexer_4_out, multiplexer_5_out, multiplexer_6_out,
       multiplexer_7_out;

  Multiplexer #(.select(1), .width(32), .disabled("Z"), .enable("false")) multiplexer_1 (
    .in0(PC), .in1({32{1'b0}}), .out(multiplexer_1_out), .sel(SYNC_RESET));
  Multiplexer #(.select(1), .width(32), .disabled("Z"), .enable("false")) multiplexer_2 (
    .in0(IR), .in1({32{1'b0}}), .out(multiplexer_2_out), .sel(SYNC_RESET));
  Multiplexer #(.select(1), .width(22), .disabled("Z"), .enable("false")) multiplexer_3 (
    .in0(CTRL), .in1({22{1'b0}}), .out(multiplexer_3_out), .sel(SYNC_RESET));
  Multiplexer #(.select(1), .width(32), .disabled("Z"), .enable("false")) multiplexer_4 (
    .in0(Res1), .in1({32{1'b0}}), .out(multiplexer_4_out), .sel(SYNC_RESET));
  Multiplexer #(.select(1), .width(32), .disabled("Z"), .enable("false")) multiplexer_5 (
    .in0(Res2), .in1({32{1'b0}}), .out(multiplexer_5_out), .sel(SYNC_RESET));
  Multiplexer #(.select(1), .width(32), .disabled("Z"), .enable("false")) multiplexer_6 (
    .in0(MDin), .in1({32{1'b0}}), .out(multiplexer_6_out), .sel(SYNC_RESET));
  Multiplexer #(.select(1), .width(32), .disabled("Z"), .enable("false")) multiplexer_7 (
    .in0(R1), .in1({32{1'b0}}), .out(multiplexer_7_out), .sel(SYNC_RESET));
  Multiplexer #(.select(1), .width(5), .disabled("Z"), .enable("false")) multiplexer_8 (
    .in0(WB), .in1({5{1'b0}}), .out(multiplexer_8_out), .sel(SYNC_RESET));
  Register #(.width(32), .trigger("rising"), .Select("low")) register_1 (
    .D(multiplexer_1_out), .en(\使能 ), .Q(out_12), .clk(CLK));  // open: clr
  Register #(.width(32), .trigger("rising"), .Select("low")) register_2 (
    .D(multiplexer_2_out), .en(\使能 ), .Q(out_13), .clk(CLK));  // open: clr
  Register #(.width(22), .trigger("rising"), .Select("low")) register_3 (
    .D(multiplexer_3_out), .en(\使能 ), .Q(out_14), .clk(CLK));  // open: clr
  Register #(.width(32), .trigger("rising"), .Select("low")) register_4 (
    .D(multiplexer_4_out), .en(\使能 ), .Q(out_15), .clk(CLK));  // open: clr
  Register #(.width(32), .trigger("rising"), .Select("low")) register_5 (
    .D(multiplexer_5_out), .en(\使能 ), .Q(out_16), .clk(CLK));  // open: clr
  Register #(.width(32), .trigger("rising"), .Select("low")) register_6 (
    .D(multiplexer_6_out), .en(\使能 ), .Q(out_17), .clk(CLK));  // open: clr
  Register #(.width(32), .trigger("rising"), .Select("low")) register_7 (
    .D(multiplexer_7_out), .en(\使能 ), .Q(out_18), .clk(CLK));  // open: clr
  Register #(.width(5), .trigger("rising"), .Select("low")) register_8 (
    .D(multiplexer_8_out), .en(\使能 ), .Q(out_19), .clk(CLK));  // open: clr
endmodule

module \MEM_WB气泡  (
  input  [31:0] PC,
  input  [31:0] IR,
  input  [21:0] CTRL,
  input  [31:0] R1,
  input  [31:0] R2,
  input  [4:0] WB,
  input  [31:0] ALU_RES,
  input  [31:0] MEM_RES,
  input  [31:0] ALU_RES2,
  input  SYNC_RESET,
  input  \使能 ,
  input  CLK,
  output [31:0] out_13,
  output [31:0] out_14,
  output [21:0] out_15,
  output [31:0] out_16,
  output [31:0] out_17,
  output [4:0] out_18,
  output [31:0] out_19,
  output [31:0] out_20,
  output [31:0] out_21
);

  wire [4:0] multiplexer_6_out;
  wire [21:0] multiplexer_3_out;
  wire [31:0] multiplexer_1_out, multiplexer_2_out, multiplexer_4_out, multiplexer_5_out, multiplexer_7_out,
       multiplexer_8_out, multiplexer_9_out;

  Multiplexer #(.select(1), .width(32), .disabled("Z"), .enable("false")) multiplexer_1 (
    .in0(PC), .in1({32{1'b0}}), .out(multiplexer_1_out), .sel(SYNC_RESET));
  Multiplexer #(.select(1), .width(32), .disabled("Z"), .enable("false")) multiplexer_2 (
    .in0(IR), .in1({32{1'b0}}), .out(multiplexer_2_out), .sel(SYNC_RESET));
  Multiplexer #(.select(1), .width(22), .disabled("Z"), .enable("false")) multiplexer_3 (
    .in0(CTRL), .in1({22{1'b0}}), .out(multiplexer_3_out), .sel(SYNC_RESET));
  Multiplexer #(.select(1), .width(32), .disabled("Z"), .enable("false")) multiplexer_4 (
    .in0(R1), .in1({32{1'b0}}), .out(multiplexer_4_out), .sel(SYNC_RESET));
  Multiplexer #(.select(1), .width(32), .disabled("Z"), .enable("false")) multiplexer_5 (
    .in0(R2), .in1({32{1'b0}}), .out(multiplexer_5_out), .sel(SYNC_RESET));
  Multiplexer #(.select(1), .width(5), .disabled("Z"), .enable("false")) multiplexer_6 (
    .in0(WB), .in1({5{1'b0}}), .out(multiplexer_6_out), .sel(SYNC_RESET));
  Multiplexer #(.select(1), .width(32), .disabled("Z"), .enable("false")) multiplexer_7 (
    .in0(ALU_RES), .in1({32{1'b0}}), .out(multiplexer_7_out), .sel(SYNC_RESET));
  Multiplexer #(.select(1), .width(32), .disabled("Z"), .enable("false")) multiplexer_8 (
    .in0(MEM_RES), .in1({32{1'b0}}), .out(multiplexer_8_out), .sel(SYNC_RESET));
  Multiplexer #(.select(1), .width(32), .disabled("Z"), .enable("false")) multiplexer_9 (
    .in0(ALU_RES2), .in1({32{1'b0}}), .out(multiplexer_9_out), .sel(SYNC_RESET));
  Register #(.width(32), .trigger("rising"), .Select("low")) register_1 (
    .D(multiplexer_1_out), .en(\使能 ), .Q(out_13), .clk(CLK));  // open: clr
  Register #(.width(32), .trigger("rising"), .Select("low")) register_2 (
    .D(multiplexer_2_out), .en(\使能 ), .Q(out_14), .clk(CLK));  // open: clr
  Register #(.width(22), .trigger("rising"), .Select("low")) register_3 (
    .D(multiplexer_3_out), .en(\使能 ), .Q(out_15), .clk(CLK));  // open: clr
  Register #(.width(32), .trigger("rising"), .Select("low")) register_4 (
    .D(multiplexer_4_out), .en(\使能 ), .Q(out_16), .clk(CLK));  // open: clr
  Register #(.width(32), .trigger("rising"), .Select("low")) register_5 (
    .D(multiplexer_5_out), .en(\使能 ), .Q(out_17), .clk(CLK));  // open: clr
  Register #(.width(5), .trigger("rising"), .Select("low")) register_6 (
    .D(multiplexer_6_out), .en(\使能 ), .Q(out_18), .clk(CLK));  // open: clr
  Register #(.width(32), .trigger("rising"), .Select("low")) register_7 (
    .D(multiplexer_7_out), .en(\使能 ), .Q(out_19), .clk(CLK));  // open: clr
  Register #(.width(32), .trigger("rising"), .Select("low")) register_8 (
    .D(multiplexer_8_out), .en(\使能 ), .Q(out_20), .clk(CLK));  // open: clr
  Register #(.width(32), .trigger("rising"), .Select("low")) register_9 (
    .D(multiplexer_9_out), .en(\使能 ), .Q(out_21), .clk(CLK));  // open: clr
endmodule
